// Logisim project 流水线全版本.circ as structural Verilog: 16 circuits, main circuit ◇单周期MIPS
module \单周期MIPS  (
  input  IR1,
  input  IR2,
  input  IR3,
  input  \同步清零信号 ,
  input  in_5,
  input  in_6,
  input  in_7,
  output RegWrite,
  output MemWrite,
  output [31:0] PC,
  output [31:0] IR,
  output [31:0] RDin,
  output [31:0] MDin,
  output [31:0] LedData,
  output \与中断屏蔽位与 ,
  output out_16,
  output out_17,
  output out_18,
  output [3:0] sum,
  output [1:0] out_20
);

  wire \_1号中断_out , and_1_out, and_2_out, and_3_out, and_4_out, and_5_out, and_7_out, and_8_out, and_9_out,
       B, CLK, clock_2_out, comparator_1_eq, comparator_2_eq, comparator_3_eq, comparator_4_eq,
       comparator_5_gt, d_ff_1_q, Go, Halt, IR1_t, IR2_t, IR3_t, IRA, IRB, IRC, JAL, JMP, JR,
       mips_alu_3_equal, not_1_out, not_2_out, not_3_out, not_4_out, not_5_out, not_6_out, not_7_out,
       or_1_out, or_2_out, SignedExt, Syscall, W1, W2, W3, \单周期硬布线控制器_1_alu_src , \单周期硬布线控制器_1_beq ,
       \单周期硬布线控制器_1_bne , \单周期硬布线控制器_1_memtoreg , \单周期硬布线控制器_1_regdst , \单周期硬布线控制器_1_regwrite ;
  wire [3:0] adder_1_out, v1, v2, v3, \单周期硬布线控制器_1_alu_op ;
  wire [4:0] bit_extender_3_out, multiplexer_6_out, multiplexer_7_out, multiplexer_8_out, multiplexer_9_out,
       multiplexer_10_out, multiplexer_14_out, multiplier_1_out;
  wire [15:0] \总周期数 ;
  wire [27:0] PC_4;
  wire [31:0] bit_extender_1_out, bit_extender_2_out, bit_extender_4_out, mips_alu_2_result,
       mips_alu_3_result, multiplexer_1_out, multiplexer_2_out, multiplexer_3_out, multiplexer_11_out,
       multiplexer_13_out, multiplexer_17_out, multiplexer_18_out, ram_1_data, rs, shifter_1_out,
       shifter_2_out;
  wire [31:28] J;

  Clock #(.highDuration(1), .lowDuration(1)) clock_1 (.out(CLK));
  Button _1 (.out(IRA));
  Button _2 (.out(IRB));
  Button _3 (.out(IRC));
  Counter #(.width(16), .max('hffff), .ongoal("wrap"), .trigger("rising"), .behavior("old")) counter_1 (
    .Q(\总周期数 ), .clk(and_1_out));  // open: load, D, count, carry, clr, preset
  and and_1 (and_1_out, CLK, not_1_out);
  not not_1 (not_1_out, Halt);
  Button \u_继续运行  (.out(Go));
  LED #(.active("true")) led_1 (.in(W1));
  LED #(.active("true")) led_2 (.in(W2));
  LED #(.active("true")) led_3 (.in(W3));
  not not_2 (not_2_out, JR);
  and and_2 (and_2_out, not_2_out, JMP);
  Multiplexer #(.select(1), .width(32), .disabled("Z"), .enable("false")) multiplexer_1 (
    .in0(multiplexer_2_out), .in1({J, IR[25:0], 2'b00}), .out(multiplexer_1_out), .sel(and_2_out));
  Multiplexer #(.select(1), .width(32), .disabled("Z"), .enable("false")) multiplexer_2 (
    .in0(multiplexer_3_out), .in1(rs), .out(multiplexer_2_out), .sel(JR));
  Multiplexer #(.select(1), .width(32), .disabled("Z"), .enable("false")) multiplexer_3 (
    .in0({J, PC_4}), .in1(mips_alu_2_result), .out(multiplexer_3_out), .sel(B));
  Clock #(.highDuration(1), .lowDuration(1)) clock_2 (.out(clock_2_out));
  Button \_1号中断  (.out(\_1号中断_out ));
  LED #(.active("true")) \_1号中断等待指示灯  (.in(or_1_out));
  Hex_Digit_Display hex_digit_display_1 (.value(LedData[31:28]));  // open: dp
  not not_3 (not_3_out, Halt);
  MIPS_ALU mips_alu_1 (.X(PC), .Y(32'h4), .AluOP(4'b0101), .Result({J, PC_4}));  // open: Equal, Result_2, shamt
  or or_1 (or_1_out, \与中断屏蔽位与 , d_ff_1_q);
  Adder #(.width(4)) adder_1 (.a(v1), .b(v2), .out(adder_1_out));  // open: cin, cout
  Hex_Digit_Display hex_digit_display_2 (.value(LedData[27:24]));  // open: dp
  Hex_Digit_Display hex_digit_display_3 (.value(LedData[23:20]));  // open: dp
  not not_4 (not_4_out, comparator_1_eq);
  Comparator #(.width(32), .mode("twosComplement")) comparator_1 (
    .a(rs), .b(32'h22), .eq(comparator_1_eq));  // open: gt, lt
  Register #(.width(32), .trigger("rising"), .Select("low")) u_PC (
    .D(multiplexer_1_out), .en(not_3_out), .Q(PC), .clk(CLK));  // open: clr
  D_Flip_Flop #(.trigger("rising"), .Pre_Clr_Positions("LEGACY"), .NegatePresetClear("false"), .enable("true"), .NewFFLayout("false")) d_ff_1 (
    .clk(\_1号中断_out ), .D(1'b1), .Q(d_ff_1_q), .reset(\与中断屏蔽位与 ));  // open: Qn, preset, en
  // Probe on sum
  Adder #(.width(4)) adder_2 (.a(adder_1_out), .b(v3), .out(sum));  // open: cin, cout
  Multiplexer #(.select(4), .width(2), .disabled("Z"), .enable("false")) multiplexer_4 (
    .in0(2'b00), .in1(2'b01), .in3(2'b10), .in4(2'b10), .in5(2'b11), .in6(2'b11), .in7(2'b11), .in8(2'b11),
    .in9(2'b11), .out(out_20), .sel(sum));  // open: in2, in10, in11, in12, in13, in14, in15
  Hex_Digit_Display hex_digit_display_4 (.value(LedData[19:16]));  // open: dp
  Hex_Digit_Display hex_digit_display_5 (.value(LedData[15:12]));  // open: dp
  and and_3 (and_3_out, Syscall, not_4_out);
  and and_4 (and_4_out, comparator_1_eq, Syscall);
  // Probe on PC
  or or_2 (or_2_out, d_ff_1_q, \与中断屏蔽位与 );
  // Probe on out_20
  Hex_Digit_Display hex_digit_display_6 (.value(LedData[7:4]));  // open: dp
  Hex_Digit_Display hex_digit_display_7 (.value(LedData[11:8]));  // open: dp
  // Probe on \总周期数 
  Counter #(.width(1), .max('h1), .ongoal("wrap"), .trigger("rising"), .behavior("old")) counter_2 (
    .load(and_3_out), .D(and_3_out), .count(1'b0), .Q(Halt), .clk(CLK), .clr(Go));  // open: carry, preset
  Counter #(.width(32), .max('hffffffff), .ongoal("wrap"), .trigger("rising"), .behavior("old")) counter_3 (
    .load(and_4_out), .D(MDin), .count(1'b0), .Q(LedData), .clk(CLK));  // open: carry, clr, preset
  ROM #(.addrWidth(10), .dataWidth(32), .Select("high")) rom_1 (.addr(PC[11:2]), .data(IR));
  MIPS_ALU mips_alu_2 (
    .X({J, PC_4}), .Y(shifter_1_out), .AluOP(4'b0101), .Result(mips_alu_2_result));  // open: Equal, Result_2, shamt
  and and_5 (and_5_out, or_2_out, ~\同步清零信号 );  // AND_Gate
  Hex_Digit_Display hex_digit_display_8 (.value(LedData[3:0]));  // open: dp
  D_Flip_Flop #(.trigger("rising"), .Pre_Clr_Positions("LEGACY"), .NegatePresetClear("false"), .enable("true"), .NewFFLayout("false")) u_IR1 (
    .clk(clock_2_out), .D(and_5_out), .Q(\与中断屏蔽位与 ));  // open: Qn, preset, en, reset
  \中断按键参考电路  \u_中断按键参考电路_1  (.\与中断屏蔽位与 (out_16), .\同步清零信号 (in_5), .in_2(IR1_t), .out_5(W1), .in_1(CLK));
  Multiplexer #(.select(1), .width(4), .disabled("Z"), .enable("false")) multiplexer_5 (
    .in0(4'b0000), .in1(4'b0001), .out(v1), .sel(W1));
  Multiplexer #(.select(1), .width(5), .disabled("Z"), .enable("false")) multiplexer_6 (
    .in0(IR[25:21]), .in1(5'b00010), .out(multiplexer_6_out), .sel(Syscall));
  Multiplexer #(.select(1), .width(5), .disabled("Z"), .enable("false")) multiplexer_7 (
    .in0(IR[20:16]), .in1(IR[15:11]), .out(multiplexer_7_out), .sel(\单周期硬布线控制器_1_regdst ));
  or or_3 (IR1_t, IR1, IRA);
  Multiplexer #(.select(1), .width(5), .disabled("Z"), .enable("false")) multiplexer_8 (
    .in0(multiplexer_6_out), .in1({5{1'b1}}), .out(multiplexer_8_out), .sel(JR));
  Multiplexer #(.select(1), .width(5), .disabled("Z"), .enable("false")) multiplexer_9 (
    .in0(IR[20:16]), .in1(5'b00100), .out(multiplexer_9_out), .sel(Syscall));
  Multiplexer #(.select(1), .width(5), .disabled("Z"), .enable("false")) multiplexer_10 (
    .in0(multiplexer_7_out), .in1({5{1'b1}}), .out(multiplexer_10_out), .sel(JAL));
  assign bit_extender_1_out = {{16{1'b0}}, IR[15:0]};  // Bit_Extender bit_extender_1
  assign bit_extender_2_out = {{16{IR[15]}}, IR[15:0]};  // Bit_Extender bit_extender_2
  \中断按键参考电路  \u_中断按键参考电路_2  (.\与中断屏蔽位与 (out_17), .\同步清零信号 (in_6), .in_2(IR2_t), .out_5(W2), .in_1(CLK));
  or or_4 (IR2_t, IR2, IRB);
  \单周期硬布线控制器  \u_单周期硬布线控制器_1  (
    .Func(IR[5:0]), .OP(IR[31:26]), .ALU_OP(\单周期硬布线控制器_1_alu_op ), .MemToReg(\单周期硬布线控制器_1_memtoreg ),
    .MemWrite(MemWrite), .ALU_SRC(\单周期硬布线控制器_1_alu_src ), .RegWrite(\单周期硬布线控制器_1_regwrite ),
    .SysCALL(Syscall), .SignedExt(SignedExt), .RegDst(\单周期硬布线控制器_1_regdst ), .JR(JR), .JMP(JMP),
    .Beq(\单周期硬布线控制器_1_beq ), .JAL(JAL), .Bne(\单周期硬布线控制器_1_bne ));
  Multiplexer #(.select(1), .width(32), .disabled("Z"), .enable("false")) multiplexer_11 (
    .in0(bit_extender_1_out), .in1(bit_extender_2_out), .out(multiplexer_11_out), .sel(SignedExt));
  Shifter #(.width(32), .shift("ll")) shifter_1 (.in(multiplexer_11_out), .\dist (5'b00010), .out(shifter_1_out));
  Multiplexer #(.select(1), .width(4), .disabled("Z"), .enable("false")) multiplexer_12 (
    .in0(4'b0000), .in1(4'b0011), .out(v2), .sel(W2));
  MIPS_Regifile mips_regifile_1 (
    .Din(RDin), .Clk(CLK), .R1(rs), .R2(MDin), .WE(RegWrite), .W_num(multiplexer_10_out),
    .R1_num(multiplexer_8_out), .R2_num(multiplexer_9_out));
  or or_5 (IR3_t, IR3, IRC);
  not not_5 (not_5_out, Halt);
  and and_6 (RegWrite, not_5_out, \单周期硬布线控制器_1_regwrite );
  Multiplexer #(.select(1), .width(32), .disabled("Z"), .enable("false")) multiplexer_13 (
    .in0(MDin), .in1(multiplexer_11_out), .out(multiplexer_13_out), .sel(\单周期硬布线控制器_1_alu_src ));
  Multiplexer #(.select(1), .width(5), .disabled("Z"), .enable("false")) multiplexer_14 (
    .in0(IR[10:6]), .in1(rs[4:0]), .out(multiplexer_14_out), .sel(comparator_2_eq));
  Comparator #(.width(6), .mode("twosComplement")) comparator_2 (
    .a(IR[5:0]), .b(6'b000111), .eq(comparator_2_eq));  // open: gt, lt
  \中断按键参考电路  \u_中断按键参考电路_3  (.\与中断屏蔽位与 (out_18), .\同步清零信号 (in_7), .in_2(IR3_t), .out_5(W3), .in_1(CLK));
  Multiplexer #(.select(1), .width(32), .disabled("Z"), .enable("false")) multiplexer_15 (
    .in0(multiplexer_17_out), .in1({J, PC_4}), .out(RDin), .sel(JAL));
  Multiplexer #(.select(1), .width(4), .disabled("Z"), .enable("false")) multiplexer_16 (
    .in0(4'b0000), .in1(4'b0101), .out(v3), .sel(W3));
  MIPS_ALU mips_alu_3 (
    .X(rs), .Y(multiplexer_13_out), .AluOP(\单周期硬布线控制器_1_alu_op ), .Equal(mips_alu_3_equal),
    .Result(mips_alu_3_result), .shamt(multiplexer_14_out));  // open: Result_2
  Comparator #(.width(6), .mode("twosComplement")) comparator_3 (
    .a(IR[31:26]), .b(6'b000111), .eq(comparator_3_eq));  // open: gt, lt
  assign bit_extender_3_out = {{3{1'b0}}, mips_alu_3_result[1:0]};  // Bit_Extender bit_extender_3
  not not_6 (not_6_out, Halt);
  Multiplexer #(.select(1), .width(32), .disabled("Z"), .enable("false")) multiplexer_17 (
    .in0(multiplexer_18_out), .in1(bit_extender_4_out), .out(multiplexer_17_out), .sel(comparator_4_eq));
  Comparator #(.width(6), .mode("twosComplement")) comparator_4 (
    .a(IR[31:26]), .b(6'b100000), .eq(comparator_4_eq));  // open: gt, lt
  not not_7 (not_7_out, mips_alu_3_equal);
  Comparator #(.width(32), .mode("twosComplement")) comparator_5 (
    .a(rs), .b({32{1'b0}}), .gt(comparator_5_gt));  // open: eq, lt
  Multiplier #(.width(5)) multiplier_1 (
    .a(bit_extender_3_out), .b(5'b01000), .out(multiplier_1_out));  // open: cin, cout
  RAM #(.addrWidth(10), .dataWidth(32), .bus("separate"), .Select("high")) ram_1 (
    .addr(mips_alu_3_result[11:2]), .din(MDin), .data(ram_1_data), .str(MemWrite), .sel(not_6_out), .clk(CLK));  // open: ld, clr
  and and_7 (and_7_out, mips_alu_3_equal, \单周期硬布线控制器_1_beq );
  or or_6 (B, and_7_out, and_9_out, and_8_out);
  and and_8 (and_8_out, \单周期硬布线控制器_1_bne , not_7_out);
  and and_9 (and_9_out, comparator_3_eq, comparator_5_gt);
  Multiplexer #(.select(1), .width(32), .disabled("Z"), .enable("false")) multiplexer_18 (
    .in0(mips_alu_3_result), .in1(ram_1_data), .out(multiplexer_18_out), .sel(\单周期硬布线控制器_1_memtoreg ));
  Shifter #(.width(32), .shift("lr")) shifter_2 (
    .in(multiplexer_18_out), .\dist (multiplier_1_out), .out(shifter_2_out));
  assign bit_extender_4_out = {{24{shifter_2_out[7]}}, shifter_2_out[7:0]};  // Bit_Extender bit_extender_4

  // Other names for the same wires on the sheet: OP[5:0] = IR[31:26]; Func[5:0] = IR[5:0]; J[27:2] = IR[25:0];
  //   shamt[4:0] = IR[10:6]; PC_4[31:28] = J; rt[31:0] = MDin

  // Notes on the sheet:
  //   中断源
  //   中断等待指示
  //   总复位信号应将除ROM以外所有存储组件全部清零
  //   中断信号采样参考电路
  //   数码管输出
  //   指令存储器
  //   当前最高优先级
  //   数码管输出应该用寄存器锁存，否则显示数据只能一闪而过
  //   指令字
  //   contents of rom_1 (hex, n*v repeats v):
  //   20110001 8000c05 20110001 20120002 20130003 8000c09 20110001 20120002 20130003 8000c0d 20110001
  //   20120002 20130003 8000c11 20110001 20120002 20130003 c000cb8 20100001 20110001 118fc0 112020
  //   20020022 c 118882 12200001 8000c15 112020 20020022 c 20110001 118880 112020 20020022 c 12200001
  //   8000c1f 20110001 118fc0 112020 20020022 c 1188c3 112020 20020022 c 118903 112020 20020022 c 118903
  //   112020 20020022 c 118903 112020 20020022 c 118903 112020 20020022 c 118903 112020 20020022 c 118903
  //   112020 20020022 c 118903 112020 20020022 c 20100001 109fc0 139fc3 8021 2012000c 24160003 26100001
  //   3210000f 20080008 20090001 139900 2709825 132020 20020022 c 1094022 1500fff9 22100001 2018000f
  //   2188024 108700 20080008 20090001 139902 2709825 132021 20020022 c 1094022 1500fff9 108702 2c9b022
  //   12c00001 8000c50 4020 1084027 84400 3508ffff 82021 20020022 c 2010ffff 20110000 ae300000 22100001
  //   22310004 ae300000 22100001 22310004 ae300000 22100001 22310004 ae300000 22100001 22310004 ae300000
  //   22100001 22310004 ae300000 22100001 22310004 ae300000 22100001 22310004 ae300000 22100001 22310004
  //   ae300000 22100001 22310004 ae300000 22100001 22310004 ae300000 22100001 22310004 ae300000 22100001
  //   22310004 ae300000 22100001 22310004 ae300000 22100001 22310004 ae300000 22100001 22310004 ae300000
  //   22100001 22310004 22100001 8020 2011003c 8e130000 8e340000 274402a 11000002 ae330000 ae140000
  //   2231fffc 1611fff8 102020 20020022 c 22100004 2011003c 1611fff2 20020032 c 20100000 22100001 102020
  //   20020022 c 22100002 102020 20020022 c 22100003 102020 20020022 c 22100004 102020 20020022 c 22100005
  //   102020 20020022 c 22100006 102020 20020022 c 22100007 102020 20020022 c 22100008 102020 20020022
  //   20020022 c 3e00008
  //   Reset 
  //   OP
  //   Func
  //   rs
  //   rt
  //   rd
  //   JMP
  //   JR
  //   OP
  //   Func
  //   Beq
  //   Bne
  //   MemToReg
  //   MemWrite
  //   AluOP
  //   AluSrcB
  //   RegWrite
  //   JAL
  //   RegDst
  //   Syscall
  //   SRAV指令偏移地址
  //   为方便自动评测，需要输出PC，IR，寄存器堆写如数据RDin
  //   RAM写使能MemWrite、RAM写入数据MDin等信号
  //   BGTZ
endmodule

// 单周期硬布线控制器
module \单周期硬布线控制器  (
  input  [5:0] OP,
  input  [5:0] Func,
  output [3:0] ALU_OP,
  output MemToReg,
  output MemWrite,
  output ALU_SRC,
  output RegWrite,
  output SysCALL,
  output SignedExt,
  output RegDst,
  output Beq,
  output Bne,
  output JR,
  output JMP,
  output JAL
);

  \运算控制器自动生成  \u_运算控制器自动生成_1  (
    .OP0(OP[0]), .OP1(OP[1]), .OP2(OP[2]), .OP3(OP[3]), .OP4(OP[4]), .OP5(OP[5]), .F0(Func[0]), .F1(Func[1]),
    .F2(Func[2]), .F3(Func[3]), .F4(Func[4]), .F5(Func[5]), .S0(ALU_OP[0]), .S1(ALU_OP[1]), .S2(ALU_OP[2]),
    .S3(ALU_OP[3]));
  \控制信号自动生成  \u_控制信号自动生成_1  (
    .OP0(OP[0]), .OP1(OP[1]), .OP2(OP[2]), .OP3(OP[3]), .OP4(OP[4]), .OP5(OP[5]), .F0(Func[0]), .F1(Func[1]),
    .F2(Func[2]), .F3(Func[3]), .F4(Func[4]), .F5(Func[5]), .MemToReg(MemToReg), .MemWrite(MemWrite),
    .ALU_SRC(ALU_SRC), .RegWrite(RegWrite), .SysCALL(SysCALL), .SignedExt(SignedExt), .RegDst(RegDst),
    .BEQ(Beq), .BNE(Bne), .JR(JR), .JUMP(JMP), .JAL(JAL));

  // Other names for the same wires on the sheet: OP_CODE[5:0] = OP

  // Notes on the sheet:
  //   运算器控制器，根据指令生成运算器功能选择信号
  //   控制信号生成，产生数据通路需要的其他控制信号
endmodule

// 运算器控制器
module \运算控制器自动生成  (
  input  OP0,
  input  OP1,
  input  OP2,
  input  OP3,
  input  OP4,
  input  OP5,
  input  F0,
  input  F1,
  input  F2,
  input  F3,
  input  F4,
  input  F5,
  output S0,
  output S1,
  output S2,
  output S3
);

  wire and_1_out, and_2_out, and_3_out, and_4_out, and_5_out, and_6_out, and_7_out, and_8_out, and_9_out,
       and_10_out, and_11_out, and_12_out, and_13_out, and_14_out, and_15_out, and_16_out, and_17_out,
       and_18_out, and_19_out, and_20_out, and_21_out, and_22_out, and_23_out, and_24_out, and_25_out,
       and_26_out, and_27_out, and_28_out, and_29_out, and_30_out, and_31_out, and_32_out, and_33_out,
       and_34_out, and_35_out, and_36_out, and_37_out, and_38_out, not_1_out, not_2_out, not_3_out,
       not_4_out, not_5_out, not_6_out, not_7_out, not_8_out, not_9_out, not_10_out, not_11_out, not_12_out,
       not_13_out, not_14_out, not_15_out, not_16_out, not_17_out, not_18_out, not_19_out, not_20_out,
       not_21_out, not_22_out, not_23_out, not_24_out, not_25_out, not_26_out, not_27_out, not_28_out,
       not_29_out, not_30_out, not_31_out, not_32_out, not_33_out, not_34_out, not_35_out, not_36_out,
       not_37_out, not_38_out, not_39_out, not_40_out, not_41_out, not_42_out, not_43_out, not_44_out,
       not_45_out, not_46_out, not_47_out, not_48_out, not_49_out, not_50_out, not_51_out, not_52_out,
       not_53_out, not_54_out, not_55_out, not_56_out, not_57_out, not_58_out, not_59_out, not_60_out,
       not_61_out, not_62_out, not_63_out, not_64_out, not_65_out, not_66_out, not_67_out, not_68_out,
       not_69_out, not_70_out, not_71_out, not_72_out, not_73_out, not_74_out, not_75_out, not_76_out,
       not_77_out, not_78_out, not_79_out, not_80_out, not_81_out, not_82_out, not_83_out, not_84_out,
       not_85_out, not_86_out, not_87_out, not_88_out, not_89_out, not_90_out, not_91_out, not_92_out,
       not_93_out, not_94_out, not_95_out, not_96_out, not_97_out, not_98_out, not_99_out, not_100_out,
       not_101_out, not_102_out, not_103_out, not_104_out, not_105_out, not_106_out, not_107_out,
       not_108_out, not_109_out, not_110_out, not_111_out, not_112_out, not_113_out, not_114_out,
       not_115_out, not_116_out, not_117_out, not_118_out, not_119_out, not_120_out, not_121_out,
       not_122_out, not_123_out, not_124_out, not_125_out, not_126_out, not_127_out, not_128_out,
       not_129_out, not_130_out, not_131_out, not_132_out, not_133_out, not_134_out, not_135_out,
       not_136_out, not_137_out, not_138_out, not_139_out, not_140_out, not_141_out, not_142_out,
       not_143_out, not_144_out, not_145_out, not_146_out, not_147_out, not_148_out, not_149_out,
       not_150_out, not_151_out, not_152_out, not_153_out, not_154_out, not_155_out, not_156_out,
       not_157_out, not_158_out, not_159_out, not_160_out, not_161_out, not_162_out, not_163_out,
       not_164_out, not_165_out, not_166_out, not_167_out, not_168_out, not_169_out, not_170_out,
       not_171_out, not_172_out, not_173_out, not_174_out, not_175_out, not_176_out, not_177_out,
       not_178_out, not_179_out, not_180_out, not_181_out, not_182_out, not_183_out, not_184_out,
       not_185_out, not_186_out, not_187_out, not_188_out, not_189_out, not_190_out, not_191_out,
       not_192_out, not_193_out, not_194_out, not_195_out, not_196_out, not_197_out, not_198_out,
       not_199_out, not_200_out, not_201_out, not_202_out, not_203_out, not_204_out, not_205_out,
       not_206_out, not_207_out, not_208_out, not_209_out, not_210_out, not_211_out, not_212_out,
       not_213_out, not_214_out, not_215_out, not_216_out, not_217_out, not_218_out, not_219_out,
       not_220_out, not_221_out, not_222_out, not_223_out, not_224_out, not_225_out, not_226_out,
       not_227_out, not_228_out, not_229_out, not_230_out, not_231_out, not_232_out, not_233_out,
       not_234_out, not_235_out, not_236_out, not_237_out, not_238_out, not_239_out, not_240_out,
       not_241_out, not_242_out, not_243_out, not_244_out, not_245_out, not_246_out, not_247_out,
       not_248_out, not_249_out, not_250_out, not_251_out, not_252_out, not_253_out, not_254_out,
       not_255_out, not_256_out, not_257_out, not_258_out, not_259_out, not_260_out, not_261_out, not_262_out;

  not not_1 (not_1_out, OP5);
  not not_2 (not_2_out, OP4);
  not not_3 (not_3_out, OP3);
  not not_4 (not_4_out, OP2);
  not not_5 (not_5_out, OP1);
  not not_6 (not_6_out, OP0);
  not not_7 (not_7_out, F5);
  not not_8 (not_8_out, F4);
  not not_9 (not_9_out, F3);
  not not_10 (not_10_out, F2);
  not not_11 (not_11_out, OP5);
  not not_12 (not_12_out, OP4);
  not not_13 (not_13_out, OP3);
  not not_14 (not_14_out, OP2);
  not not_15 (not_15_out, OP1);
  not not_16 (not_16_out, OP0);
  not not_17 (not_17_out, F4);
  not not_18 (not_18_out, F3);
  not not_19 (not_19_out, F2);
  not not_20 (not_20_out, F1);
  not not_21 (not_21_out, F0);
  not not_22 (not_22_out, OP5);
  not not_23 (not_23_out, OP4);
  not not_24 (not_24_out, OP3);
  not not_25 (not_25_out, OP2);
  not not_26 (not_26_out, OP1);
  not not_27 (not_27_out, OP0);
  not not_28 (not_28_out, F4);
  not not_29 (not_29_out, F3);
  not not_30 (not_30_out, F2);
  not not_31 (not_31_out, F1);
  not not_32 (not_32_out, OP5);
  not not_33 (not_33_out, OP4);
  not not_34 (not_34_out, OP3);
  not not_35 (not_35_out, OP2);
  not not_36 (not_36_out, OP1);
  not not_37 (not_37_out, OP0);
  not not_38 (not_38_out, F4);
  not not_39 (not_39_out, F3);
  not not_40 (not_40_out, F1);
  not not_41 (not_41_out, F0);
  not not_42 (not_42_out, OP5);
  not not_43 (not_43_out, OP4);
  not not_44 (not_44_out, OP3);
  not not_45 (not_45_out, OP2);
  not not_46 (not_46_out, OP1);
  not not_47 (not_47_out, OP0);
  not not_48 (not_48_out, F4);
  not not_49 (not_49_out, F2);
  not not_50 (not_50_out, F0);
  not not_51 (not_51_out, OP5);
  not not_52 (not_52_out, OP4);
  not not_53 (not_53_out, OP2);
  not not_54 (not_54_out, OP1);
  not not_55 (not_55_out, OP0);
  not not_56 (not_56_out, OP5);
  not not_57 (not_57_out, OP4);
  not not_58 (not_58_out, OP1);
  not not_59 (not_59_out, OP0);
  not not_60 (not_60_out, OP5);
  not not_61 (not_61_out, OP4);
  not not_62 (not_62_out, OP2);
  not not_63 (not_63_out, OP1);
  not not_64 (not_64_out, OP5);
  not not_65 (not_65_out, OP4);
  not not_66 (not_66_out, OP2);
  not not_67 (not_67_out, OP0);
  not not_68 (not_68_out, OP4);
  not not_69 (not_69_out, OP3);
  not not_70 (not_70_out, OP2);
  not not_71 (not_71_out, OP4);
  not not_72 (not_72_out, OP2);
  not not_73 (not_73_out, OP5);
  not not_74 (not_74_out, OP4);
  not not_75 (not_75_out, OP3);
  not not_76 (not_76_out, OP2);
  not not_77 (not_77_out, OP1);
  not not_78 (not_78_out, OP0);
  not not_79 (not_79_out, F4);
  not not_80 (not_80_out, F3);
  not not_81 (not_81_out, F0);
  not not_82 (not_82_out, OP5);
  not not_83 (not_83_out, OP4);
  not not_84 (not_84_out, OP3);
  not not_85 (not_85_out, OP2);
  not not_86 (not_86_out, OP1);
  not not_87 (not_87_out, OP0);
  not not_88 (not_88_out, F5);
  not not_89 (not_89_out, F4);
  not not_90 (not_90_out, F3);
  not not_91 (not_91_out, OP4);
  not not_92 (not_92_out, OP3);
  not not_93 (not_93_out, OP2);
  not not_94 (not_94_out, OP1);
  not not_95 (not_95_out, OP0);
  not not_96 (not_96_out, OP0);
  not not_97 (not_97_out, OP1);
  not not_98 (not_98_out, OP2);
  not not_99 (not_99_out, OP3);
  not not_100 (not_100_out, OP4);
  not not_101 (not_101_out, OP5);
  not not_102 (not_102_out, F0);
  not not_103 (not_103_out, F1);
  not not_104 (not_104_out, F3);
  not not_105 (not_105_out, F4);
  not not_106 (not_106_out, OP0);
  not not_107 (not_107_out, OP1);
  not not_108 (not_108_out, OP2);
  not not_109 (not_109_out, OP3);
  not not_110 (not_110_out, OP4);
  not not_111 (not_111_out, OP5);
  not not_112 (not_112_out, F0);
  not not_113 (not_113_out, F2);
  not not_114 (not_114_out, F3);
  not not_115 (not_115_out, F4);
  not not_116 (not_116_out, OP0);
  not not_117 (not_117_out, OP1);
  not not_118 (not_118_out, OP2);
  not not_119 (not_119_out, OP3);
  not not_120 (not_120_out, OP4);
  not not_121 (not_121_out, OP5);
  not not_122 (not_122_out, F0);
  not not_123 (not_123_out, F2);
  not not_124 (not_124_out, F4);
  not not_125 (not_125_out, OP0);
  not not_126 (not_126_out, OP1);
  not not_127 (not_127_out, OP2);
  not not_128 (not_128_out, OP3);
  not not_129 (not_129_out, OP4);
  not not_130 (not_130_out, OP5);
  not not_131 (not_131_out, F3);
  not not_132 (not_132_out, F4);
  not not_133 (not_133_out, OP0);
  not not_134 (not_134_out, OP1);
  not not_135 (not_135_out, OP4);
  not not_136 (not_136_out, OP5);
  not not_137 (not_137_out, OP0);
  not not_138 (not_138_out, OP2);
  not not_139 (not_139_out, OP4);
  not not_140 (not_140_out, OP5);
  not not_141 (not_141_out, OP5);
  not not_142 (not_142_out, OP4);
  not not_143 (not_143_out, OP3);
  not not_144 (not_144_out, OP2);
  not not_145 (not_145_out, OP1);
  not not_146 (not_146_out, OP0);
  not not_147 (not_147_out, F4);
  not not_148 (not_148_out, F3);
  not not_149 (not_149_out, F2);
  not not_150 (not_150_out, F1);
  not not_151 (not_151_out, F0);
  not not_152 (not_152_out, OP5);
  not not_153 (not_153_out, OP4);
  not not_154 (not_154_out, OP3);
  not not_155 (not_155_out, OP2);
  not not_156 (not_156_out, OP1);
  not not_157 (not_157_out, OP0);
  not not_158 (not_158_out, F4);
  not not_159 (not_159_out, F3);
  not not_160 (not_160_out, F2);
  not not_161 (not_161_out, F1);
  not not_162 (not_162_out, OP5);
  not not_163 (not_163_out, OP4);
  not not_164 (not_164_out, OP3);
  not not_165 (not_165_out, OP2);
  not not_166 (not_166_out, OP1);
  not not_167 (not_167_out, OP0);
  not not_168 (not_168_out, F4);
  not not_169 (not_169_out, F3);
  not not_170 (not_170_out, F2);
  not not_171 (not_171_out, F0);
  not not_172 (not_172_out, OP5);
  not not_173 (not_173_out, OP4);
  not not_174 (not_174_out, OP3);
  not not_175 (not_175_out, OP2);
  not not_176 (not_176_out, OP1);
  not not_177 (not_177_out, OP0);
  not not_178 (not_178_out, F4);
  not not_179 (not_179_out, F3);
  not not_180 (not_180_out, F1);
  not not_181 (not_181_out, F0);
  not not_182 (not_182_out, OP5);
  not not_183 (not_183_out, OP4);
  not not_184 (not_184_out, OP3);
  not not_185 (not_185_out, OP2);
  not not_186 (not_186_out, OP1);
  not not_187 (not_187_out, OP0);
  not not_188 (not_188_out, F4);
  not not_189 (not_189_out, F2);
  not not_190 (not_190_out, OP5);
  not not_191 (not_191_out, OP4);
  not not_192 (not_192_out, OP2);
  not not_193 (not_193_out, OP1);
  not not_194 (not_194_out, OP0);
  not not_195 (not_195_out, OP5);
  not not_196 (not_196_out, OP4);
  not not_197 (not_197_out, OP1);
  not not_198 (not_198_out, OP0);
  not not_199 (not_199_out, OP5);
  not not_200 (not_200_out, OP4);
  not not_201 (not_201_out, OP2);
  not not_202 (not_202_out, OP1);
  not not_203 (not_203_out, OP4);
  not not_204 (not_204_out, OP3);
  not not_205 (not_205_out, OP2);
  not not_206 (not_206_out, OP4);
  not not_207 (not_207_out, OP2);
  not not_208 (not_208_out, OP4);
  not not_209 (not_209_out, OP3);
  not not_210 (not_210_out, OP2);
  not not_211 (not_211_out, OP1);
  not not_212 (not_212_out, OP0);
  not not_213 (not_213_out, OP5);
  not not_214 (not_214_out, OP4);
  not not_215 (not_215_out, OP3);
  not not_216 (not_216_out, OP2);
  not not_217 (not_217_out, OP1);
  not not_218 (not_218_out, OP0);
  not not_219 (not_219_out, F4);
  not not_220 (not_220_out, F3);
  not not_221 (not_221_out, F1);
  not not_222 (not_222_out, OP5);
  not not_223 (not_223_out, OP4);
  not not_224 (not_224_out, OP3);
  not not_225 (not_225_out, OP2);
  not not_226 (not_226_out, OP1);
  not not_227 (not_227_out, OP0);
  not not_228 (not_228_out, F4);
  not not_229 (not_229_out, F3);
  not not_230 (not_230_out, OP5);
  not not_231 (not_231_out, OP4);
  not not_232 (not_232_out, OP3);
  not not_233 (not_233_out, OP2);
  not not_234 (not_234_out, OP1);
  not not_235 (not_235_out, OP0);
  not not_236 (not_236_out, F4);
  not not_237 (not_237_out, F2);
  not not_238 (not_238_out, F0);
  not not_239 (not_239_out, OP5);
  not not_240 (not_240_out, OP4);
  not not_241 (not_241_out, OP3);
  not not_242 (not_242_out, OP2);
  not not_243 (not_243_out, OP1);
  not not_244 (not_244_out, OP0);
  not not_245 (not_245_out, F4);
  not not_246 (not_246_out, F2);
  not not_247 (not_247_out, OP5);
  not not_248 (not_248_out, OP4);
  not not_249 (not_249_out, OP2);
  not not_250 (not_250_out, OP0);
  not not_251 (not_251_out, OP5);
  not not_252 (not_252_out, OP4);
  not not_253 (not_253_out, OP1);
  not not_254 (not_254_out, OP5);
  not not_255 (not_255_out, OP4);
  not not_256 (not_256_out, OP3);
  not not_257 (not_257_out, OP2);
  not not_258 (not_258_out, OP1);
  not not_259 (not_259_out, OP0);
  not not_260 (not_260_out, F4);
  not not_261 (not_261_out, F3);
  not not_262 (not_262_out, F0);
  and and_1 (and_1_out, not_1_out, not_2_out, not_3_out, not_4_out, not_5_out, not_6_out, not_7_out, not_8_out, not_9_out, not_10_out, F1, F0);
  and and_2 (and_2_out, not_11_out, not_12_out, not_13_out, not_14_out, not_15_out, not_16_out, F5, not_17_out, not_18_out, not_19_out, not_20_out, not_21_out);
  and and_3 (and_3_out, not_22_out, not_23_out, not_24_out, not_25_out, not_26_out, not_27_out, F5, not_28_out, not_29_out, not_30_out, not_31_out, F0);
  and and_4 (and_4_out, not_32_out, not_33_out, not_34_out, not_35_out, not_36_out, not_37_out, F5, not_38_out, not_39_out, F2, not_40_out, not_41_out);
  and and_5 (and_5_out, not_42_out, not_43_out, not_44_out, not_45_out, not_46_out, not_47_out, F5, not_48_out, F3, not_49_out, F1, not_50_out);
  and and_6 (and_6_out, not_51_out, not_52_out, OP3, not_53_out, not_54_out, not_55_out);
  and and_7 (and_7_out, not_56_out, not_57_out, OP3, OP2, not_58_out, not_59_out);
  and and_8 (and_8_out, not_60_out, not_61_out, OP3, not_62_out, not_63_out, OP0);
  and and_9 (and_9_out, not_64_out, not_65_out, OP3, not_66_out, OP1, not_67_out);
  and and_10 (and_10_out, OP5, not_68_out, not_69_out, not_70_out, OP1, OP0);
  and and_11 (and_11_out, OP5, not_71_out, OP3, not_72_out, OP1, OP0);
  and and_12 (and_12_out, not_73_out, not_74_out, not_75_out, not_76_out, not_77_out, not_78_out, F5, not_79_out, not_80_out, F2, F1, not_81_out);
  and and_13 (and_13_out, not_82_out, not_83_out, not_84_out, not_85_out, not_86_out, not_87_out, not_88_out, not_89_out, not_90_out, F2, F1, F0);
  and and_14 (and_14_out, OP5, not_91_out, not_92_out, not_93_out, not_94_out, not_95_out);
  and and_15 (and_15_out, not_96_out, not_97_out, not_98_out, not_99_out, not_100_out, not_101_out, not_102_out, not_103_out, F2, not_104_out, not_105_out, F5);
  and and_16 (and_16_out, not_106_out, not_107_out, not_108_out, not_109_out, not_110_out, not_111_out, not_112_out, F1, not_113_out, not_114_out, not_115_out);
  and and_17 (and_17_out, not_116_out, not_117_out, not_118_out, not_119_out, not_120_out, not_121_out, not_122_out, F1, not_123_out, not_124_out, F5);
  and and_18 (and_18_out, not_125_out, not_126_out, not_127_out, not_128_out, not_129_out, not_130_out, F0, F1, F2, not_131_out, not_132_out, F5);
  and and_19 (and_19_out, not_133_out, not_134_out, OP2, OP3, not_135_out, not_136_out);
  and and_20 (and_20_out, not_137_out, OP1, not_138_out, OP3, not_139_out, not_140_out);
  and and_21 (and_21_out, not_141_out, not_142_out, not_143_out, not_144_out, not_145_out, not_146_out, F5, not_147_out, not_148_out, not_149_out, not_150_out, not_151_out);
  and and_22 (and_22_out, not_152_out, not_153_out, not_154_out, not_155_out, not_156_out, not_157_out, F5, not_158_out, not_159_out, not_160_out, not_161_out, F0);
  and and_23 (and_23_out, not_162_out, not_163_out, not_164_out, not_165_out, not_166_out, not_167_out, F5, not_168_out, not_169_out, not_170_out, F1, not_171_out);
  and and_24 (and_24_out, not_172_out, not_173_out, not_174_out, not_175_out, not_176_out, not_177_out, F5, not_178_out, not_179_out, F2, not_180_out, not_181_out);
  and and_25 (and_25_out, not_182_out, not_183_out, not_184_out, not_185_out, not_186_out, not_187_out, F5, not_188_out, F3, not_189_out, F1, F0);
  and and_26 (and_26_out, not_190_out, not_191_out, OP3, not_192_out, not_193_out, not_194_out);
  and and_27 (and_27_out, not_195_out, not_196_out, OP3, OP2, not_197_out, not_198_out);
  and and_28 (and_28_out, not_199_out, not_200_out, OP3, not_201_out, not_202_out, OP0);
  and and_29 (and_29_out, OP5, not_203_out, not_204_out, not_205_out, OP1, OP0);
  and and_30 (and_30_out, OP5, not_206_out, OP3, not_207_out, OP1, OP0);
  and and_31 (and_31_out, OP5, not_208_out, not_209_out, not_210_out, not_211_out, not_212_out);
  and and_32 (and_32_out, not_213_out, not_214_out, not_215_out, not_216_out, not_217_out, not_218_out, F5, not_219_out, not_220_out, F2, not_221_out, F0);
  and and_33 (and_33_out, not_222_out, not_223_out, not_224_out, not_225_out, not_226_out, not_227_out, F5, not_228_out, not_229_out, F2, F1, F0);
  and and_34 (and_34_out, not_230_out, not_231_out, not_232_out, not_233_out, not_234_out, not_235_out, F5, not_236_out, F3, not_237_out, F1, not_238_out);
  and and_35 (and_35_out, not_239_out, not_240_out, not_241_out, not_242_out, not_243_out, not_244_out, F5, not_245_out, F3, not_246_out, F1, F0);
  and and_36 (and_36_out, not_247_out, not_248_out, OP3, not_249_out, OP1, not_250_out);
  and and_37 (and_37_out, not_251_out, not_252_out, OP3, OP2, not_253_out, OP0);
  and and_38 (and_38_out, not_254_out, not_255_out, not_256_out, not_257_out, not_258_out, not_259_out, F5, not_260_out, not_261_out, F2, F1, not_262_out);
  or or_1 (S1, and_15_out, and_16_out, and_17_out, and_18_out, and_19_out, and_20_out);
  or or_2 (S2, and_21_out, and_22_out, and_23_out, and_24_out, and_25_out, and_26_out, and_27_out, and_28_out, and_29_out, and_30_out, and_31_out);
  or or_3 (S3, and_32_out, and_33_out, and_34_out, and_35_out, and_36_out, and_37_out, and_38_out);
  or or_4 (S0, and_1_out, and_2_out, and_3_out, and_4_out, and_5_out, and_6_out, and_7_out, and_8_out, and_9_out, and_10_out, and_11_out, and_12_out, and_13_out, and_14_out);
endmodule

// 控制信号生成
module \控制信号自动生成  (
  input  OP0,
  input  OP1,
  input  OP2,
  input  OP3,
  input  OP4,
  input  OP5,
  input  F0,
  input  F1,
  input  F2,
  input  F3,
  input  F4,
  input  F5,
  output MemToReg,
  output MemWrite,
  output ALU_SRC,
  output RegWrite,
  output SysCALL,
  output SignedExt,
  output RegDst,
  output BEQ,
  output BNE,
  output JR,
  output JUMP,
  output JAL
);

  wire and_1_out, and_2_out, and_4_out, and_5_out, and_6_out, and_7_out, and_8_out, and_9_out, and_10_out,
       and_11_out, and_12_out, and_13_out, and_14_out, and_15_out, and_16_out, and_17_out, and_18_out,
       and_19_out, and_20_out, and_21_out, and_22_out, and_23_out, and_24_out, and_25_out, and_26_out,
       and_27_out, and_28_out, and_29_out, and_30_out, and_31_out, and_32_out, and_34_out, and_35_out,
       and_36_out, and_37_out, and_38_out, and_39_out, and_40_out, and_41_out, and_42_out, and_43_out,
       and_44_out, and_45_out, and_46_out, and_47_out, and_48_out, and_49_out, and_50_out, and_51_out,
       and_52_out, and_53_out, and_54_out, and_55_out, and_59_out, and_60_out, and_61_out, not_1_out,
       not_2_out, not_3_out, not_4_out, not_5_out, not_6_out, not_7_out, not_8_out, not_9_out, not_10_out,
       not_11_out, not_12_out, not_13_out, not_14_out, not_15_out, not_16_out, not_17_out, not_18_out,
       not_19_out, not_20_out, not_21_out, not_22_out, not_23_out, not_24_out, not_25_out, not_26_out,
       not_27_out, not_28_out, not_29_out, not_30_out, not_31_out, not_32_out, not_33_out, not_34_out,
       not_35_out, not_36_out, not_37_out, not_38_out, not_39_out, not_40_out, not_41_out, not_42_out,
       not_43_out, not_44_out, not_45_out, not_46_out, not_47_out, not_48_out, not_49_out, not_50_out,
       not_51_out, not_52_out, not_53_out, not_54_out, not_55_out, not_56_out, not_57_out, not_58_out,
       not_59_out, not_60_out, not_61_out, not_62_out, not_63_out, not_64_out, not_65_out, not_66_out,
       not_67_out, not_68_out, not_69_out, not_70_out, not_71_out, not_72_out, not_73_out, not_74_out,
       not_75_out, not_76_out, not_77_out, not_78_out, not_79_out, not_80_out, not_81_out, not_82_out,
       not_83_out, not_84_out, not_85_out, not_86_out, not_87_out, not_88_out, not_89_out, not_90_out,
       not_91_out, not_92_out, not_93_out, not_94_out, not_95_out, not_96_out, not_97_out, not_98_out,
       not_99_out, not_100_out, not_101_out, not_102_out, not_103_out, not_104_out, not_105_out, not_106_out,
       not_107_out, not_108_out, not_109_out, not_110_out, not_111_out, not_112_out, not_113_out,
       not_114_out, not_115_out, not_116_out, not_117_out, not_118_out, not_119_out, not_120_out,
       not_121_out, not_122_out, not_123_out, not_124_out, not_125_out, not_126_out, not_127_out,
       not_128_out, not_129_out, not_130_out, not_131_out, not_132_out, not_133_out, not_134_out,
       not_135_out, not_136_out, not_137_out, not_138_out, not_139_out, not_140_out, not_141_out,
       not_142_out, not_143_out, not_144_out, not_145_out, not_146_out, not_147_out, not_148_out,
       not_149_out, not_150_out, not_151_out, not_152_out, not_153_out, not_154_out, not_155_out,
       not_156_out, not_157_out, not_158_out, not_159_out, not_160_out, not_161_out, not_162_out,
       not_163_out, not_164_out, not_165_out, not_166_out, not_167_out, not_168_out, not_169_out,
       not_170_out, not_171_out, not_172_out, not_173_out, not_174_out, not_175_out, not_176_out,
       not_177_out, not_178_out, not_179_out, not_180_out, not_181_out, not_182_out, not_183_out,
       not_184_out, not_185_out, not_186_out, not_187_out, not_188_out, not_189_out, not_190_out,
       not_191_out, not_192_out, not_193_out, not_194_out, not_195_out, not_196_out, not_197_out,
       not_198_out, not_199_out, not_200_out, not_201_out, not_202_out, not_203_out, not_204_out,
       not_205_out, not_206_out, not_207_out, not_208_out, not_209_out, not_210_out, not_211_out,
       not_212_out, not_213_out, not_214_out, not_215_out, not_216_out, not_217_out, not_218_out,
       not_219_out, not_220_out, not_221_out, not_222_out, not_223_out, not_224_out, not_225_out,
       not_226_out, not_227_out, not_228_out, not_229_out, not_230_out, not_231_out, not_232_out,
       not_233_out, not_234_out, not_235_out, not_236_out, not_237_out, not_238_out, not_239_out,
       not_240_out, not_241_out, not_242_out, not_243_out, not_244_out, not_245_out, not_246_out,
       not_247_out, not_248_out, not_249_out, not_250_out, not_251_out, not_252_out, not_253_out,
       not_254_out, not_255_out, not_256_out, not_257_out, not_258_out, not_259_out, not_260_out,
       not_261_out, not_262_out, not_263_out, not_264_out, not_265_out, not_266_out, not_267_out,
       not_268_out, not_269_out, not_270_out, not_271_out, not_272_out, not_273_out, not_274_out,
       not_275_out, not_276_out, not_277_out, not_278_out, not_279_out, not_280_out, not_281_out,
       not_282_out, not_283_out, not_284_out, not_285_out, not_286_out, not_287_out, not_288_out,
       not_289_out, not_290_out, not_291_out, not_292_out, not_293_out, not_294_out, not_295_out,
       not_296_out, not_297_out, not_298_out, not_299_out, not_300_out, not_301_out, not_302_out,
       not_303_out, not_304_out, not_305_out, not_306_out, not_307_out, not_308_out, not_309_out,
       not_310_out, not_311_out, not_312_out, not_313_out, not_314_out, not_315_out, not_316_out,
       not_317_out, not_318_out, not_319_out, not_320_out, not_321_out, not_322_out, not_323_out,
       not_324_out, not_325_out, not_326_out, not_327_out, not_328_out, not_329_out, not_330_out,
       not_331_out, not_332_out, not_333_out, not_334_out, not_335_out, not_336_out, not_337_out,
       not_338_out, not_339_out, not_340_out, not_341_out, not_342_out, not_343_out, not_344_out,
       not_345_out, not_346_out, not_347_out, not_348_out, not_349_out, not_350_out, not_351_out,
       not_352_out, not_353_out, not_354_out, not_355_out, not_356_out, not_357_out, not_358_out,
       not_359_out, not_360_out, not_361_out, not_362_out, not_363_out, not_364_out, not_365_out,
       not_366_out, not_367_out, not_368_out, not_369_out, not_370_out, not_371_out, not_372_out,
       not_373_out, not_374_out, not_375_out, not_376_out, not_377_out, not_378_out, not_379_out,
       not_380_out, not_381_out, not_382_out, not_383_out, not_384_out, not_385_out, not_386_out,
       not_387_out, not_388_out, not_389_out, not_390_out, not_391_out, not_392_out, not_393_out,
       not_394_out, not_395_out, not_396_out, not_397_out, not_398_out, not_399_out, not_400_out,
       not_401_out, not_402_out, not_403_out, not_404_out, not_405_out, not_406_out, not_407_out,
       not_408_out, not_409_out, not_410_out, not_411_out, not_412_out, not_413_out;

  not not_1 (not_1_out, OP4);
  not not_2 (not_2_out, OP3);
  not not_3 (not_3_out, OP2);
  not not_4 (not_4_out, OP4);
  not not_5 (not_5_out, OP3);
  not not_6 (not_6_out, OP2);
  not not_7 (not_7_out, OP1);
  not not_8 (not_8_out, OP0);
  not not_9 (not_9_out, OP4);
  not not_10 (not_10_out, OP2);
  not not_11 (not_11_out, OP5);
  not not_12 (not_12_out, OP4);
  not not_13 (not_13_out, OP2);
  not not_14 (not_14_out, OP1);
  not not_15 (not_15_out, OP0);
  not not_16 (not_16_out, OP5);
  not not_17 (not_17_out, OP4);
  not not_18 (not_18_out, OP1);
  not not_19 (not_19_out, OP0);
  not not_20 (not_20_out, OP5);
  not not_21 (not_21_out, OP4);
  not not_22 (not_22_out, OP2);
  not not_23 (not_23_out, OP1);
  not not_24 (not_24_out, OP5);
  not not_25 (not_25_out, OP4);
  not not_26 (not_26_out, OP2);
  not not_27 (not_27_out, OP0);
  not not_28 (not_28_out, OP5);
  not not_29 (not_29_out, OP4);
  not not_30 (not_30_out, OP1);
  not not_31 (not_31_out, OP4);
  not not_32 (not_32_out, OP3);
  not not_33 (not_33_out, OP2);
  not not_34 (not_34_out, OP4);
  not not_35 (not_35_out, OP2);
  not not_36 (not_36_out, OP4);
  not not_37 (not_37_out, OP3);
  not not_38 (not_38_out, OP2);
  not not_39 (not_39_out, OP1);
  not not_40 (not_40_out, OP0);
  not not_41 (not_41_out, OP5);
  not not_42 (not_42_out, OP4);
  not not_43 (not_43_out, OP3);
  not not_44 (not_44_out, OP2);
  not not_45 (not_45_out, OP1);
  not not_46 (not_46_out, OP0);
  not not_47 (not_47_out, F5);
  not not_48 (not_48_out, F4);
  not not_49 (not_49_out, F3);
  not not_50 (not_50_out, F2);
  not not_51 (not_51_out, F1);
  not not_52 (not_52_out, F0);
  not not_53 (not_53_out, OP5);
  not not_54 (not_54_out, OP4);
  not not_55 (not_55_out, OP3);
  not not_56 (not_56_out, OP2);
  not not_57 (not_57_out, OP1);
  not not_58 (not_58_out, OP0);
  not not_59 (not_59_out, F5);
  not not_60 (not_60_out, F4);
  not not_61 (not_61_out, F3);
  not not_62 (not_62_out, F2);
  not not_63 (not_63_out, OP5);
  not not_64 (not_64_out, OP4);
  not not_65 (not_65_out, OP3);
  not not_66 (not_66_out, OP2);
  not not_67 (not_67_out, OP1);
  not not_68 (not_68_out, OP0);
  not not_69 (not_69_out, F5);
  not not_70 (not_70_out, F4);
  not not_71 (not_71_out, F3);
  not not_72 (not_72_out, F2);
  not not_73 (not_73_out, F0);
  not not_74 (not_74_out, OP5);
  not not_75 (not_75_out, OP4);
  not not_76 (not_76_out, OP3);
  not not_77 (not_77_out, OP2);
  not not_78 (not_78_out, OP1);
  not not_79 (not_79_out, OP0);
  not not_80 (not_80_out, F4);
  not not_81 (not_81_out, F3);
  not not_82 (not_82_out, F2);
  not not_83 (not_83_out, F1);
  not not_84 (not_84_out, F0);
  not not_85 (not_85_out, OP5);
  not not_86 (not_86_out, OP4);
  not not_87 (not_87_out, OP3);
  not not_88 (not_88_out, OP2);
  not not_89 (not_89_out, OP1);
  not not_90 (not_90_out, OP0);
  not not_91 (not_91_out, F4);
  not not_92 (not_92_out, F3);
  not not_93 (not_93_out, F2);
  not not_94 (not_94_out, F1);
  not not_95 (not_95_out, OP5);
  not not_96 (not_96_out, OP4);
  not not_97 (not_97_out, OP3);
  not not_98 (not_98_out, OP2);
  not not_99 (not_99_out, OP1);
  not not_100 (not_100_out, OP0);
  not not_101 (not_101_out, F4);
  not not_102 (not_102_out, F3);
  not not_103 (not_103_out, F2);
  not not_104 (not_104_out, F0);
  not not_105 (not_105_out, OP5);
  not not_106 (not_106_out, OP4);
  not not_107 (not_107_out, OP3);
  not not_108 (not_108_out, OP2);
  not not_109 (not_109_out, OP1);
  not not_110 (not_110_out, OP0);
  not not_111 (not_111_out, F4);
  not not_112 (not_112_out, F3);
  not not_113 (not_113_out, F1);
  not not_114 (not_114_out, F0);
  not not_115 (not_115_out, OP5);
  not not_116 (not_116_out, OP4);
  not not_117 (not_117_out, OP3);
  not not_118 (not_118_out, OP2);
  not not_119 (not_119_out, OP1);
  not not_120 (not_120_out, OP0);
  not not_121 (not_121_out, F4);
  not not_122 (not_122_out, F3);
  not not_123 (not_123_out, F1);
  not not_124 (not_124_out, OP5);
  not not_125 (not_125_out, OP4);
  not not_126 (not_126_out, OP3);
  not not_127 (not_127_out, OP2);
  not not_128 (not_128_out, OP1);
  not not_129 (not_129_out, OP0);
  not not_130 (not_130_out, F4);
  not not_131 (not_131_out, F3);
  not not_132 (not_132_out, OP5);
  not not_133 (not_133_out, OP4);
  not not_134 (not_134_out, OP3);
  not not_135 (not_135_out, OP2);
  not not_136 (not_136_out, OP1);
  not not_137 (not_137_out, OP0);
  not not_138 (not_138_out, F4);
  not not_139 (not_139_out, F2);
  not not_140 (not_140_out, F0);
  not not_141 (not_141_out, OP5);
  not not_142 (not_142_out, OP4);
  not not_143 (not_143_out, OP3);
  not not_144 (not_144_out, OP2);
  not not_145 (not_145_out, OP1);
  not not_146 (not_146_out, OP0);
  not not_147 (not_147_out, F4);
  not not_148 (not_148_out, F2);
  not not_149 (not_149_out, OP5);
  not not_150 (not_150_out, OP4);
  not not_151 (not_151_out, OP3);
  not not_152 (not_152_out, OP2);
  not not_153 (not_153_out, OP5);
  not not_154 (not_154_out, OP4);
  not not_155 (not_155_out, OP2);
  not not_156 (not_156_out, OP1);
  not not_157 (not_157_out, OP0);
  not not_158 (not_158_out, OP5);
  not not_159 (not_159_out, OP4);
  not not_160 (not_160_out, OP1);
  not not_161 (not_161_out, OP0);
  not not_162 (not_162_out, OP5);
  not not_163 (not_163_out, OP4);
  not not_164 (not_164_out, OP2);
  not not_165 (not_165_out, OP1);
  not not_166 (not_166_out, OP5);
  not not_167 (not_167_out, OP4);
  not not_168 (not_168_out, OP2);
  not not_169 (not_169_out, OP0);
  not not_170 (not_170_out, OP5);
  not not_171 (not_171_out, OP4);
  not not_172 (not_172_out, OP1);
  not not_173 (not_173_out, OP4);
  not not_174 (not_174_out, OP3);
  not not_175 (not_175_out, OP2);
  not not_176 (not_176_out, OP5);
  not not_177 (not_177_out, OP4);
  not not_178 (not_178_out, OP3);
  not not_179 (not_179_out, OP2);
  not not_180 (not_180_out, OP1);
  not not_181 (not_181_out, OP0);
  not not_182 (not_182_out, F4);
  not not_183 (not_183_out, F3);
  not not_184 (not_184_out, F0);
  not not_185 (not_185_out, OP5);
  not not_186 (not_186_out, OP4);
  not not_187 (not_187_out, OP3);
  not not_188 (not_188_out, OP2);
  not not_189 (not_189_out, OP1);
  not not_190 (not_190_out, OP0);
  not not_191 (not_191_out, F5);
  not not_192 (not_192_out, F4);
  not not_193 (not_193_out, F3);
  not not_194 (not_194_out, OP4);
  not not_195 (not_195_out, OP3);
  not not_196 (not_196_out, OP2);
  not not_197 (not_197_out, OP1);
  not not_198 (not_198_out, OP0);
  not not_199 (not_199_out, OP5);
  not not_200 (not_200_out, OP4);
  not not_201 (not_201_out, OP3);
  not not_202 (not_202_out, OP2);
  not not_203 (not_203_out, OP1);
  not not_204 (not_204_out, OP0);
  not not_205 (not_205_out, F5);
  not not_206 (not_206_out, F4);
  not not_207 (not_207_out, F1);
  not not_208 (not_208_out, F0);
  not not_209 (not_209_out, OP5);
  not not_210 (not_210_out, OP4);
  not not_211 (not_211_out, OP3);
  not not_212 (not_212_out, OP1);
  not not_213 (not_213_out, OP0);
  not not_214 (not_214_out, OP5);
  not not_215 (not_215_out, OP4);
  not not_216 (not_216_out, OP3);
  not not_217 (not_217_out, OP1);
  not not_218 (not_218_out, OP5);
  not not_219 (not_219_out, OP4);
  not not_220 (not_220_out, OP2);
  not not_221 (not_221_out, OP1);
  not not_222 (not_222_out, OP0);
  not not_223 (not_223_out, OP5);
  not not_224 (not_224_out, OP4);
  not not_225 (not_225_out, OP2);
  not not_226 (not_226_out, OP1);
  not not_227 (not_227_out, OP5);
  not not_228 (not_228_out, OP4);
  not not_229 (not_229_out, OP2);
  not not_230 (not_230_out, OP0);
  not not_231 (not_231_out, OP4);
  not not_232 (not_232_out, OP3);
  not not_233 (not_233_out, OP2);
  not not_234 (not_234_out, OP4);
  not not_235 (not_235_out, OP2);
  not not_236 (not_236_out, OP4);
  not not_237 (not_237_out, OP3);
  not not_238 (not_238_out, OP2);
  not not_239 (not_239_out, OP1);
  not not_240 (not_240_out, OP0);
  not not_241 (not_241_out, OP5);
  not not_242 (not_242_out, OP4);
  not not_243 (not_243_out, OP3);
  not not_244 (not_244_out, OP5);
  not not_245 (not_245_out, OP4);
  not not_246 (not_246_out, OP3);
  not not_247 (not_247_out, OP2);
  not not_248 (not_248_out, OP1);
  not not_249 (not_249_out, OP0);
  not not_250 (not_250_out, F5);
  not not_251 (not_251_out, F4);
  not not_252 (not_252_out, F3);
  not not_253 (not_253_out, F2);
  not not_254 (not_254_out, F1);
  not not_255 (not_255_out, F0);
  not not_256 (not_256_out, OP5);
  not not_257 (not_257_out, OP4);
  not not_258 (not_258_out, OP3);
  not not_259 (not_259_out, OP2);
  not not_260 (not_260_out, OP1);
  not not_261 (not_261_out, OP0);
  not not_262 (not_262_out, F5);
  not not_263 (not_263_out, F4);
  not not_264 (not_264_out, F3);
  not not_265 (not_265_out, F2);
  not not_266 (not_266_out, OP5);
  not not_267 (not_267_out, OP4);
  not not_268 (not_268_out, OP3);
  not not_269 (not_269_out, OP2);
  not not_270 (not_270_out, OP1);
  not not_271 (not_271_out, OP0);
  not not_272 (not_272_out, F5);
  not not_273 (not_273_out, F4);
  not not_274 (not_274_out, F3);
  not not_275 (not_275_out, F2);
  not not_276 (not_276_out, F0);
  not not_277 (not_277_out, OP5);
  not not_278 (not_278_out, OP4);
  not not_279 (not_279_out, OP3);
  not not_280 (not_280_out, OP2);
  not not_281 (not_281_out, OP1);
  not not_282 (not_282_out, OP0);
  not not_283 (not_283_out, F4);
  not not_284 (not_284_out, F3);
  not not_285 (not_285_out, F2);
  not not_286 (not_286_out, F1);
  not not_287 (not_287_out, F0);
  not not_288 (not_288_out, OP5);
  not not_289 (not_289_out, OP4);
  not not_290 (not_290_out, OP3);
  not not_291 (not_291_out, OP2);
  not not_292 (not_292_out, OP1);
  not not_293 (not_293_out, OP0);
  not not_294 (not_294_out, F4);
  not not_295 (not_295_out, F3);
  not not_296 (not_296_out, F2);
  not not_297 (not_297_out, F1);
  not not_298 (not_298_out, OP5);
  not not_299 (not_299_out, OP4);
  not not_300 (not_300_out, OP3);
  not not_301 (not_301_out, OP2);
  not not_302 (not_302_out, OP1);
  not not_303 (not_303_out, OP0);
  not not_304 (not_304_out, F4);
  not not_305 (not_305_out, F3);
  not not_306 (not_306_out, F2);
  not not_307 (not_307_out, F0);
  not not_308 (not_308_out, OP5);
  not not_309 (not_309_out, OP4);
  not not_310 (not_310_out, OP3);
  not not_311 (not_311_out, OP2);
  not not_312 (not_312_out, OP1);
  not not_313 (not_313_out, OP0);
  not not_314 (not_314_out, F4);
  not not_315 (not_315_out, F3);
  not not_316 (not_316_out, F1);
  not not_317 (not_317_out, F0);
  not not_318 (not_318_out, OP5);
  not not_319 (not_319_out, OP4);
  not not_320 (not_320_out, OP3);
  not not_321 (not_321_out, OP2);
  not not_322 (not_322_out, OP1);
  not not_323 (not_323_out, OP0);
  not not_324 (not_324_out, F4);
  not not_325 (not_325_out, F3);
  not not_326 (not_326_out, F1);
  not not_327 (not_327_out, OP5);
  not not_328 (not_328_out, OP4);
  not not_329 (not_329_out, OP3);
  not not_330 (not_330_out, OP2);
  not not_331 (not_331_out, OP1);
  not not_332 (not_332_out, OP0);
  not not_333 (not_333_out, F4);
  not not_334 (not_334_out, F3);
  not not_335 (not_335_out, OP5);
  not not_336 (not_336_out, OP4);
  not not_337 (not_337_out, OP3);
  not not_338 (not_338_out, OP2);
  not not_339 (not_339_out, OP1);
  not not_340 (not_340_out, OP0);
  not not_341 (not_341_out, F4);
  not not_342 (not_342_out, F2);
  not not_343 (not_343_out, F0);
  not not_344 (not_344_out, OP5);
  not not_345 (not_345_out, OP4);
  not not_346 (not_346_out, OP3);
  not not_347 (not_347_out, OP2);
  not not_348 (not_348_out, OP1);
  not not_349 (not_349_out, OP0);
  not not_350 (not_350_out, F4);
  not not_351 (not_351_out, F2);
  not not_352 (not_352_out, OP5);
  not not_353 (not_353_out, OP4);
  not not_354 (not_354_out, OP3);
  not not_355 (not_355_out, OP2);
  not not_356 (not_356_out, OP1);
  not not_357 (not_357_out, OP0);
  not not_358 (not_358_out, F4);
  not not_359 (not_359_out, F3);
  not not_360 (not_360_out, F0);
  not not_361 (not_361_out, OP5);
  not not_362 (not_362_out, OP4);
  not not_363 (not_363_out, OP3);
  not not_364 (not_364_out, OP2);
  not not_365 (not_365_out, OP1);
  not not_366 (not_366_out, OP0);
  not not_367 (not_367_out, F5);
  not not_368 (not_368_out, F4);
  not not_369 (not_369_out, F3);
  not not_370 (not_370_out, OP5);
  not not_371 (not_371_out, OP4);
  not not_372 (not_372_out, OP3);
  not not_373 (not_373_out, OP1);
  not not_374 (not_374_out, OP0);
  not not_375 (not_375_out, OP5);
  not not_376 (not_376_out, OP4);
  not not_377 (not_377_out, OP3);
  not not_378 (not_378_out, OP1);
  not not_379 (not_379_out, OP5);
  not not_380 (not_380_out, OP4);
  not not_381 (not_381_out, OP3);
  not not_382 (not_382_out, OP2);
  not not_383 (not_383_out, OP1);
  not not_384 (not_384_out, OP0);
  not not_385 (not_385_out, F5);
  not not_386 (not_386_out, F4);
  not not_387 (not_387_out, F2);
  not not_388 (not_388_out, F1);
  not not_389 (not_389_out, F0);
  not not_390 (not_390_out, OP5);
  not not_391 (not_391_out, OP4);
  not not_392 (not_392_out, OP3);
  not not_393 (not_393_out, OP2);
  not not_394 (not_394_out, OP1);
  not not_395 (not_395_out, OP0);
  not not_396 (not_396_out, F5);
  not not_397 (not_397_out, F4);
  not not_398 (not_398_out, F2);
  not not_399 (not_399_out, F1);
  not not_400 (not_400_out, F0);
  not not_401 (not_401_out, OP5);
  not not_402 (not_402_out, OP4);
  not not_403 (not_403_out, OP3);
  not not_404 (not_404_out, OP2);
  not not_405 (not_405_out, OP0);
  not not_406 (not_406_out, OP5);
  not not_407 (not_407_out, OP4);
  not not_408 (not_408_out, OP3);
  not not_409 (not_409_out, OP2);
  not not_410 (not_410_out, OP5);
  not not_411 (not_411_out, OP4);
  not not_412 (not_412_out, OP3);
  not not_413 (not_413_out, OP2);
  and and_1 (and_1_out, OP5, not_1_out, not_2_out, not_3_out, OP1, OP0);
  and and_2 (and_2_out, OP5, not_4_out, not_5_out, not_6_out, not_7_out, not_8_out);
  and and_3 (MemWrite, OP5, not_9_out, OP3, not_10_out, OP1, OP0);
  and and_4 (and_4_out, not_11_out, not_12_out, OP3, not_13_out, not_14_out, not_15_out);
  and and_5 (and_5_out, not_16_out, not_17_out, OP3, OP2, not_18_out, not_19_out);
  and and_6 (and_6_out, not_20_out, not_21_out, OP3, not_22_out, not_23_out, OP0);
  and and_7 (and_7_out, not_24_out, not_25_out, OP3, not_26_out, OP1, not_27_out);
  and and_8 (and_8_out, not_28_out, not_29_out, OP3, OP2, not_30_out, OP0);
  and and_9 (and_9_out, OP5, not_31_out, not_32_out, not_33_out, OP1, OP0);
  and and_10 (and_10_out, OP5, not_34_out, OP3, not_35_out, OP1, OP0);
  and and_11 (and_11_out, OP5, not_36_out, not_37_out, not_38_out, not_39_out, not_40_out);
  and and_12 (and_12_out, not_41_out, not_42_out, not_43_out, not_44_out, not_45_out, not_46_out, not_47_out, not_48_out, not_49_out, not_50_out, not_51_out, not_52_out);
  and and_13 (and_13_out, not_53_out, not_54_out, not_55_out, not_56_out, not_57_out, not_58_out, not_59_out, not_60_out, not_61_out, not_62_out, F1, F0);
  and and_14 (and_14_out, not_63_out, not_64_out, not_65_out, not_66_out, not_67_out, not_68_out, not_69_out, not_70_out, not_71_out, not_72_out, F1, not_73_out);
  and and_15 (and_15_out, not_74_out, not_75_out, not_76_out, not_77_out, not_78_out, not_79_out, F5, not_80_out, not_81_out, not_82_out, not_83_out, not_84_out);
  and and_16 (and_16_out, not_85_out, not_86_out, not_87_out, not_88_out, not_89_out, not_90_out, F5, not_91_out, not_92_out, not_93_out, not_94_out, F0);
  and and_17 (and_17_out, not_95_out, not_96_out, not_97_out, not_98_out, not_99_out, not_100_out, F5, not_101_out, not_102_out, not_103_out, F1, not_104_out);
  and and_18 (and_18_out, not_105_out, not_106_out, not_107_out, not_108_out, not_109_out, not_110_out, F5, not_111_out, not_112_out, F2, not_113_out, not_114_out);
  and and_19 (and_19_out, not_115_out, not_116_out, not_117_out, not_118_out, not_119_out, not_120_out, F5, not_121_out, not_122_out, F2, not_123_out, F0);
  and and_20 (and_20_out, not_124_out, not_125_out, not_126_out, not_127_out, not_128_out, not_129_out, F5, not_130_out, not_131_out, F2, F1, F0);
  and and_21 (and_21_out, not_132_out, not_133_out, not_134_out, not_135_out, not_136_out, not_137_out, F5, not_138_out, F3, not_139_out, F1, not_140_out);
  and and_22 (and_22_out, not_141_out, not_142_out, not_143_out, not_144_out, not_145_out, not_146_out, F5, not_147_out, F3, not_148_out, F1, F0);
  and and_23 (and_23_out, not_149_out, not_150_out, not_151_out, not_152_out, OP1, OP0);
  and and_24 (and_24_out, not_153_out, not_154_out, OP3, not_155_out, not_156_out, not_157_out);
  and and_25 (and_25_out, not_158_out, not_159_out, OP3, OP2, not_160_out, not_161_out);
  and and_26 (and_26_out, not_162_out, not_163_out, OP3, not_164_out, not_165_out, OP0);
  and and_27 (and_27_out, not_166_out, not_167_out, OP3, not_168_out, OP1, not_169_out);
  and and_28 (and_28_out, not_170_out, not_171_out, OP3, OP2, not_172_out, OP0);
  and and_29 (and_29_out, OP5, not_173_out, not_174_out, not_175_out, OP1, OP0);
  and and_30 (and_30_out, not_176_out, not_177_out, not_178_out, not_179_out, not_180_out, not_181_out, F5, not_182_out, not_183_out, F2, F1, not_184_out);
  and and_31 (and_31_out, not_185_out, not_186_out, not_187_out, not_188_out, not_189_out, not_190_out, not_191_out, not_192_out, not_193_out, F2, F1, F0);
  and and_32 (and_32_out, OP5, not_194_out, not_195_out, not_196_out, not_197_out, not_198_out);
  and and_33 (SysCALL, not_199_out, not_200_out, not_201_out, not_202_out, not_203_out, not_204_out, not_205_out, not_206_out, F3, F2, not_207_out, not_208_out);
  and and_34 (and_34_out, not_209_out, not_210_out, not_211_out, OP2, not_212_out, not_213_out);
  and and_35 (and_35_out, not_214_out, not_215_out, not_216_out, OP2, not_217_out, OP0);
  and and_36 (and_36_out, not_218_out, not_219_out, OP3, not_220_out, not_221_out, not_222_out);
  and and_37 (and_37_out, not_223_out, not_224_out, OP3, not_225_out, not_226_out, OP0);
  and and_38 (and_38_out, not_227_out, not_228_out, OP3, not_229_out, OP1, not_230_out);
  and and_39 (and_39_out, OP5, not_231_out, not_232_out, not_233_out, OP1, OP0);
  and and_40 (and_40_out, OP5, not_234_out, OP3, not_235_out, OP1, OP0);
  and and_41 (and_41_out, OP5, not_236_out, not_237_out, not_238_out, not_239_out, not_240_out);
  and and_42 (and_42_out, not_241_out, not_242_out, not_243_out, OP2, OP1, OP0);
  and and_43 (and_43_out, not_244_out, not_245_out, not_246_out, not_247_out, not_248_out, not_249_out, not_250_out, not_251_out, not_252_out, not_253_out, not_254_out, not_255_out);
  and and_44 (and_44_out, not_256_out, not_257_out, not_258_out, not_259_out, not_260_out, not_261_out, not_262_out, not_263_out, not_264_out, not_265_out, F1, F0);
  and and_45 (and_45_out, not_266_out, not_267_out, not_268_out, not_269_out, not_270_out, not_271_out, not_272_out, not_273_out, not_274_out, not_275_out, F1, not_276_out);
  and and_46 (and_46_out, not_277_out, not_278_out, not_279_out, not_280_out, not_281_out, not_282_out, F5, not_283_out, not_284_out, not_285_out, not_286_out, not_287_out);
  and and_47 (and_47_out, not_288_out, not_289_out, not_290_out, not_291_out, not_292_out, not_293_out, F5, not_294_out, not_295_out, not_296_out, not_297_out, F0);
  and and_48 (and_48_out, not_298_out, not_299_out, not_300_out, not_301_out, not_302_out, not_303_out, F5, not_304_out, not_305_out, not_306_out, F1, not_307_out);
  and and_49 (and_49_out, not_308_out, not_309_out, not_310_out, not_311_out, not_312_out, not_313_out, F5, not_314_out, not_315_out, F2, not_316_out, not_317_out);
  and and_50 (and_50_out, not_318_out, not_319_out, not_320_out, not_321_out, not_322_out, not_323_out, F5, not_324_out, not_325_out, F2, not_326_out, F0);
  and and_51 (and_51_out, not_327_out, not_328_out, not_329_out, not_330_out, not_331_out, not_332_out, F5, not_333_out, not_334_out, F2, F1, F0);
  and and_52 (and_52_out, not_335_out, not_336_out, not_337_out, not_338_out, not_339_out, not_340_out, F5, not_341_out, F3, not_342_out, F1, not_343_out);
  and and_53 (and_53_out, not_344_out, not_345_out, not_346_out, not_347_out, not_348_out, not_349_out, F5, not_350_out, F3, not_351_out, F1, F0);
  and and_54 (and_54_out, not_352_out, not_353_out, not_354_out, not_355_out, not_356_out, not_357_out, F5, not_358_out, not_359_out, F2, F1, not_360_out);
  and and_55 (and_55_out, not_361_out, not_362_out, not_363_out, not_364_out, not_365_out, not_366_out, not_367_out, not_368_out, not_369_out, F2, F1, F0);
  and and_56 (BEQ, not_370_out, not_371_out, not_372_out, OP2, not_373_out, not_374_out);
  and and_57 (BNE, not_375_out, not_376_out, not_377_out, OP2, not_378_out, OP0);
  and and_58 (JR, not_379_out, not_380_out, not_381_out, not_382_out, not_383_out, not_384_out, not_385_out, not_386_out, F3, not_387_out, not_388_out, not_389_out);
  and and_59 (and_59_out, not_390_out, not_391_out, not_392_out, not_393_out, not_394_out, not_395_out, not_396_out, not_397_out, F3, not_398_out, not_399_out, not_400_out);
  and and_60 (and_60_out, not_401_out, not_402_out, not_403_out, not_404_out, OP1, not_405_out);
  and and_61 (and_61_out, not_406_out, not_407_out, not_408_out, not_409_out, OP1, OP0);
  and and_62 (JAL, not_410_out, not_411_out, not_412_out, not_413_out, OP1, OP0);
  or or_1 (MemToReg, and_1_out, and_2_out);
  or or_2 (ALU_SRC, and_4_out, and_5_out, and_6_out, and_7_out, and_8_out, and_9_out, and_10_out, and_11_out);
  or or_3 (SignedExt, and_34_out, and_35_out, and_36_out, and_37_out, and_38_out, and_39_out, and_40_out, and_41_out, and_42_out);
  or or_4 (JUMP, and_59_out, and_60_out, and_61_out);
  or or_5 (RegWrite, and_12_out, and_13_out, and_14_out, and_15_out, and_16_out, and_17_out, and_18_out, and_19_out, and_20_out, and_21_out, and_22_out, and_23_out, and_24_out, and_25_out, and_26_out, and_27_out, and_28_out, and_29_out, and_30_out, and_31_out, and_32_out);
  or or_6 (RegDst, and_43_out, and_44_out, and_45_out, and_46_out, and_47_out, and_48_out, and_49_out, and_50_out, and_51_out, and_52_out, and_53_out, and_54_out, and_55_out);
endmodule

// ALU
module MIPS_ALU (
  input  [4:0] shamt,
  input  [31:0] X,
  input  [31:0] Y,
  input  [3:0] AluOP,
  output Equal,
  output [31:0] Result,
  output [31:0] Result_2
);

  wire [0:0] comparator_1_lt, comparator_2_lt;
  wire [31:0] adder_1_out, AND_out, divider_1_out, divider_1_rem, multiplier_1_cout, multiplier_1_out,
       NOR_out, OR_out, shifter_1_out, shifter_2_out, shifter_3_out, subtractor_1_out, XOR_out;

  assign AND_out = X & Y;  // AND_Gate AND, 32 bits wide
  assign OR_out = X | Y;  // OR_Gate OR, 32 bits wide
  Shifter #(.width(32), .shift("ll")) shifter_1 (.in(Y), .\dist (shamt), .out(shifter_1_out));
  Shifter #(.width(32), .shift("ar")) shifter_2 (.in(Y), .\dist (shamt), .out(shifter_2_out));
  Shifter #(.width(32), .shift("lr")) shifter_3 (.in(Y), .\dist (shamt), .out(shifter_3_out));
  Multiplier #(.width(32)) multiplier_1 (.a(X), .b(Y), .out(multiplier_1_out), .cout(multiplier_1_cout));  // open: cin
  Divider #(.width(32)) divider_1 (.a(X), .b(Y), .out(divider_1_out), .rem(divider_1_rem));  // open: upper
  Adder #(.width(32)) adder_1 (.a(X), .b(Y), .out(adder_1_out));  // open: cin, cout
  Subtractor #(.width(32)) subtractor_1 (.a(X), .b(Y), .out(subtractor_1_out));  // open: bin, bout
  assign XOR_out = X ^ Y;  // XOR_Gate XOR, 32 bits wide
  assign NOR_out = ~(X | Y);  // NOR_Gate NOR, 32 bits wide
  Comparator #(.width(32), .mode("twosComplement")) comparator_1 (
    .a(X), .b(Y), .eq(Equal), .lt(comparator_1_lt[0]));  // open: gt
  Comparator #(.width(32), .mode("unsigned")) comparator_2 (.a(X), .b(Y), .lt(comparator_2_lt[0]));  // open: gt, eq
  Multiplexer #(.select(4), .width(32), .disabled("Z"), .enable("false")) multiplexer_1 (
    .in0(shifter_1_out), .in1(shifter_2_out), .in2(shifter_3_out), .in3(multiplier_1_out),
    .in4(divider_1_out), .in5(adder_1_out), .in6(subtractor_1_out), .in7(AND_out), .in8(OR_out),
    .in9(XOR_out), .in10(NOR_out), .in11({{31{1'b0}}, comparator_1_lt[0]}),
    .in12({{31{1'b0}}, comparator_2_lt[0]}), .in13({32{1'b0}}), .in14({32{1'b0}}), .in15({32{1'b0}}),
    .out(Result), .sel(AluOP));
  Multiplexer #(.select(4), .width(32), .disabled("Z"), .enable("false")) multiplexer_2 (
    .in0({32{1'b0}}), .in1({32{1'b0}}), .in2({32{1'b0}}), .in3(multiplier_1_cout), .in4(divider_1_rem),
    .in5({32{1'b0}}), .in6({32{1'b0}}), .in7({32{1'b0}}), .in8({32{1'b0}}), .in9({32{1'b0}}),
    .in10({32{1'b0}}), .in11({32{1'b0}}), .in12({32{1'b0}}), .in13({32{1'b0}}), .in14({32{1'b0}}),
    .in15({32{1'b0}}), .out(Result_2), .sel(AluOP));

  // Other names for the same wires on the sheet: Result2[31:0] = Result_2; S[3:0] = AluOP

  // Notes on the sheet:
  //   不要改变此引脚区域内容，也不要改变ALU封装形式
  //   输入引脚
  //   输出引脚
endmodule

module MIPS_Regifile (
  input  [31:0] Din,
  input  Clk,
  input  WE,
  input  [4:0] R1_num,
  input  [4:0] R2_num,
  input  [4:0] W_num,
  output [31:0] R1,
  output [31:0] R2
);

  // RegisterFile registerfile_1: pin names not known; wires that end beside it: Din, Clk, WE, W_num, R1_num, R2_num, R1, R2
endmodule

module \理想流水线  (
  output RegWrite,
  output MemWrite,
  output [31:0] IF_PC,
  output [31:0] ID_PC,
  output [31:0] EX_PC,
  output [31:0] M_PC,
  output [31:0] WB_PC,
  output [31:0] RDin,
  output [31:0] MDin,
  output [31:0] LedData
);

  wire and_1_out, and_2_out, and_3_out, and_4_out, and_5_out, and_6_out, and_7_out, and_8_out, and_11_out,
       and_12_out, and_13_out, and_14_out, and_15_out, and_16_out, and_17_out, and_18_out, and_19_out,
       and_20_out, B, bdc, CLK, comparator_1_eq, comparator_2_eq, comparator_3_eq, comparator_4_eq,
       comparator_5_eq, comparator_6_eq, comparator_7_eq, comparator_8_eq, comparator_9_gt, comparator_10_eq,
       comparator_11_eq, Ex_Conflict, Ex_RegWrite, Go, Halt, IR1, IR2, IR3, JAL, JMP, JR, Mem_Conflict,
       Mem_RegWrite, mips_alu_3_equal, not_1_out, not_2_out, not_3_out, not_4_out, not_5_out, not_6_out,
       not_7_out, not_8_out, or_2_out, or_3_out, or_6_out, R1_NotUsed, R2_NotUsed, RST, SignedExt, Syscall,
       W1, W2, W3, \单周期硬布线控制器_1_alu_src , \单周期硬布线控制器_1_beq , \单周期硬布线控制器_1_bne , \单周期硬布线控制器_1_jal ,
       \单周期硬布线控制器_1_jmp , \单周期硬布线控制器_1_jr , \单周期硬布线控制器_1_memtoreg , \单周期硬布线控制器_1_memwrite ,
       \单周期硬布线控制器_1_regdst , \单周期硬布线控制器_1_regwrite , \单周期硬布线控制器_1_syscall , \数据相关 , \无条件 ,
       \气泡ex_mem_1_dout22_8 , \气泡ex_mem_1_dout22_9 , \气泡ex_mem_1_dout22_10 , \气泡ex_mem_1_传输状态out_表明当前传输数据有效 ,
       \气泡id_ex_1_dout22_6 , \气泡id_ex_1_dout22_7 , \气泡id_ex_1_dout22_8 , \气泡id_ex_1_dout22_9 ,
       \气泡id_ex_1_dout22_10 , \气泡id_ex_1_传输状态out_表明当前传输数据有效 , \气泡if_id_1_传输状态out_表明当前传输数据有效 ,
       \气泡mem_wb_1_dout22_7 , \气泡mem_wb_1_dout22_10 ;
  wire [1:0] \气泡mem_wb_1_dout22_11 ;
  wire [3:0] \单周期硬布线控制器_1_alu_op , \气泡id_ex_1_dout22_14 ;
  wire [4:0] bit_extender_4_out, Ex_WriteReg_num, LB, Mem_WriteReg_num, multiplexer_4_out, multiplexer_5_out,
       multiplexer_6_out, multiplexer_7_out, multiplexer_10_out, multiplexer_13_out, R1_num, R2_num, W_num,
       \气泡id_ex_1_dout22_21 ;
  wire [5:0] OP, \气泡ex_mem_1_dout22_2 , \气泡id_ex_1_dout22_4 , \气泡id_ex_1_dout22_22 ;
  wire [15:0] \LoadUse次数 , \总周期数 , \插入气泡数 , \无条件分支数 , \条件分支成功数 ;
  wire [31:0] bit_extender_1_out, bit_extender_2_out, bit_extender_3_out, IR, mips_alu_1_result,
       mips_alu_2_result, mips_alu_3_result, mips_regifile_1_r1, mips_regifile_1_r2, multiplexer_1_out,
       multiplexer_2_out, multiplexer_3_out, multiplexer_11_out, multiplexer_12_out, multiplexer_15_out,
       multiplexer_16_out, PC_4, ram_1_data, rs, rsf, rt, shifter_1_out, shifter_2_out,
       \气泡ex_mem_1_dout22_3 , \气泡ex_mem_1_dout22_13 , \气泡ex_mem_1_dout22_15 , \气泡id_ex_1_dout22_2 ,
       \气泡id_ex_1_dout22_3 , \气泡id_ex_1_dout22_15 , \气泡id_ex_1_dout22_17 , \气泡id_ex_1_dout22_18 ,
       \气泡if_id_1_dout22_2 , \气泡if_id_1_dout22_3 , \气泡mem_wb_1_dout22_12 , \气泡mem_wb_1_dout22_13 ;

  Button \u_总复位  (.out(RST));
  Button _1 (.out(IR1));
  Button _2 (.out(IR2));
  Button _3 (.out(IR3));
  Button \u_继续运行  (.out(Go));
  LED #(.active("true")) led_1 (.in(W1));
  LED #(.active("true")) led_2 (.in(W2));
  LED #(.active("true")) led_3 (.in(W3));
  Hex_Digit_Display hex_digit_display_1 (.value(LedData[31:28]));  // open: dp
  // Probe on mips_alu_2_result
  Hex_Digit_Display hex_digit_display_2 (.value(LedData[23:20]));  // open: dp
  Hex_Digit_Display hex_digit_display_3 (.value(LedData[27:24]));  // open: dp
  and and_1 (and_1_out, JMP, not_1_out);
  not not_1 (not_1_out, JR);
  Multiplexer #(.select(1), .width(32), .disabled("Z"), .enable("false")) multiplexer_1 (
    .in0(multiplexer_2_out), .in1(\气泡id_ex_1_dout22_15 ), .out(multiplexer_1_out), .sel(and_1_out));
  Multiplexer #(.select(1), .width(32), .disabled("Z"), .enable("false")) multiplexer_2 (
    .in0(multiplexer_3_out), .in1(rs), .out(multiplexer_2_out), .sel(JR));
  Multiplexer #(.select(1), .width(32), .disabled("Z"), .enable("false")) multiplexer_3 (
    .in0(mips_alu_1_result), .in1(mips_alu_2_result), .out(multiplexer_3_out), .sel(B));
  Hex_Digit_Display hex_digit_display_4 (.value(LedData[15:12]));  // open: dp
  Hex_Digit_Display hex_digit_display_5 (.value(LedData[19:16]));  // open: dp
  Register #(.width(32), .trigger("rising"), .Select("low")) PC (
    .D(multiplexer_1_out), .en(and_2_out), .Q(IF_PC), .clk(CLK), .clr(RST));
  and and_2 (and_2_out, ~Halt, ~and_3_out);  // AND_Gate
  and and_3 (and_3_out, \数据相关 , ~bdc);  // AND_Gate
  Multiplexer #(.select(1), .width(5), .disabled("Z"), .enable("false")) multiplexer_4 (
    .in0(R1_num), .in1({5{1'b0}}), .out(multiplexer_4_out), .sel(R1_NotUsed));
  Multiplexer #(.select(1), .width(5), .disabled("Z"), .enable("false")) multiplexer_5 (
    .in0(R2_num), .in1({5{1'b0}}), .out(multiplexer_5_out), .sel(R2_NotUsed));
  Hex_Digit_Display hex_digit_display_6 (.value(LedData[7:4]));  // open: dp
  Hex_Digit_Display hex_digit_display_7 (.value(LedData[11:8]));  // open: dp
  Clock #(.highDuration(1), .lowDuration(1)) clock_1 (.out(CLK));
  Hex_Digit_Display hex_digit_display_8 (.value(LedData[3:0]));  // open: dp
  // Probe on IF_PC
  MIPS_ALU mips_alu_1 (
    .X(IF_PC), .Y(32'h4), .AluOP(4'b0101), .Result(mips_alu_1_result));  // open: Equal, Result_2, shamt
  ROM #(.addrWidth(10), .dataWidth(32), .Select("high")) rom_1 (.addr(IF_PC[11:2]), .data(IR));
  Comparator #(.width(5), .mode("twosComplement")) comparator_1 (
    .a(multiplexer_4_out), .b(Ex_WriteReg_num), .eq(comparator_1_eq));  // open: gt, lt
  Comparator #(.width(5), .mode("twosComplement")) comparator_2 (
    .a(Ex_WriteReg_num), .b(multiplexer_5_out), .eq(comparator_2_eq));  // open: gt, lt
  Comparator #(.width(5), .mode("twosComplement")) comparator_3 (
    .a(multiplexer_4_out), .b({5{1'b0}}), .eq(comparator_3_eq));  // open: gt, lt
  Comparator #(.width(5), .mode("twosComplement")) comparator_4 (
    .a(multiplexer_5_out), .b({5{1'b0}}), .eq(comparator_4_eq));  // open: gt, lt
  Comparator #(.width(5), .mode("twosComplement")) comparator_5 (
    .a(multiplexer_4_out), .b(Mem_WriteReg_num), .eq(comparator_5_eq));  // open: gt, lt
  Comparator #(.width(5), .mode("twosComplement")) comparator_6 (
    .a(Mem_WriteReg_num), .b(multiplexer_5_out), .eq(comparator_6_eq));  // open: gt, lt
  // Probe on \总周期数 
  // Probe on \无条件分支数 
  // Probe on \条件分支成功数 
  // Probe on \插入气泡数 
  // Probe on \LoadUse次数 
  or or_1 (bdc, B, \无条件 );
  \气泡IF_ID  \u_气泡if_id_1  (
    .Din22_2(mips_alu_1_result), .Din22_3(IR), .\传输状态In_表明当前传输数据有效 (1'b1), .Dout22_2(\气泡if_id_1_dout22_2 ),
    .Dout22_3(\气泡if_id_1_dout22_3 ), .\传输状态Out_表明当前传输数据有效 (\气泡if_id_1_传输状态out_表明当前传输数据有效 ),
    .\同步清零_气泡_高电平有效 (bdc), .CLK(CLK), .\使能端_低电平有效_stall_高电平有效 (and_8_out), .Din22(IF_PC), .Dout22(ID_PC));
  and and_4 (and_4_out, comparator_1_eq, ~comparator_3_eq);  // AND_Gate
  and and_5 (and_5_out, comparator_2_eq, ~comparator_4_eq);  // AND_Gate
  and and_6 (and_6_out, comparator_5_eq, ~comparator_3_eq);  // AND_Gate
  and and_7 (and_7_out, comparator_6_eq, ~comparator_4_eq);  // AND_Gate
  // Probe on IF_PC[11:0]
  // Probe on EX_PC[11:0]
  // Probe on ID_PC[11:0]
  and and_8 (and_8_out, \数据相关 , ~bdc);  // AND_Gate
  or or_2 (or_2_out, and_4_out, and_5_out);
  or or_3 (or_3_out, and_6_out, and_7_out);
  // Probe on M_PC[11:0]
  R_Not_Used r_not_used_1 (
    .OpCode(\气泡if_id_1_dout22_3 [31:26]), .Funct(\气泡if_id_1_dout22_3 [5:0]), .R2_Unused(R2_NotUsed),
    .R1_Unused(R1_NotUsed));
  Multiplexer #(.select(1), .width(5), .disabled("Z"), .enable("false")) multiplexer_6 (
    .in0(\气泡if_id_1_dout22_3 [25:21]), .in1(5'b00010), .out(multiplexer_6_out), .sel(\单周期硬布线控制器_1_syscall ));
  Multiplexer #(.select(1), .width(5), .disabled("Z"), .enable("false")) multiplexer_7 (
    .in0(\气泡if_id_1_dout22_3 [20:16]), .in1(\气泡if_id_1_dout22_3 [15:11]), .out(multiplexer_7_out),
    .sel(\单周期硬布线控制器_1_regdst ));
  and and_9 (Ex_Conflict, or_2_out, Ex_RegWrite);
  and and_10 (Mem_Conflict, or_3_out, Mem_RegWrite);
  // Probe on WB_PC[11:0]
  Multiplexer #(.select(1), .width(5), .disabled("Z"), .enable("false")) multiplexer_8 (
    .in0(multiplexer_6_out), .in1({5{1'b1}}), .out(R1_num), .sel(\单周期硬布线控制器_1_jr ));
  Multiplexer #(.select(1), .width(5), .disabled("Z"), .enable("false")) multiplexer_9 (
    .in0(\气泡if_id_1_dout22_3 [20:16]), .in1(5'b00100), .out(R2_num), .sel(\单周期硬布线控制器_1_syscall ));
  Multiplexer #(.select(1), .width(5), .disabled("Z"), .enable("false")) multiplexer_10 (
    .in0(multiplexer_7_out), .in1({5{1'b1}}), .out(multiplexer_10_out), .sel(\单周期硬布线控制器_1_jal ));
  assign bit_extender_1_out = {{16{1'b0}}, \气泡if_id_1_dout22_3 [15:0]};  // Bit_Extender bit_extender_1
  assign bit_extender_2_out = {{16{\气泡if_id_1_dout22_3 [15]}}, \气泡if_id_1_dout22_3 [15:0]};  // Bit_Extender bit_extender_2
  or or_4 (\数据相关 , Ex_Conflict, Mem_Conflict);
  \单周期硬布线控制器  \u_单周期硬布线控制器_1  (
    .Func(\气泡if_id_1_dout22_3 [5:0]), .OP(\气泡if_id_1_dout22_3 [31:26]), .ALU_OP(\单周期硬布线控制器_1_alu_op ),
    .MemToReg(\单周期硬布线控制器_1_memtoreg ), .MemWrite(\单周期硬布线控制器_1_memwrite ), .ALU_SRC(\单周期硬布线控制器_1_alu_src ),
    .RegWrite(\单周期硬布线控制器_1_regwrite ), .SysCALL(\单周期硬布线控制器_1_syscall ), .SignedExt(SignedExt),
    .RegDst(\单周期硬布线控制器_1_regdst ), .JR(\单周期硬布线控制器_1_jr ), .JMP(\单周期硬布线控制器_1_jmp ), .Beq(\单周期硬布线控制器_1_beq ),
    .JAL(\单周期硬布线控制器_1_jal ), .Bne(\单周期硬布线控制器_1_bne ));
  MIPS_Regifile mips_regifile_1 (
    .Din(RDin), .Clk(CLK), .R1(mips_regifile_1_r1), .R2(mips_regifile_1_r2), .WE(RegWrite), .W_num(W_num),
    .R1_num(R1_num), .R2_num(R2_num));
  Multiplexer #(.select(1), .width(32), .disabled("Z"), .enable("false")) multiplexer_11 (
    .in0(bit_extender_1_out), .in1(bit_extender_2_out), .out(multiplexer_11_out), .sel(SignedExt));
  Counter #(.width(16), .max('hffff), .ongoal("wrap"), .trigger("rising"), .behavior("old")) counter_1 (
    .Q(\总周期数 ), .clk(and_11_out));  // open: load, D, count, carry, clr, preset
  and and_11 (and_11_out, CLK, not_2_out);
  not not_2 (not_2_out, Halt);
  or or_5 (\无条件 , JMP, JAL, JR);
  or or_6 (or_6_out, bdc, Ex_Conflict, Mem_Conflict);
  Multiplexer #(.select(1), .width(32), .disabled("Z"), .enable("false")) multiplexer_12 (
    .in0(mips_regifile_1_r2), .in1(multiplexer_11_out), .out(multiplexer_12_out), .sel(\单周期硬布线控制器_1_alu_src ));
  Shifter #(.width(32), .shift("ll")) shifter_1 (.in(multiplexer_11_out), .\dist (5'b00010), .out(shifter_1_out));
  // Probe on \总周期数 
  \气泡ID_EX  \u_气泡id_ex_1  (
    .Din22_2(\气泡if_id_1_dout22_2 ), .Din22_3(shifter_1_out),
    .\传输状态In_表明当前传输数据有效 (\气泡if_id_1_传输状态out_表明当前传输数据有效 ), .Dout22_2(\气泡id_ex_1_dout22_2 ),
    .Dout22_3(\气泡id_ex_1_dout22_3 ), .\传输状态Out_表明当前传输数据有效 (\气泡id_ex_1_传输状态out_表明当前传输数据有效 ),
    .\同步清零_气泡_高电平有效 (or_6_out), .CLK(CLK), .Din22_4(\气泡if_id_1_dout22_3 [31:26]),
    .Dout22_4(\气泡id_ex_1_dout22_4 ), .Din22_6(\单周期硬布线控制器_1_beq ), .Dout22_6(\气泡id_ex_1_dout22_6 ),
    .Din22_7(\单周期硬布线控制器_1_bne ), .Dout22_7(\气泡id_ex_1_dout22_7 ), .Din22_8(\单周期硬布线控制器_1_syscall ),
    .Dout22_8(\气泡id_ex_1_dout22_8 ), .Din22_9(\单周期硬布线控制器_1_memtoreg ), .Dout22_9(\气泡id_ex_1_dout22_9 ),
    .Din22_10(\单周期硬布线控制器_1_memwrite ), .Dout22_10(\气泡id_ex_1_dout22_10 ), .Din22_11(\单周期硬布线控制器_1_jmp ),
    .Dout22_11(JMP), .Din22_12(\单周期硬布线控制器_1_jr ), .Dout22_12(JR), .Din22_13(\单周期硬布线控制器_1_jal ),
    .Dout22_13(JAL), .Din22_16(mips_regifile_1_r1), .Dout22_16(rs), .Din22_17(multiplexer_12_out),
    .Dout22_17(\气泡id_ex_1_dout22_17 ), .Din22_14(\单周期硬布线控制器_1_alu_op ), .Dout22_14(\气泡id_ex_1_dout22_14 ),
    .Din22_18(mips_regifile_1_r2), .Dout22_18(\气泡id_ex_1_dout22_18 ), .Din22_21(\气泡if_id_1_dout22_3 [10:6]),
    .Dout22_21(\气泡id_ex_1_dout22_21 ), .Din22_22(\气泡if_id_1_dout22_3 [5:0]),
    .Dout22_22(\气泡id_ex_1_dout22_22 ), .Din22_23(multiplexer_10_out), .Dout22_23(Ex_WriteReg_num),
    .Din22_5(\单周期硬布线控制器_1_regwrite ), .Dout22_5(Ex_RegWrite),
    .Din22_15({\气泡if_id_1_dout22_2 [31:28], \气泡if_id_1_dout22_3 [25:0], 2'b00}),
    .Dout22_15(\气泡id_ex_1_dout22_15 ), .Din22(ID_PC), .Dout22(EX_PC));  // open: 使能端_低电平有效_stall_高电平有效, Din22_20, Dout22_20, Din22_19, Dout22_19
  Counter #(.width(16), .max('hffff), .ongoal("wrap"), .trigger("falling"), .behavior("old")) counter_2 (
    .count(\无条件 ), .Q(\无条件分支数 ), .clk(and_12_out));  // open: load, D, carry, clr, preset
  and and_12 (and_12_out, CLK, not_3_out);
  not not_3 (not_3_out, Halt);
  Multiplexer #(.select(1), .width(5), .disabled("Z"), .enable("false")) multiplexer_13 (
    .in0(\气泡id_ex_1_dout22_21 ), .in1(rs[4:0]), .out(multiplexer_13_out), .sel(comparator_7_eq));
  Comparator #(.width(6), .mode("twosComplement")) comparator_7 (
    .a(\气泡id_ex_1_dout22_22 ), .b(6'b000111), .eq(comparator_7_eq));  // open: gt, lt
  Counter #(.width(16), .max('hffff), .ongoal("wrap"), .trigger("rising"), .behavior("old")) counter_3 (
    .count(B), .Q(\条件分支成功数 ), .clk(and_13_out));  // open: load, D, carry, clr, preset
  and and_13 (and_13_out, CLK, not_4_out);
  not not_4 (not_4_out, Halt);
  MIPS_ALU mips_alu_2 (
    .X(\气泡id_ex_1_dout22_2 ), .Y(\气泡id_ex_1_dout22_3 ), .AluOP(4'b0101), .Result(mips_alu_2_result),
    .shamt({5{1'b0}}));  // open: Equal, Result_2
  Comparator #(.width(6), .mode("twosComplement")) comparator_8 (
    .a(\气泡id_ex_1_dout22_4 ), .b(6'b000111), .eq(comparator_8_eq));  // open: gt, lt
  and and_14 (and_14_out, comparator_8_eq, comparator_9_gt);
  Comparator #(.width(32), .mode("twosComplement")) comparator_9 (
    .a(rs), .b({32{1'b0}}), .gt(comparator_9_gt));  // open: eq, lt
  and and_15 (and_15_out, \气泡id_ex_1_dout22_6 , mips_alu_3_equal);
  and and_16 (and_16_out, \气泡id_ex_1_dout22_7 , not_5_out);
  not not_5 (not_5_out, mips_alu_3_equal);
  MIPS_ALU mips_alu_3 (
    .X(rs), .Y(\气泡id_ex_1_dout22_17 ), .AluOP(\气泡id_ex_1_dout22_14 ), .Equal(mips_alu_3_equal),
    .Result(mips_alu_3_result), .shamt(multiplexer_13_out));  // open: Result_2
  or or_7 (B, and_14_out, and_15_out, and_16_out);
  and and_17 (and_17_out, \数据相关 , ~bdc);  // AND_Gate
  // Probe on mips_alu_3_result
  Counter #(.width(16), .max('hffff), .ongoal("wrap"), .trigger("rising"), .behavior("old")) counter_4 (
    .count(and_17_out), .Q(\插入气泡数 ), .clk(and_18_out));  // open: load, D, carry, clr, preset
  and and_18 (and_18_out, CLK, not_6_out);
  not not_6 (not_6_out, Halt);
  \气泡EX_MEM  \u_气泡ex_mem_1  (
    .Din22_8(JAL), .Din22_9(\气泡id_ex_1_dout22_8 ), .Din22_10(\气泡id_ex_1_dout22_9 ),
    .Din22_11(\气泡id_ex_1_dout22_10 ), .Din22_13(mips_alu_3_result), .Din22_14(\气泡id_ex_1_dout22_18 ),
    .\传输状态In_表明当前传输数据有效 (\气泡id_ex_1_传输状态out_表明当前传输数据有效 ), .Dout22_8(\气泡ex_mem_1_dout22_8 ),
    .Dout22_9(\气泡ex_mem_1_dout22_9 ), .Dout22_10(\气泡ex_mem_1_dout22_10 ), .Dout22_11(MemWrite),
    .Dout22_13(\气泡ex_mem_1_dout22_13 ), .Dout22_14(MDin),
    .\传输状态Out_表明当前传输数据有效 (\气泡ex_mem_1_传输状态out_表明当前传输数据有效 ), .CLK(CLK), .Din22_2(\气泡id_ex_1_dout22_4 ),
    .Dout22_2(\气泡ex_mem_1_dout22_2 ), .Din22_3(\气泡id_ex_1_dout22_2 ), .Dout22_3(\气泡ex_mem_1_dout22_3 ),
    .Din22_15(rs), .Dout22_15(\气泡ex_mem_1_dout22_15 ), .Din22_16(Ex_WriteReg_num),
    .Dout22_16(Mem_WriteReg_num), .Din22_4(Ex_RegWrite), .Dout22_4(Mem_RegWrite), .Din22(EX_PC), .Dout22(M_PC));  // open: Din22_5, Din22_6, Din22_7, Dout22_5, Dout22_6, Dout22_7, 同步清零_气泡_高电平有效, 使能端_低电平有效_stall_高电平有效, Din22_12, Dout22_12
  Multiplexer #(.select(1), .width(32), .disabled("Z"), .enable("false")) multiplexer_14 (
    .in0(multiplexer_15_out), .in1(PC_4), .out(RDin), .sel(\气泡mem_wb_1_dout22_10 ));
  // Probe on \气泡ex_mem_1_dout22_13 
  // Probe on MDin
  Comparator #(.width(32), .mode("twosComplement")) comparator_10 (
    .a(rsf), .b(32'h22), .eq(comparator_10_eq));  // open: gt, lt
  Multiplexer #(.select(1), .width(32), .disabled("Z"), .enable("false")) multiplexer_15 (
    .in0(multiplexer_16_out), .in1(bit_extender_3_out), .out(multiplexer_15_out), .sel(comparator_11_eq));
  Comparator #(.width(6), .mode("twosComplement")) comparator_11 (
    .a(OP), .b(6'b100000), .eq(comparator_11_eq));  // open: gt, lt
  not not_7 (not_7_out, comparator_10_eq);
  and and_19 (and_19_out, comparator_10_eq, Syscall);
  not not_8 (not_8_out, Halt);
  and and_20 (and_20_out, Syscall, not_7_out);
  \气泡MEM_WB  \u_气泡mem_wb_1  (
    .Din22_6(\气泡ex_mem_1_dout22_9 ), .Din22_7(\气泡ex_mem_1_dout22_10 ), .Din22_10(\气泡ex_mem_1_dout22_8 ),
    .Din22_11(\气泡ex_mem_1_dout22_13 [1:0]), .Din22_12(\气泡ex_mem_1_dout22_13 ), .Din22_13(ram_1_data),
    .\传输状态In_表明当前传输数据有效 (\气泡ex_mem_1_传输状态out_表明当前传输数据有效 ), .Dout22_6(Syscall),
    .Dout22_7(\气泡mem_wb_1_dout22_7 ), .Dout22_10(\气泡mem_wb_1_dout22_10 ), .Dout22_11(\气泡mem_wb_1_dout22_11 ),
    .Dout22_12(\气泡mem_wb_1_dout22_12 ), .Dout22_13(\气泡mem_wb_1_dout22_13 ), .CLK(CLK),
    .Din22_2(\气泡ex_mem_1_dout22_2 ), .Dout22_2(OP), .Din22_3(\气泡ex_mem_1_dout22_3 ), .Dout22_3(PC_4),
    .Din22_14(\气泡ex_mem_1_dout22_15 ), .Dout22_14(rsf), .Din22_15(Mem_WriteReg_num), .Dout22_15(W_num),
    .Din22_4(Mem_RegWrite), .Dout22_4(RegWrite), .Din22_16(MDin), .Dout22_16(rt), .Din22(M_PC), .Dout22(WB_PC));  // open: Din22_5, Din22_8, Din22_9, Dout22_5, Dout22_8, Dout22_9, 传输状态Out_表明当前传输数据有效, 同步清零_气泡_高电平有效, 使能端_低电平有效_stall_高电平有效
  RAM #(.addrWidth(10), .dataWidth(32), .bus("separate"), .Select("high")) ram_1 (
    .addr(\气泡ex_mem_1_dout22_13 [11:2]), .din(MDin), .data(ram_1_data), .str(MemWrite), .sel(not_8_out),
    .clk(CLK), .clr(RST));  // open: ld
  Shifter #(.width(32), .shift("lr")) shifter_2 (.in(multiplexer_16_out), .\dist (LB), .out(shifter_2_out));
  Counter #(.width(1), .max('h1), .ongoal("wrap"), .trigger("rising"), .behavior("old")) counter_5 (
    .load(and_20_out), .D(and_20_out), .count(1'b0), .Q(Halt), .clk(CLK), .clr(Go));  // open: carry, preset
  Counter #(.width(32), .max('hffffffff), .ongoal("wrap"), .trigger("rising"), .behavior("old")) counter_6 (
    .load(and_19_out), .D(rt), .count(1'b0), .Q(LedData), .clk(CLK));  // open: carry, clr, preset
  Multiplexer #(.select(1), .width(32), .disabled("Z"), .enable("false")) multiplexer_16 (
    .in0(\气泡mem_wb_1_dout22_12 ), .in1(\气泡mem_wb_1_dout22_13 ), .out(multiplexer_16_out),
    .sel(\气泡mem_wb_1_dout22_7 ));
  assign bit_extender_3_out = {{24{shifter_2_out[7]}}, shifter_2_out[7:0]};  // Bit_Extender bit_extender_3
  assign bit_extender_4_out = {{3{1'b0}}, \气泡mem_wb_1_dout22_11 };  // Bit_Extender bit_extender_4
  Multiplier #(.width(5)) multiplier_1 (.a(bit_extender_4_out), .b(5'b01000), .out(LB));  // open: cin, cout

  // Other names for the same wires on the sheet: MEM_PC[31:0] = M_PC

  // Notes on the sheet:
  //   中断源
  //   中断等待指示
  //   总复位信号应将除ROM以外所有存储组件全部清零
  //   数码管输出
  //   数码管输出应该用寄存器锁存，否则显示数据只能一闪而过
  //   指令存储器
  //   contents of rom_1 (hex, n*v repeats v):
  //   20100000 20110000 20120000 20130000 36100000 36310001 36520002 36730003 ae100000 ae110004 ae120008
  //   ae13000c 2002000a 20110000 20120000 20130000 c
  //   指令字
  //   OP
  //   Func
  //   rs
  //   rt
  //   rd
  //   流水调试日志用
  //   JMP
  //   JR
  //   OP
  //   Func
  //   Beq
  //   Bne
  //   MemToReg
  //   MemWrite
  //   AluOP
  //   AluSrcB
  //   RegWrite
  //   JAL
  //   RegDst
  //   Syscall
  //   为方便自动评测，需要输出流水线各段保存的PC值，注意是PC不是PC+4，另外ID段寄存器写入信息，Mem段内存写入信息也要输出
  //   BGTZ
  //   SRAV指令偏移地址
endmodule

module \理想流水接口  (
  input  [3:0] Din22,
  input  Din22_2,
  input  Din22_3,
  input  Din22_4,
  input  [31:0] Din22_5,
  input  [31:0] Din22_6,
  input  [31:0] Din22_7,
  input  [31:0] Din22_8,
  input  [4:0] Din22_9,
  input  [31:0] Din22_10,
  input  [31:0] Din22_11,
  input  \传输状态In_表明当前传输数据有效 ,
  input  CLK,
  input  \同步清零_气泡_高电平有效 ,
  input  \使能端_低电平有效_stall_高电平有效 ,
  output [3:0] Dout22,
  output Dout22_2,
  output Dout22_3,
  output Dout22_4,
  output [31:0] Dout22_5,
  output [31:0] Dout22_6,
  output [31:0] Dout22_7,
  output [31:0] Dout22_8,
  output [4:0] Dout22_9,
  output [31:0] Dout22_10,
  output [31:0] Dout22_11,
  output \传输状态Out_表明当前传输数据有效 
);

  wire multiplexer_2_out, multiplexer_3_out, multiplexer_4_out, multiplexer_12_out, pull_resistor_2_node;
  wire [3:0] multiplexer_1_out;
  wire [4:0] multiplexer_9_out;
  wire [31:0] multiplexer_5_out, multiplexer_6_out, multiplexer_7_out, multiplexer_8_out, multiplexer_10_out,
       multiplexer_11_out;

  Multiplexer #(.select(1), .width(4), .disabled("Z"), .enable("false")) multiplexer_1 (
    .in0(Din22), .in1(4'b0000), .out(multiplexer_1_out), .sel(\同步清零_气泡_高电平有效 ));
  Multiplexer #(.select(1), .width(1), .disabled("Z"), .enable("false")) multiplexer_2 (
    .in0(Din22_2), .in1(1'b0), .out(multiplexer_2_out), .sel(\同步清零_气泡_高电平有效 ));
  Multiplexer #(.select(1), .width(1), .disabled("Z"), .enable("false")) multiplexer_3 (
    .in0(Din22_3), .in1(1'b0), .out(multiplexer_3_out), .sel(\同步清零_气泡_高电平有效 ));
  Multiplexer #(.select(1), .width(1), .disabled("Z"), .enable("false")) multiplexer_4 (
    .in0(Din22_4), .in1(1'b0), .out(multiplexer_4_out), .sel(\同步清零_气泡_高电平有效 ));
  Multiplexer #(.select(1), .width(32), .disabled("Z"), .enable("false")) multiplexer_5 (
    .in0(Din22_5), .in1({32{1'b0}}), .out(multiplexer_5_out), .sel(\同步清零_气泡_高电平有效 ));
  Multiplexer #(.select(1), .width(32), .disabled("Z"), .enable("false")) multiplexer_6 (
    .in0(Din22_6), .in1({32{1'b0}}), .out(multiplexer_6_out), .sel(\同步清零_气泡_高电平有效 ));
  Multiplexer #(.select(1), .width(32), .disabled("Z"), .enable("false")) multiplexer_7 (
    .in0(Din22_7), .in1({32{1'b0}}), .out(multiplexer_7_out), .sel(\同步清零_气泡_高电平有效 ));
  Multiplexer #(.select(1), .width(32), .disabled("Z"), .enable("false")) multiplexer_8 (
    .in0(Din22_8), .in1({32{1'b0}}), .out(multiplexer_8_out), .sel(\同步清零_气泡_高电平有效 ));
  Multiplexer #(.select(1), .width(5), .disabled("Z"), .enable("false")) multiplexer_9 (
    .in0(Din22_9), .in1({5{1'b0}}), .out(multiplexer_9_out), .sel(\同步清零_气泡_高电平有效 ));
  Multiplexer #(.select(1), .width(32), .disabled("Z"), .enable("false")) multiplexer_10 (
    .in0(Din22_10), .in1({32{1'b0}}), .out(multiplexer_10_out), .sel(\同步清零_气泡_高电平有效 ));
  Multiplexer #(.select(1), .width(32), .disabled("Z"), .enable("false")) multiplexer_11 (
    .in0(Din22_11), .in1({32{1'b0}}), .out(multiplexer_11_out), .sel(\同步清零_气泡_高电平有效 ));
  Multiplexer #(.select(1), .width(1), .disabled("Z"), .enable("false")) multiplexer_12 (
    .in0(\传输状态In_表明当前传输数据有效 ), .in1(1'b0), .out(multiplexer_12_out), .sel(\同步清零_气泡_高电平有效 ));
  Pull_Resistor #(.pull(0)) pull_resistor_1 (.node(\同步清零_气泡_高电平有效 ));
  Register #(.width(4), .trigger("rising"), .Select("low")) register_1 (
    .D(multiplexer_1_out), .en(pull_resistor_2_node), .Q(Dout22), .clk(CLK));  // open: clr
  Register #(.width(1), .trigger("rising"), .Select("low")) register_2 (
    .D(multiplexer_2_out), .en(pull_resistor_2_node), .Q(Dout22_2), .clk(CLK));  // open: clr
  Register #(.width(1), .trigger("rising"), .Select("low")) register_3 (
    .D(multiplexer_3_out), .en(pull_resistor_2_node), .Q(Dout22_3), .clk(CLK));  // open: clr
  Register #(.width(1), .trigger("rising"), .Select("low")) register_4 (
    .D(multiplexer_4_out), .en(pull_resistor_2_node), .Q(Dout22_4), .clk(CLK));  // open: clr
  Register #(.width(32), .trigger("rising"), .Select("low")) register_5 (
    .D(multiplexer_5_out), .en(pull_resistor_2_node), .Q(Dout22_5), .clk(CLK));  // open: clr
  Register #(.width(32), .trigger("rising"), .Select("low")) register_6 (
    .D(multiplexer_6_out), .en(pull_resistor_2_node), .Q(Dout22_6), .clk(CLK));  // open: clr
  Register #(.width(32), .trigger("rising"), .Select("low")) register_7 (
    .D(multiplexer_7_out), .en(pull_resistor_2_node), .Q(Dout22_7), .clk(CLK));  // open: clr
  Register #(.width(32), .trigger("rising"), .Select("low")) register_8 (
    .D(multiplexer_8_out), .en(pull_resistor_2_node), .Q(Dout22_8), .clk(CLK));  // open: clr
  Register #(.width(5), .trigger("rising"), .Select("low")) register_9 (
    .D(multiplexer_9_out), .en(pull_resistor_2_node), .Q(Dout22_9), .clk(CLK));  // open: clr
  Register #(.width(32), .trigger("rising"), .Select("low")) register_10 (
    .D(multiplexer_10_out), .en(pull_resistor_2_node), .Q(Dout22_10), .clk(CLK));  // open: clr
  Register #(.width(32), .trigger("rising"), .Select("low")) register_11 (
    .D(multiplexer_11_out), .en(pull_resistor_2_node), .Q(Dout22_11), .clk(CLK));  // open: clr
  Register #(.width(1), .trigger("rising"), .Select("low")) register_12 (
    .D(multiplexer_12_out), .en(pull_resistor_2_node), .Q(\传输状态Out_表明当前传输数据有效 ), .clk(CLK));  // open: clr
  Pull_Resistor #(.pull(0)) pull_resistor_2 (.node(pull_resistor_2_node));
  not not_1 (pull_resistor_2_node, \使能端_低电平有效_stall_高电平有效 );

  // Notes on the sheet:
  //   同步清零_气泡_高电平有效: pull=down
  //   使能端_低电平有效_stall_高电平有效: pull=down
endmodule
module \气泡流水线  (
  output RegWrite,
  output MemWrite,
  output [31:0] IF_PC,
  output [31:0] ID_PC,
  output [31:0] EX_PC,
  output [31:0] M_PC,
  output [31:0] WB_PC,
  output [31:0] RDin,
  output [31:0] MDin,
  output [31:0] LedData
);

  wire and_1_out, and_2_out, and_3_out, and_4_out, and_5_out, and_6_out, and_7_out, and_8_out, and_11_out,
       and_12_out, and_13_out, and_14_out, and_15_out, and_16_out, and_17_out, and_18_out, and_19_out,
       and_20_out, B, bdc, CLK, comparator_1_eq, comparator_2_eq, comparator_3_eq, comparator_4_eq,
       comparator_5_eq, comparator_6_eq, comparator_7_eq, comparator_8_eq, comparator_9_gt, comparator_10_eq,
       comparator_11_eq, Ex_Conflict, Ex_RegWrite, Go, Halt, IR1, IR2, IR3, JAL, JMP, JR, Mem_Conflict,
       Mem_RegWrite, mips_alu_3_equal, not_1_out, not_2_out, not_3_out, not_4_out, not_5_out, not_6_out,
       not_7_out, not_8_out, or_2_out, or_3_out, or_6_out, R1_NotUsed, R2_NotUsed, RST, SignedExt, Syscall,
       W1, W2, W3, \单周期硬布线控制器_1_alu_src , \单周期硬布线控制器_1_beq , \单周期硬布线控制器_1_bne , \单周期硬布线控制器_1_jal ,
       \单周期硬布线控制器_1_jmp , \单周期硬布线控制器_1_jr , \单周期硬布线控制器_1_memtoreg , \单周期硬布线控制器_1_memwrite ,
       \单周期硬布线控制器_1_regdst , \单周期硬布线控制器_1_regwrite , \单周期硬布线控制器_1_syscall , \数据相关 , \无条件 ,
       \气泡ex_mem_1_dout22_8 , \气泡ex_mem_1_dout22_9 , \气泡ex_mem_1_dout22_10 , \气泡ex_mem_1_传输状态out_表明当前传输数据有效 ,
       \气泡id_ex_1_dout22_6 , \气泡id_ex_1_dout22_7 , \气泡id_ex_1_dout22_8 , \气泡id_ex_1_dout22_9 ,
       \气泡id_ex_1_dout22_10 , \气泡id_ex_1_传输状态out_表明当前传输数据有效 , \气泡if_id_1_传输状态out_表明当前传输数据有效 ,
       \气泡mem_wb_1_dout22_7 , \气泡mem_wb_1_dout22_10 ;
  wire [1:0] \气泡mem_wb_1_dout22_11 ;
  wire [3:0] \单周期硬布线控制器_1_alu_op , \气泡id_ex_1_dout22_14 ;
  wire [4:0] bit_extender_4_out, Ex_WriteReg_num, LB, Mem_WriteReg_num, multiplexer_4_out, multiplexer_5_out,
       multiplexer_6_out, multiplexer_7_out, multiplexer_10_out, multiplexer_13_out, R1_num, R2_num, W_num,
       \气泡id_ex_1_dout22_21 ;
  wire [5:0] OP, \气泡ex_mem_1_dout22_2 , \气泡id_ex_1_dout22_4 , \气泡id_ex_1_dout22_22 ;
  wire [15:0] \LoadUse次数 , \总周期数 , \插入气泡数 , \无条件分支数 , \条件分支成功数 ;
  wire [31:0] bit_extender_1_out, bit_extender_2_out, bit_extender_3_out, IR, mips_alu_1_result,
       mips_alu_2_result, mips_alu_3_result, mips_regifile_1_r1, mips_regifile_1_r2, multiplexer_1_out,
       multiplexer_2_out, multiplexer_3_out, multiplexer_11_out, multiplexer_12_out, multiplexer_15_out,
       multiplexer_16_out, PC_4, ram_1_data, rs, rsf, rt, shifter_1_out, shifter_2_out,
       \气泡ex_mem_1_dout22_3 , \气泡ex_mem_1_dout22_13 , \气泡ex_mem_1_dout22_15 , \气泡id_ex_1_dout22_2 ,
       \气泡id_ex_1_dout22_3 , \气泡id_ex_1_dout22_15 , \气泡id_ex_1_dout22_17 , \气泡id_ex_1_dout22_18 ,
       \气泡if_id_1_dout22_2 , \气泡if_id_1_dout22_3 , \气泡mem_wb_1_dout22_12 , \气泡mem_wb_1_dout22_13 ;

  Button \u_总复位  (.out(RST));
  Button _1 (.out(IR1));
  Button _2 (.out(IR2));
  Button _3 (.out(IR3));
  Button \u_继续运行  (.out(Go));
  LED #(.active("true")) led_1 (.in(W1));
  LED #(.active("true")) led_2 (.in(W2));
  LED #(.active("true")) led_3 (.in(W3));
  Hex_Digit_Display hex_digit_display_1 (.value(LedData[31:28]));  // open: dp
  // Probe on mips_alu_2_result
  Hex_Digit_Display hex_digit_display_2 (.value(LedData[23:20]));  // open: dp
  Hex_Digit_Display hex_digit_display_3 (.value(LedData[27:24]));  // open: dp
  and and_1 (and_1_out, JMP, not_1_out);
  not not_1 (not_1_out, JR);
  Multiplexer #(.select(1), .width(32), .disabled("Z"), .enable("false")) multiplexer_1 (
    .in0(multiplexer_2_out), .in1(\气泡id_ex_1_dout22_15 ), .out(multiplexer_1_out), .sel(and_1_out));
  Multiplexer #(.select(1), .width(32), .disabled("Z"), .enable("false")) multiplexer_2 (
    .in0(multiplexer_3_out), .in1(rs), .out(multiplexer_2_out), .sel(JR));
  Multiplexer #(.select(1), .width(32), .disabled("Z"), .enable("false")) multiplexer_3 (
    .in0(mips_alu_1_result), .in1(mips_alu_2_result), .out(multiplexer_3_out), .sel(B));
  Hex_Digit_Display hex_digit_display_4 (.value(LedData[19:16]));  // open: dp
  Hex_Digit_Display hex_digit_display_5 (.value(LedData[15:12]));  // open: dp
  Register #(.width(32), .trigger("rising"), .Select("low")) PC (
    .D(multiplexer_1_out), .en(and_2_out), .Q(IF_PC), .clk(CLK), .clr(RST));
  and and_2 (and_2_out, ~Halt, ~and_3_out);  // AND_Gate
  and and_3 (and_3_out, \数据相关 , ~bdc);  // AND_Gate
  Multiplexer #(.select(1), .width(5), .disabled("Z"), .enable("false")) multiplexer_4 (
    .in0(R1_num), .in1({5{1'b0}}), .out(multiplexer_4_out), .sel(R1_NotUsed));
  Multiplexer #(.select(1), .width(5), .disabled("Z"), .enable("false")) multiplexer_5 (
    .in0(R2_num), .in1({5{1'b0}}), .out(multiplexer_5_out), .sel(R2_NotUsed));
  Hex_Digit_Display hex_digit_display_6 (.value(LedData[7:4]));  // open: dp
  Hex_Digit_Display hex_digit_display_7 (.value(LedData[11:8]));  // open: dp
  Clock #(.highDuration(1), .lowDuration(1)) clock_1 (.out(CLK));
  Hex_Digit_Display hex_digit_display_8 (.value(LedData[3:0]));  // open: dp
  // Probe on IF_PC
  MIPS_ALU mips_alu_1 (
    .X(IF_PC), .Y(32'h4), .AluOP(4'b0101), .Result(mips_alu_1_result));  // open: Equal, Result_2, shamt
  ROM #(.addrWidth(10), .dataWidth(32), .Select("high")) rom_1 (.addr(IF_PC[11:2]), .data(IR));
  Comparator #(.width(5), .mode("twosComplement")) comparator_1 (
    .a(multiplexer_4_out), .b(Ex_WriteReg_num), .eq(comparator_1_eq));  // open: gt, lt
  Comparator #(.width(5), .mode("twosComplement")) comparator_2 (
    .a(Ex_WriteReg_num), .b(multiplexer_5_out), .eq(comparator_2_eq));  // open: gt, lt
  Comparator #(.width(5), .mode("twosComplement")) comparator_3 (
    .a(multiplexer_4_out), .b({5{1'b0}}), .eq(comparator_3_eq));  // open: gt, lt
  Comparator #(.width(5), .mode("twosComplement")) comparator_4 (
    .a(multiplexer_5_out), .b({5{1'b0}}), .eq(comparator_4_eq));  // open: gt, lt
  Comparator #(.width(5), .mode("twosComplement")) comparator_5 (
    .a(multiplexer_4_out), .b(Mem_WriteReg_num), .eq(comparator_5_eq));  // open: gt, lt
  Comparator #(.width(5), .mode("twosComplement")) comparator_6 (
    .a(Mem_WriteReg_num), .b(multiplexer_5_out), .eq(comparator_6_eq));  // open: gt, lt
  // Probe on \总周期数 
  // Probe on \无条件分支数 
  // Probe on \条件分支成功数 
  // Probe on \插入气泡数 
  // Probe on \LoadUse次数 
  or or_1 (bdc, B, \无条件 );
  \气泡IF_ID  \u_气泡if_id_1  (
    .Din22_2(mips_alu_1_result), .Din22_3(IR), .\传输状态In_表明当前传输数据有效 (1'b1), .Dout22_2(\气泡if_id_1_dout22_2 ),
    .Dout22_3(\气泡if_id_1_dout22_3 ), .\传输状态Out_表明当前传输数据有效 (\气泡if_id_1_传输状态out_表明当前传输数据有效 ),
    .\同步清零_气泡_高电平有效 (bdc), .CLK(CLK), .\使能端_低电平有效_stall_高电平有效 (and_8_out), .Din22(IF_PC), .Dout22(ID_PC));
  and and_4 (and_4_out, comparator_1_eq, ~comparator_3_eq);  // AND_Gate
  and and_5 (and_5_out, comparator_2_eq, ~comparator_4_eq);  // AND_Gate
  and and_6 (and_6_out, comparator_5_eq, ~comparator_3_eq);  // AND_Gate
  and and_7 (and_7_out, comparator_6_eq, ~comparator_4_eq);  // AND_Gate
  // Probe on IF_PC[11:0]
  // Probe on ID_PC[11:0]
  // Probe on EX_PC[11:0]
  and and_8 (and_8_out, \数据相关 , ~bdc);  // AND_Gate
  or or_2 (or_2_out, and_4_out, and_5_out);
  or or_3 (or_3_out, and_6_out, and_7_out);
  // Probe on M_PC[11:0]
  R_Not_Used r_not_used_1 (
    .OpCode(\气泡if_id_1_dout22_3 [31:26]), .Funct(\气泡if_id_1_dout22_3 [5:0]), .R2_Unused(R2_NotUsed),
    .R1_Unused(R1_NotUsed));
  Multiplexer #(.select(1), .width(5), .disabled("Z"), .enable("false")) multiplexer_6 (
    .in0(\气泡if_id_1_dout22_3 [25:21]), .in1(5'b00010), .out(multiplexer_6_out), .sel(\单周期硬布线控制器_1_syscall ));
  Multiplexer #(.select(1), .width(5), .disabled("Z"), .enable("false")) multiplexer_7 (
    .in0(\气泡if_id_1_dout22_3 [20:16]), .in1(\气泡if_id_1_dout22_3 [15:11]), .out(multiplexer_7_out),
    .sel(\单周期硬布线控制器_1_regdst ));
  and and_9 (Ex_Conflict, or_2_out, Ex_RegWrite);
  and and_10 (Mem_Conflict, or_3_out, Mem_RegWrite);
  // Probe on WB_PC[11:0]
  Multiplexer #(.select(1), .width(5), .disabled("Z"), .enable("false")) multiplexer_8 (
    .in0(multiplexer_6_out), .in1({5{1'b1}}), .out(R1_num), .sel(\单周期硬布线控制器_1_jr ));
  Multiplexer #(.select(1), .width(5), .disabled("Z"), .enable("false")) multiplexer_9 (
    .in0(\气泡if_id_1_dout22_3 [20:16]), .in1(5'b00100), .out(R2_num), .sel(\单周期硬布线控制器_1_syscall ));
  Multiplexer #(.select(1), .width(5), .disabled("Z"), .enable("false")) multiplexer_10 (
    .in0(multiplexer_7_out), .in1({5{1'b1}}), .out(multiplexer_10_out), .sel(\单周期硬布线控制器_1_jal ));
  assign bit_extender_1_out = {{16{1'b0}}, \气泡if_id_1_dout22_3 [15:0]};  // Bit_Extender bit_extender_1
  assign bit_extender_2_out = {{16{\气泡if_id_1_dout22_3 [15]}}, \气泡if_id_1_dout22_3 [15:0]};  // Bit_Extender bit_extender_2
  or or_4 (\数据相关 , Ex_Conflict, Mem_Conflict);
  \单周期硬布线控制器  \u_单周期硬布线控制器_1  (
    .Func(\气泡if_id_1_dout22_3 [5:0]), .OP(\气泡if_id_1_dout22_3 [31:26]), .ALU_OP(\单周期硬布线控制器_1_alu_op ),
    .MemToReg(\单周期硬布线控制器_1_memtoreg ), .MemWrite(\单周期硬布线控制器_1_memwrite ), .ALU_SRC(\单周期硬布线控制器_1_alu_src ),
    .RegWrite(\单周期硬布线控制器_1_regwrite ), .SysCALL(\单周期硬布线控制器_1_syscall ), .SignedExt(SignedExt),
    .RegDst(\单周期硬布线控制器_1_regdst ), .JR(\单周期硬布线控制器_1_jr ), .JMP(\单周期硬布线控制器_1_jmp ), .Beq(\单周期硬布线控制器_1_beq ),
    .JAL(\单周期硬布线控制器_1_jal ), .Bne(\单周期硬布线控制器_1_bne ));
  MIPS_Regifile mips_regifile_1 (
    .Din(RDin), .Clk(CLK), .R1(mips_regifile_1_r1), .R2(mips_regifile_1_r2), .WE(RegWrite), .W_num(W_num),
    .R1_num(R1_num), .R2_num(R2_num));
  Multiplexer #(.select(1), .width(32), .disabled("Z"), .enable("false")) multiplexer_11 (
    .in0(bit_extender_1_out), .in1(bit_extender_2_out), .out(multiplexer_11_out), .sel(SignedExt));
  Counter #(.width(16), .max('hffff), .ongoal("wrap"), .trigger("rising"), .behavior("old")) counter_1 (
    .Q(\总周期数 ), .clk(and_11_out));  // open: load, D, count, carry, clr, preset
  and and_11 (and_11_out, CLK, not_2_out);
  not not_2 (not_2_out, Halt);
  or or_5 (\无条件 , JMP, JAL, JR);
  or or_6 (or_6_out, bdc, Ex_Conflict, Mem_Conflict);
  Multiplexer #(.select(1), .width(32), .disabled("Z"), .enable("false")) multiplexer_12 (
    .in0(mips_regifile_1_r2), .in1(multiplexer_11_out), .out(multiplexer_12_out), .sel(\单周期硬布线控制器_1_alu_src ));
  Shifter #(.width(32), .shift("ll")) shifter_1 (.in(multiplexer_11_out), .\dist (5'b00010), .out(shifter_1_out));
  // Probe on \总周期数 
  \气泡ID_EX  \u_气泡id_ex_1  (
    .Din22_2(\气泡if_id_1_dout22_2 ), .Din22_3(shifter_1_out),
    .\传输状态In_表明当前传输数据有效 (\气泡if_id_1_传输状态out_表明当前传输数据有效 ), .Dout22_2(\气泡id_ex_1_dout22_2 ),
    .Dout22_3(\气泡id_ex_1_dout22_3 ), .\传输状态Out_表明当前传输数据有效 (\气泡id_ex_1_传输状态out_表明当前传输数据有效 ),
    .\同步清零_气泡_高电平有效 (or_6_out), .CLK(CLK), .Din22_4(\气泡if_id_1_dout22_3 [31:26]),
    .Dout22_4(\气泡id_ex_1_dout22_4 ), .Din22_6(\单周期硬布线控制器_1_beq ), .Dout22_6(\气泡id_ex_1_dout22_6 ),
    .Din22_7(\单周期硬布线控制器_1_bne ), .Dout22_7(\气泡id_ex_1_dout22_7 ), .Din22_8(\单周期硬布线控制器_1_syscall ),
    .Dout22_8(\气泡id_ex_1_dout22_8 ), .Din22_9(\单周期硬布线控制器_1_memtoreg ), .Dout22_9(\气泡id_ex_1_dout22_9 ),
    .Din22_10(\单周期硬布线控制器_1_memwrite ), .Dout22_10(\气泡id_ex_1_dout22_10 ), .Din22_11(\单周期硬布线控制器_1_jmp ),
    .Dout22_11(JMP), .Din22_12(\单周期硬布线控制器_1_jr ), .Dout22_12(JR), .Din22_13(\单周期硬布线控制器_1_jal ),
    .Dout22_13(JAL), .Din22_16(mips_regifile_1_r1), .Dout22_16(rs), .Din22_17(multiplexer_12_out),
    .Dout22_17(\气泡id_ex_1_dout22_17 ), .Din22_14(\单周期硬布线控制器_1_alu_op ), .Dout22_14(\气泡id_ex_1_dout22_14 ),
    .Din22_18(mips_regifile_1_r2), .Dout22_18(\气泡id_ex_1_dout22_18 ), .Din22_21(\气泡if_id_1_dout22_3 [10:6]),
    .Dout22_21(\气泡id_ex_1_dout22_21 ), .Din22_22(\气泡if_id_1_dout22_3 [5:0]),
    .Dout22_22(\气泡id_ex_1_dout22_22 ), .Din22_23(multiplexer_10_out), .Dout22_23(Ex_WriteReg_num),
    .Din22_5(\单周期硬布线控制器_1_regwrite ), .Dout22_5(Ex_RegWrite),
    .Din22_15({\气泡if_id_1_dout22_2 [31:28], \气泡if_id_1_dout22_3 [25:0], 2'b00}),
    .Dout22_15(\气泡id_ex_1_dout22_15 ), .Din22(ID_PC), .Dout22(EX_PC));  // open: 使能端_低电平有效_stall_高电平有效, Din22_20, Dout22_20, Din22_19, Dout22_19
  Counter #(.width(16), .max('hffff), .ongoal("wrap"), .trigger("falling"), .behavior("old")) counter_2 (
    .count(\无条件 ), .Q(\无条件分支数 ), .clk(and_12_out));  // open: load, D, carry, clr, preset
  and and_12 (and_12_out, CLK, not_3_out);
  not not_3 (not_3_out, Halt);
  Multiplexer #(.select(1), .width(5), .disabled("Z"), .enable("false")) multiplexer_13 (
    .in0(\气泡id_ex_1_dout22_21 ), .in1(rs[4:0]), .out(multiplexer_13_out), .sel(comparator_7_eq));
  Comparator #(.width(6), .mode("twosComplement")) comparator_7 (
    .a(\气泡id_ex_1_dout22_22 ), .b(6'b000111), .eq(comparator_7_eq));  // open: gt, lt
  Counter #(.width(16), .max('hffff), .ongoal("wrap"), .trigger("rising"), .behavior("old")) counter_3 (
    .count(B), .Q(\条件分支成功数 ), .clk(and_13_out));  // open: load, D, carry, clr, preset
  and and_13 (and_13_out, CLK, not_4_out);
  not not_4 (not_4_out, Halt);
  MIPS_ALU mips_alu_2 (
    .X(\气泡id_ex_1_dout22_2 ), .Y(\气泡id_ex_1_dout22_3 ), .AluOP(4'b0101), .Result(mips_alu_2_result),
    .shamt({5{1'b0}}));  // open: Equal, Result_2
  Comparator #(.width(6), .mode("twosComplement")) comparator_8 (
    .a(\气泡id_ex_1_dout22_4 ), .b(6'b000111), .eq(comparator_8_eq));  // open: gt, lt
  and and_14 (and_14_out, comparator_8_eq, comparator_9_gt);
  Comparator #(.width(32), .mode("twosComplement")) comparator_9 (
    .a(rs), .b({32{1'b0}}), .gt(comparator_9_gt));  // open: eq, lt
  and and_15 (and_15_out, \气泡id_ex_1_dout22_6 , mips_alu_3_equal);
  and and_16 (and_16_out, \气泡id_ex_1_dout22_7 , not_5_out);
  not not_5 (not_5_out, mips_alu_3_equal);
  MIPS_ALU mips_alu_3 (
    .X(rs), .Y(\气泡id_ex_1_dout22_17 ), .AluOP(\气泡id_ex_1_dout22_14 ), .Equal(mips_alu_3_equal),
    .Result(mips_alu_3_result), .shamt(multiplexer_13_out));  // open: Result_2
  or or_7 (B, and_14_out, and_15_out, and_16_out);
  and and_17 (and_17_out, \数据相关 , ~bdc);  // AND_Gate
  // Probe on mips_alu_3_result
  Counter #(.width(16), .max('hffff), .ongoal("wrap"), .trigger("rising"), .behavior("old")) counter_4 (
    .count(and_17_out), .Q(\插入气泡数 ), .clk(and_18_out));  // open: load, D, carry, clr, preset
  and and_18 (and_18_out, CLK, not_6_out);
  not not_6 (not_6_out, Halt);
  \气泡EX_MEM  \u_气泡ex_mem_1  (
    .Din22_8(JAL), .Din22_9(\气泡id_ex_1_dout22_8 ), .Din22_10(\气泡id_ex_1_dout22_9 ),
    .Din22_11(\气泡id_ex_1_dout22_10 ), .Din22_13(mips_alu_3_result), .Din22_14(\气泡id_ex_1_dout22_18 ),
    .\传输状态In_表明当前传输数据有效 (\气泡id_ex_1_传输状态out_表明当前传输数据有效 ), .Dout22_8(\气泡ex_mem_1_dout22_8 ),
    .Dout22_9(\气泡ex_mem_1_dout22_9 ), .Dout22_10(\气泡ex_mem_1_dout22_10 ), .Dout22_11(MemWrite),
    .Dout22_13(\气泡ex_mem_1_dout22_13 ), .Dout22_14(MDin),
    .\传输状态Out_表明当前传输数据有效 (\气泡ex_mem_1_传输状态out_表明当前传输数据有效 ), .CLK(CLK), .Din22_2(\气泡id_ex_1_dout22_4 ),
    .Dout22_2(\气泡ex_mem_1_dout22_2 ), .Din22_3(\气泡id_ex_1_dout22_2 ), .Dout22_3(\气泡ex_mem_1_dout22_3 ),
    .Din22_15(rs), .Dout22_15(\气泡ex_mem_1_dout22_15 ), .Din22_16(Ex_WriteReg_num),
    .Dout22_16(Mem_WriteReg_num), .Din22_4(Ex_RegWrite), .Dout22_4(Mem_RegWrite), .Din22(EX_PC), .Dout22(M_PC));  // open: Din22_5, Din22_6, Din22_7, Dout22_5, Dout22_6, Dout22_7, 同步清零_气泡_高电平有效, 使能端_低电平有效_stall_高电平有效, Din22_12, Dout22_12
  Multiplexer #(.select(1), .width(32), .disabled("Z"), .enable("false")) multiplexer_14 (
    .in0(multiplexer_15_out), .in1(PC_4), .out(RDin), .sel(\气泡mem_wb_1_dout22_10 ));
  // Probe on \气泡ex_mem_1_dout22_13 
  // Probe on MDin
  Comparator #(.width(32), .mode("twosComplement")) comparator_10 (
    .a(rsf), .b(32'h22), .eq(comparator_10_eq));  // open: gt, lt
  Multiplexer #(.select(1), .width(32), .disabled("Z"), .enable("false")) multiplexer_15 (
    .in0(multiplexer_16_out), .in1(bit_extender_3_out), .out(multiplexer_15_out), .sel(comparator_11_eq));
  Comparator #(.width(6), .mode("twosComplement")) comparator_11 (
    .a(OP), .b(6'b100000), .eq(comparator_11_eq));  // open: gt, lt
  not not_7 (not_7_out, comparator_10_eq);
  and and_19 (and_19_out, comparator_10_eq, Syscall);
  not not_8 (not_8_out, Halt);
  and and_20 (and_20_out, Syscall, not_7_out);
  Counter #(.width(1), .max('h1), .ongoal("wrap"), .trigger("rising"), .behavior("old")) counter_5 (
    .load(and_20_out), .D(and_20_out), .count(1'b0), .Q(Halt), .clk(CLK), .clr(Go));  // open: carry, preset
  Counter #(.width(32), .max('hffffffff), .ongoal("wrap"), .trigger("rising"), .behavior("old")) counter_6 (
    .load(and_19_out), .D(rt), .count(1'b0), .Q(LedData), .clk(CLK));  // open: carry, clr, preset
  \气泡MEM_WB  \u_气泡mem_wb_1  (
    .Din22_6(\气泡ex_mem_1_dout22_9 ), .Din22_7(\气泡ex_mem_1_dout22_10 ), .Din22_10(\气泡ex_mem_1_dout22_8 ),
    .Din22_11(\气泡ex_mem_1_dout22_13 [1:0]), .Din22_12(\气泡ex_mem_1_dout22_13 ), .Din22_13(ram_1_data),
    .\传输状态In_表明当前传输数据有效 (\气泡ex_mem_1_传输状态out_表明当前传输数据有效 ), .Dout22_6(Syscall),
    .Dout22_7(\气泡mem_wb_1_dout22_7 ), .Dout22_10(\气泡mem_wb_1_dout22_10 ), .Dout22_11(\气泡mem_wb_1_dout22_11 ),
    .Dout22_12(\气泡mem_wb_1_dout22_12 ), .Dout22_13(\气泡mem_wb_1_dout22_13 ), .CLK(CLK),
    .Din22_2(\气泡ex_mem_1_dout22_2 ), .Dout22_2(OP), .Din22_3(\气泡ex_mem_1_dout22_3 ), .Dout22_3(PC_4),
    .Din22_14(\气泡ex_mem_1_dout22_15 ), .Dout22_14(rsf), .Din22_15(Mem_WriteReg_num), .Dout22_15(W_num),
    .Din22_4(Mem_RegWrite), .Dout22_4(RegWrite), .Din22_16(MDin), .Dout22_16(rt), .Din22(M_PC), .Dout22(WB_PC));  // open: Din22_5, Din22_8, Din22_9, Dout22_5, Dout22_8, Dout22_9, 传输状态Out_表明当前传输数据有效, 同步清零_气泡_高电平有效, 使能端_低电平有效_stall_高电平有效
  RAM #(.addrWidth(10), .dataWidth(32), .bus("separate"), .Select("high")) ram_1 (
    .addr(\气泡ex_mem_1_dout22_13 [11:2]), .din(MDin), .data(ram_1_data), .str(MemWrite), .sel(not_8_out),
    .clk(CLK), .clr(RST));  // open: ld
  Shifter #(.width(32), .shift("lr")) shifter_2 (.in(multiplexer_16_out), .\dist (LB), .out(shifter_2_out));
  Multiplexer #(.select(1), .width(32), .disabled("Z"), .enable("false")) multiplexer_16 (
    .in0(\气泡mem_wb_1_dout22_12 ), .in1(\气泡mem_wb_1_dout22_13 ), .out(multiplexer_16_out),
    .sel(\气泡mem_wb_1_dout22_7 ));
  assign bit_extender_3_out = {{24{shifter_2_out[7]}}, shifter_2_out[7:0]};  // Bit_Extender bit_extender_3
  assign bit_extender_4_out = {{3{1'b0}}, \气泡mem_wb_1_dout22_11 };  // Bit_Extender bit_extender_4
  Multiplier #(.width(5)) multiplier_1 (.a(bit_extender_4_out), .b(5'b01000), .out(LB));  // open: cin, cout

  // Other names for the same wires on the sheet: MEM_PC[31:0] = M_PC

  // Notes on the sheet:
  //   中断源
  //   中断等待指示
  //   总复位信号应将除ROM以外所有存储组件全部清零
  //   数码管输出
  //   数码管输出应该用寄存器锁存，否则显示数据只能一闪而过
  //   指令存储器
  //   contents of rom_1 (hex, n*v repeats v):
  //   20110001 8000c05 20110001 20120002 20130003 8000c09 20110001 20120002 20130003 8000c0d 20110001
  //   20120002 20130003 8000c11 20110001 20120002 20130003 c000cb8 20100001 20110001 118fc0 112020
  //   20020022 c 118882 12200001 8000c15 112020 20020022 c 20110001 118880 112020 20020022 c 12200001
  //   8000c1f 20110001 118fc0 112020 20020022 c 1188c3 112020 20020022 c 118903 112020 20020022 c 118903
  //   112020 20020022 c 118903 112020 20020022 c 118903 112020 20020022 c 118903 112020 20020022 c 118903
  //   112020 20020022 c 118903 112020 20020022 c 20100001 109fc0 139fc3 8021 2012000c 24160003 26100001
  //   3210000f 20080008 20090001 139900 2709825 132020 20020022 c 1094022 1500fff9 22100001 2018000f
  //   2188024 108700 20080008 20090001 139902 2709825 132021 20020022 c 1094022 1500fff9 108702 2c9b022
  //   12c00001 8000c50 4020 1084027 84400 3508ffff 82021 20020022 c 2010ffff 20110000 ae300000 22100001
  //   22310004 ae300000 22100001 22310004 ae300000 22100001 22310004 ae300000 22100001 22310004 ae300000
  //   22100001 22310004 ae300000 22100001 22310004 ae300000 22100001 22310004 ae300000 22100001 22310004
  //   ae300000 22100001 22310004 ae300000 22100001 22310004 ae300000 22100001 22310004 ae300000 22100001
  //   22310004 ae300000 22100001 22310004 ae300000 22100001 22310004 ae300000 22100001 22310004 ae300000
  //   22100001 22310004 22100001 8020 2011003c 8e130000 8e340000 274402a 11000002 ae330000 ae140000
  //   2231fffc 1611fff8 102020 20020022 c 22100004 2011003c 1611fff2 20020032 c 20100000 22100001 102020
  //   20020022 c 22100002 102020 20020022 c 22100003 102020 20020022 c 22100004 102020 20020022 c 22100005
  //   102020 20020022 c 22100006 102020 20020022 c 22100007 102020 20020022 c 22100008 102020 20020022
  //   20020022 c 3e00008
  //   指令字
  //   OP
  //   Func
  //   rs
  //   rt
  //   rd
  //   流水调试日志用
  //   JMP
  //   JR
  //   OP
  //   Func
  //   Beq
  //   Bne
  //   MemToReg
  //   MemWrite
  //   AluOP
  //   AluSrcB
  //   RegWrite
  //   JAL
  //   RegDst
  //   Syscall
  //   为方便自动评测，需要输出流水线各段保存的PC值，注意是PC不是PC+4，另外ID段寄存器写入信息，Mem段内存写入信息也要输出
  //   BGTZ
  //   SRAV指令偏移地址
endmodule

module R_Not_Used (
  input  [5:0] OpCode,
  input  [5:0] Funct,
  output R1_Unused,
  output R2_Unused
);

  wire and_1_out, comparator_1_eq, comparator_2_eq, comparator_3_eq, comparator_4_eq, comparator_5_eq,
       comparator_6_eq, comparator_7_eq, comparator_8_eq, comparator_9_eq, comparator_10_eq,
       comparator_11_eq, comparator_12_eq, comparator_13_eq, comparator_14_eq, comparator_15_eq,
       comparator_16_eq, or_1_out, or_2_out, or_3_out;

  Comparator #(.width(6), .mode("twosComplement")) comparator_1 (
    .a(6'b000111), .b(OpCode), .eq(comparator_1_eq));  // open: gt, lt
  Comparator #(.width(6), .mode("twosComplement")) comparator_2 (
    .a(6'b001000), .b(Funct), .eq(comparator_2_eq));  // open: gt, lt
  Comparator #(.width(6), .mode("twosComplement")) comparator_3 (
    .a(6'b000011), .b(OpCode), .eq(comparator_3_eq));  // open: gt, lt
  Comparator #(.width(6), .mode("twosComplement")) comparator_4 (
    .a(6'b000010), .b(OpCode), .eq(comparator_4_eq));  // open: gt, lt
  Comparator #(.width(6), .mode("twosComplement")) comparator_5 (
    .a(OpCode), .b({6{1'b0}}), .eq(comparator_5_eq));  // open: gt, lt
  Comparator #(.width(6), .mode("twosComplement")) comparator_6 (
    .a(Funct), .b({6{1'b0}}), .eq(comparator_6_eq));  // open: gt, lt
  Comparator #(.width(6), .mode("twosComplement")) comparator_7 (
    .a(Funct), .b(6'b000011), .eq(comparator_7_eq));  // open: gt, lt
  Comparator #(.width(6), .mode("twosComplement")) comparator_8 (
    .a(Funct), .b(6'b000010), .eq(comparator_8_eq));  // open: gt, lt
  Comparator #(.width(6), .mode("twosComplement")) comparator_9 (
    .a(OpCode), .b(6'b101011), .eq(comparator_9_eq));  // open: gt, lt
  Comparator #(.width(6), .mode("twosComplement")) comparator_10 (
    .a(OpCode), .b(6'b001000), .eq(comparator_10_eq));  // open: gt, lt
  Comparator #(.width(6), .mode("twosComplement")) comparator_11 (
    .a(OpCode), .b(6'b001001), .eq(comparator_11_eq));  // open: gt, lt
  Comparator #(.width(6), .mode("twosComplement")) comparator_12 (
    .a(OpCode), .b(6'b001010), .eq(comparator_12_eq));  // open: gt, lt
  Comparator #(.width(6), .mode("twosComplement")) comparator_13 (
    .a(OpCode), .b(6'b001100), .eq(comparator_13_eq));  // open: gt, lt
  Comparator #(.width(6), .mode("twosComplement")) comparator_14 (
    .a(OpCode), .b(6'b001101), .eq(comparator_14_eq));  // open: gt, lt
  Comparator #(.width(6), .mode("twosComplement")) comparator_15 (
    .a(OpCode), .b(6'b100000), .eq(comparator_15_eq));  // open: gt, lt
  Comparator #(.width(6), .mode("twosComplement")) comparator_16 (
    .a(OpCode), .b(6'b100011), .eq(comparator_16_eq));  // open: gt, lt
  or or_1 (or_1_out, comparator_6_eq, comparator_7_eq, comparator_8_eq);
  or or_2 (or_2_out, comparator_10_eq, comparator_11_eq, comparator_12_eq, comparator_13_eq, comparator_14_eq, comparator_15_eq, comparator_16_eq);
  and and_1 (and_1_out, comparator_5_eq, or_1_out);
  or or_3 (or_3_out, comparator_2_eq, comparator_1_eq, comparator_4_eq, comparator_3_eq);
  or or_4 (R1_Unused, comparator_3_eq, comparator_4_eq, and_1_out, 1'b0);
  or or_5 (R2_Unused, or_3_out, or_2_out);
endmodule

module \气泡IF_ID  (
  input  \同步清零_气泡_高电平有效 ,
  input  [31:0] Din22,
  input  [31:0] Din22_2,
  input  [31:0] Din22_3,
  input  \传输状态In_表明当前传输数据有效 ,
  input  \使能端_低电平有效_stall_高电平有效 ,
  input  CLK,
  output [31:0] Dout22,
  output [31:0] Dout22_2,
  output [31:0] Dout22_3,
  output \传输状态Out_表明当前传输数据有效 
);

  wire multiplexer_4_out, not_1_out;
  wire [31:0] multiplexer_1_out, multiplexer_2_out, multiplexer_3_out;

  Multiplexer #(.select(1), .width(32), .disabled("Z"), .enable("false")) multiplexer_1 (
    .in0(Din22), .in1({32{1'b0}}), .out(multiplexer_1_out), .sel(\同步清零_气泡_高电平有效 ));
  Multiplexer #(.select(1), .width(32), .disabled("Z"), .enable("false")) multiplexer_2 (
    .in0(Din22_2), .in1({32{1'b0}}), .out(multiplexer_2_out), .sel(\同步清零_气泡_高电平有效 ));
  Multiplexer #(.select(1), .width(32), .disabled("Z"), .enable("false")) multiplexer_3 (
    .in0(Din22_3), .in1({32{1'b0}}), .out(multiplexer_3_out), .sel(\同步清零_气泡_高电平有效 ));
  Multiplexer #(.select(1), .width(1), .disabled("Z"), .enable("false")) multiplexer_4 (
    .in0(\传输状态In_表明当前传输数据有效 ), .in1(1'b0), .out(multiplexer_4_out), .sel(\同步清零_气泡_高电平有效 ));
  Pull_Resistor #(.pull(0)) pull_resistor_1 (.node(\同步清零_气泡_高电平有效 ));
  not not_1 (not_1_out, \使能端_低电平有效_stall_高电平有效 );
  Register #(.width(32), .trigger("rising"), .Select("low")) register_1 (
    .D(multiplexer_1_out), .en(not_1_out), .Q(Dout22), .clk(CLK));  // open: clr
  Register #(.width(32), .trigger("rising"), .Select("low")) register_2 (
    .D(multiplexer_2_out), .en(not_1_out), .Q(Dout22_2), .clk(CLK));  // open: clr
  Register #(.width(32), .trigger("rising"), .Select("low")) register_3 (
    .D(multiplexer_3_out), .en(not_1_out), .Q(Dout22_3), .clk(CLK));  // open: clr
  Register #(.width(1), .trigger("rising"), .Select("low")) register_4 (
    .D(multiplexer_4_out), .en(not_1_out), .Q(\传输状态Out_表明当前传输数据有效 ), .clk(CLK));  // open: clr
  Pull_Resistor #(.pull(0)) pull_resistor_2 (.node(not_1_out));

  // Notes on the sheet:
  //   同步清零_气泡_高电平有效: pull=down
  //   使能端_低电平有效_stall_高电平有效: pull=down
endmodule

module \气泡ID_EX  (
  input  \同步清零_气泡_高电平有效 ,
  input  [31:0] Din22,
  input  [31:0] Din22_2,
  input  [31:0] Din22_3,
  input  [5:0] Din22_4,
  input  Din22_5,
  input  Din22_6,
  input  Din22_7,
  input  Din22_8,
  input  Din22_9,
  input  Din22_10,
  input  Din22_11,
  input  Din22_12,
  input  Din22_13,
  input  [3:0] Din22_14,
  input  [31:0] Din22_15,
  input  [31:0] Din22_16,
  input  [31:0] Din22_17,
  input  [31:0] Din22_18,
  input  [31:0] Din22_19,
  input  Din22_20,
  input  [4:0] Din22_21,
  input  [5:0] Din22_22,
  input  [4:0] Din22_23,
  input  \传输状态In_表明当前传输数据有效 ,
  input  \使能端_低电平有效_stall_高电平有效 ,
  input  CLK,
  output [31:0] Dout22,
  output [31:0] Dout22_2,
  output [31:0] Dout22_3,
  output [5:0] Dout22_4,
  output Dout22_5,
  output Dout22_6,
  output Dout22_7,
  output Dout22_8,
  output Dout22_9,
  output Dout22_10,
  output Dout22_11,
  output Dout22_12,
  output Dout22_13,
  output [3:0] Dout22_14,
  output [31:0] Dout22_15,
  output [31:0] Dout22_16,
  output [31:0] Dout22_17,
  output [31:0] Dout22_18,
  output [31:0] Dout22_19,
  output Dout22_20,
  output [4:0] Dout22_21,
  output [5:0] Dout22_22,
  output [4:0] Dout22_23,
  output \传输状态Out_表明当前传输数据有效 
);

  wire multiplexer_5_out, multiplexer_6_out, multiplexer_7_out, multiplexer_8_out, multiplexer_9_out,
       multiplexer_10_out, multiplexer_11_out, multiplexer_12_out, multiplexer_13_out, multiplexer_20_out,
       multiplexer_24_out, pull_resistor_2_node;
  wire [3:0] multiplexer_14_out;
  wire [4:0] multiplexer_21_out, multiplexer_23_out;
  wire [5:0] multiplexer_4_out, multiplexer_22_out;
  wire [31:0] multiplexer_1_out, multiplexer_2_out, multiplexer_3_out, multiplexer_15_out,
       multiplexer_16_out, multiplexer_17_out, multiplexer_18_out, multiplexer_19_out;

  Multiplexer #(.select(1), .width(32), .disabled("Z"), .enable("false")) multiplexer_1 (
    .in0(Din22), .in1({32{1'b0}}), .out(multiplexer_1_out), .sel(\同步清零_气泡_高电平有效 ));
  Multiplexer #(.select(1), .width(32), .disabled("Z"), .enable("false")) multiplexer_2 (
    .in0(Din22_2), .in1({32{1'b0}}), .out(multiplexer_2_out), .sel(\同步清零_气泡_高电平有效 ));
  Multiplexer #(.select(1), .width(32), .disabled("Z"), .enable("false")) multiplexer_3 (
    .in0(Din22_3), .in1({32{1'b0}}), .out(multiplexer_3_out), .sel(\同步清零_气泡_高电平有效 ));
  Multiplexer #(.select(1), .width(6), .disabled("Z"), .enable("false")) multiplexer_4 (
    .in0(Din22_4), .in1({6{1'b0}}), .out(multiplexer_4_out), .sel(\同步清零_气泡_高电平有效 ));
  Multiplexer #(.select(1), .width(1), .disabled("Z"), .enable("false")) multiplexer_5 (
    .in0(Din22_5), .in1(1'b0), .out(multiplexer_5_out), .sel(\同步清零_气泡_高电平有效 ));
  Multiplexer #(.select(1), .width(1), .disabled("Z"), .enable("false")) multiplexer_6 (
    .in0(Din22_6), .in1(1'b0), .out(multiplexer_6_out), .sel(\同步清零_气泡_高电平有效 ));
  Multiplexer #(.select(1), .width(1), .disabled("Z"), .enable("false")) multiplexer_7 (
    .in0(Din22_7), .in1(1'b0), .out(multiplexer_7_out), .sel(\同步清零_气泡_高电平有效 ));
  Multiplexer #(.select(1), .width(1), .disabled("Z"), .enable("false")) multiplexer_8 (
    .in0(Din22_8), .in1(1'b0), .out(multiplexer_8_out), .sel(\同步清零_气泡_高电平有效 ));
  Multiplexer #(.select(1), .width(1), .disabled("Z"), .enable("false")) multiplexer_9 (
    .in0(Din22_9), .in1(1'b0), .out(multiplexer_9_out), .sel(\同步清零_气泡_高电平有效 ));
  Multiplexer #(.select(1), .width(1), .disabled("Z"), .enable("false")) multiplexer_10 (
    .in0(Din22_10), .in1(1'b0), .out(multiplexer_10_out), .sel(\同步清零_气泡_高电平有效 ));
  Multiplexer #(.select(1), .width(1), .disabled("Z"), .enable("false")) multiplexer_11 (
    .in0(Din22_11), .in1(1'b0), .out(multiplexer_11_out), .sel(\同步清零_气泡_高电平有效 ));
  Multiplexer #(.select(1), .width(1), .disabled("Z"), .enable("false")) multiplexer_12 (
    .in0(Din22_12), .in1(1'b0), .out(multiplexer_12_out), .sel(\同步清零_气泡_高电平有效 ));
  Multiplexer #(.select(1), .width(1), .disabled("Z"), .enable("false")) multiplexer_13 (
    .in0(Din22_13), .in1(1'b0), .out(multiplexer_13_out), .sel(\同步清零_气泡_高电平有效 ));
  Multiplexer #(.select(1), .width(4), .disabled("Z"), .enable("false")) multiplexer_14 (
    .in0(Din22_14), .in1(4'b0000), .out(multiplexer_14_out), .sel(\同步清零_气泡_高电平有效 ));
  Multiplexer #(.select(1), .width(32), .disabled("Z"), .enable("false")) multiplexer_15 (
    .in0(Din22_15), .in1({32{1'b0}}), .out(multiplexer_15_out), .sel(\同步清零_气泡_高电平有效 ));
  Multiplexer #(.select(1), .width(32), .disabled("Z"), .enable("false")) multiplexer_16 (
    .in0(Din22_16), .in1({32{1'b0}}), .out(multiplexer_16_out), .sel(\同步清零_气泡_高电平有效 ));
  Multiplexer #(.select(1), .width(32), .disabled("Z"), .enable("false")) multiplexer_17 (
    .in0(Din22_17), .in1({32{1'b0}}), .out(multiplexer_17_out), .sel(\同步清零_气泡_高电平有效 ));
  Multiplexer #(.select(1), .width(32), .disabled("Z"), .enable("false")) multiplexer_18 (
    .in0(Din22_18), .in1({32{1'b0}}), .out(multiplexer_18_out), .sel(\同步清零_气泡_高电平有效 ));
  Multiplexer #(.select(1), .width(32), .disabled("Z"), .enable("false")) multiplexer_19 (
    .in0(Din22_19), .in1({32{1'b0}}), .out(multiplexer_19_out), .sel(\同步清零_气泡_高电平有效 ));
  Multiplexer #(.select(1), .width(1), .disabled("Z"), .enable("false")) multiplexer_20 (
    .in0(Din22_20), .in1(1'b0), .out(multiplexer_20_out), .sel(\同步清零_气泡_高电平有效 ));
  Multiplexer #(.select(1), .width(5), .disabled("Z"), .enable("false")) multiplexer_21 (
    .in0(Din22_21), .in1({5{1'b0}}), .out(multiplexer_21_out), .sel(\同步清零_气泡_高电平有效 ));
  Multiplexer #(.select(1), .width(6), .disabled("Z"), .enable("false")) multiplexer_22 (
    .in0(Din22_22), .in1({6{1'b0}}), .out(multiplexer_22_out), .sel(\同步清零_气泡_高电平有效 ));
  Multiplexer #(.select(1), .width(5), .disabled("Z"), .enable("false")) multiplexer_23 (
    .in0(Din22_23), .in1({5{1'b0}}), .out(multiplexer_23_out), .sel(\同步清零_气泡_高电平有效 ));
  Multiplexer #(.select(1), .width(1), .disabled("Z"), .enable("false")) multiplexer_24 (
    .in0(\传输状态In_表明当前传输数据有效 ), .in1(1'b0), .out(multiplexer_24_out), .sel(\同步清零_气泡_高电平有效 ));
  Pull_Resistor #(.pull(0)) pull_resistor_1 (.node(\同步清零_气泡_高电平有效 ));
  Pull_Resistor #(.pull(0)) pull_resistor_2 (.node(pull_resistor_2_node));
  not not_1 (pull_resistor_2_node, \使能端_低电平有效_stall_高电平有效 );
  Register #(.width(32), .trigger("rising"), .Select("low")) register_1 (
    .D(multiplexer_1_out), .en(pull_resistor_2_node), .Q(Dout22), .clk(CLK));  // open: clr
  Register #(.width(32), .trigger("rising"), .Select("low")) register_2 (
    .D(multiplexer_2_out), .en(pull_resistor_2_node), .Q(Dout22_2), .clk(CLK));  // open: clr
  Register #(.width(32), .trigger("rising"), .Select("low")) register_3 (
    .D(multiplexer_3_out), .en(pull_resistor_2_node), .Q(Dout22_3), .clk(CLK));  // open: clr
  Register #(.width(6), .trigger("rising"), .Select("low")) register_4 (
    .D(multiplexer_4_out), .en(pull_resistor_2_node), .Q(Dout22_4), .clk(CLK));  // open: clr
  Register #(.width(1), .trigger("rising"), .Select("low")) register_5 (
    .D(multiplexer_5_out), .en(pull_resistor_2_node), .Q(Dout22_5), .clk(CLK));  // open: clr
  Register #(.width(1), .trigger("rising"), .Select("low")) register_6 (
    .D(multiplexer_6_out), .en(pull_resistor_2_node), .Q(Dout22_6), .clk(CLK));  // open: clr
  Register #(.width(1), .trigger("rising"), .Select("low")) register_7 (
    .D(multiplexer_7_out), .en(pull_resistor_2_node), .Q(Dout22_7), .clk(CLK));  // open: clr
  Register #(.width(1), .trigger("rising"), .Select("low")) register_8 (
    .D(multiplexer_8_out), .en(pull_resistor_2_node), .Q(Dout22_8), .clk(CLK));  // open: clr
  Register #(.width(1), .trigger("rising"), .Select("low")) register_9 (
    .D(multiplexer_9_out), .en(pull_resistor_2_node), .Q(Dout22_9), .clk(CLK));  // open: clr
  Register #(.width(1), .trigger("rising"), .Select("low")) register_10 (
    .D(multiplexer_10_out), .en(pull_resistor_2_node), .Q(Dout22_10), .clk(CLK));  // open: clr
  Register #(.width(1), .trigger("rising"), .Select("low")) register_11 (
    .D(multiplexer_11_out), .en(pull_resistor_2_node), .Q(Dout22_11), .clk(CLK));  // open: clr
  Register #(.width(1), .trigger("rising"), .Select("low")) register_12 (
    .D(multiplexer_12_out), .en(pull_resistor_2_node), .Q(Dout22_12), .clk(CLK));  // open: clr
  Register #(.width(1), .trigger("rising"), .Select("low")) register_13 (
    .D(multiplexer_13_out), .en(pull_resistor_2_node), .Q(Dout22_13), .clk(CLK));  // open: clr
  Register #(.width(4), .trigger("rising"), .Select("low")) register_14 (
    .D(multiplexer_14_out), .en(pull_resistor_2_node), .Q(Dout22_14), .clk(CLK));  // open: clr
  Register #(.width(32), .trigger("rising"), .Select("low")) register_15 (
    .D(multiplexer_15_out), .en(pull_resistor_2_node), .Q(Dout22_15), .clk(CLK));  // open: clr
  Register #(.width(32), .trigger("rising"), .Select("low")) register_16 (
    .D(multiplexer_16_out), .en(pull_resistor_2_node), .Q(Dout22_16), .clk(CLK));  // open: clr
  Register #(.width(32), .trigger("rising"), .Select("low")) register_17 (
    .D(multiplexer_17_out), .en(pull_resistor_2_node), .Q(Dout22_17), .clk(CLK));  // open: clr
  Register #(.width(32), .trigger("rising"), .Select("low")) register_18 (
    .D(multiplexer_18_out), .en(pull_resistor_2_node), .Q(Dout22_18), .clk(CLK));  // open: clr
  Register #(.width(32), .trigger("rising"), .Select("low")) register_19 (
    .D(multiplexer_19_out), .en(pull_resistor_2_node), .Q(Dout22_19), .clk(CLK));  // open: clr
  Register #(.width(1), .trigger("rising"), .Select("low")) register_20 (
    .D(multiplexer_20_out), .en(pull_resistor_2_node), .Q(Dout22_20), .clk(CLK));  // open: clr
  Register #(.width(5), .trigger("rising"), .Select("low")) register_21 (
    .D(multiplexer_21_out), .en(pull_resistor_2_node), .Q(Dout22_21), .clk(CLK));  // open: clr
  Register #(.width(6), .trigger("rising"), .Select("low")) register_22 (
    .D(multiplexer_22_out), .en(pull_resistor_2_node), .Q(Dout22_22), .clk(CLK));  // open: clr
  Register #(.width(5), .trigger("rising"), .Select("low")) register_23 (
    .D(multiplexer_23_out), .en(pull_resistor_2_node), .Q(Dout22_23), .clk(CLK));  // open: clr
  Register #(.width(1), .trigger("rising"), .Select("low")) register_24 (
    .D(multiplexer_24_out), .en(pull_resistor_2_node), .Q(\传输状态Out_表明当前传输数据有效 ), .clk(CLK));  // open: clr

  // Notes on the sheet:
  //   使能端_低电平有效_stall_高电平有效: pull=down
  //   同步清零_气泡_高电平有效: pull=down
endmodule

module \气泡EX_MEM  (
  input  \同步清零_气泡_高电平有效 ,
  input  [31:0] Din22,
  input  [5:0] Din22_2,
  input  [31:0] Din22_3,
  input  Din22_4,
  input  Din22_5,
  input  Din22_6,
  input  Din22_7,
  input  Din22_8,
  input  Din22_9,
  input  Din22_10,
  input  Din22_11,
  input  [31:0] Din22_12,
  input  [31:0] Din22_13,
  input  [31:0] Din22_14,
  input  [31:0] Din22_15,
  input  [4:0] Din22_16,
  input  \传输状态In_表明当前传输数据有效 ,
  input  \使能端_低电平有效_stall_高电平有效 ,
  input  CLK,
  output [31:0] Dout22,
  output [5:0] Dout22_2,
  output [31:0] Dout22_3,
  output Dout22_4,
  output Dout22_5,
  output Dout22_6,
  output Dout22_7,
  output Dout22_8,
  output Dout22_9,
  output Dout22_10,
  output Dout22_11,
  output [31:0] Dout22_12,
  output [31:0] Dout22_13,
  output [31:0] Dout22_14,
  output [31:0] Dout22_15,
  output [4:0] Dout22_16,
  output \传输状态Out_表明当前传输数据有效 
);

  wire multiplexer_4_out, multiplexer_5_out, multiplexer_6_out, multiplexer_7_out, multiplexer_8_out,
       multiplexer_9_out, multiplexer_10_out, multiplexer_11_out, multiplexer_17_out, pull_resistor_2_node;
  wire [4:0] multiplexer_16_out;
  wire [5:0] multiplexer_2_out;
  wire [31:0] multiplexer_1_out, multiplexer_3_out, multiplexer_12_out, multiplexer_13_out,
       multiplexer_14_out, multiplexer_15_out;

  Multiplexer #(.select(1), .width(32), .disabled("Z"), .enable("false")) multiplexer_1 (
    .in0(Din22), .in1({32{1'b0}}), .out(multiplexer_1_out), .sel(\同步清零_气泡_高电平有效 ));
  Multiplexer #(.select(1), .width(6), .disabled("Z"), .enable("false")) multiplexer_2 (
    .in0(Din22_2), .in1({6{1'b0}}), .out(multiplexer_2_out), .sel(\同步清零_气泡_高电平有效 ));
  Multiplexer #(.select(1), .width(32), .disabled("Z"), .enable("false")) multiplexer_3 (
    .in0(Din22_3), .in1({32{1'b0}}), .out(multiplexer_3_out), .sel(\同步清零_气泡_高电平有效 ));
  Multiplexer #(.select(1), .width(1), .disabled("Z"), .enable("false")) multiplexer_4 (
    .in0(Din22_4), .in1(1'b0), .out(multiplexer_4_out), .sel(\同步清零_气泡_高电平有效 ));
  Multiplexer #(.select(1), .width(1), .disabled("Z"), .enable("false")) multiplexer_5 (
    .in0(Din22_5), .in1(1'b0), .out(multiplexer_5_out), .sel(\同步清零_气泡_高电平有效 ));
  Multiplexer #(.select(1), .width(1), .disabled("Z"), .enable("false")) multiplexer_6 (
    .in0(Din22_6), .in1(1'b0), .out(multiplexer_6_out), .sel(\同步清零_气泡_高电平有效 ));
  Multiplexer #(.select(1), .width(1), .disabled("Z"), .enable("false")) multiplexer_7 (
    .in0(Din22_7), .in1(1'b0), .out(multiplexer_7_out), .sel(\同步清零_气泡_高电平有效 ));
  Multiplexer #(.select(1), .width(1), .disabled("Z"), .enable("false")) multiplexer_8 (
    .in0(Din22_8), .in1(1'b0), .out(multiplexer_8_out), .sel(\同步清零_气泡_高电平有效 ));
  Multiplexer #(.select(1), .width(1), .disabled("Z"), .enable("false")) multiplexer_9 (
    .in0(Din22_9), .in1(1'b0), .out(multiplexer_9_out), .sel(\同步清零_气泡_高电平有效 ));
  Multiplexer #(.select(1), .width(1), .disabled("Z"), .enable("false")) multiplexer_10 (
    .in0(Din22_10), .in1(1'b0), .out(multiplexer_10_out), .sel(\同步清零_气泡_高电平有效 ));
  Multiplexer #(.select(1), .width(1), .disabled("Z"), .enable("false")) multiplexer_11 (
    .in0(Din22_11), .in1(1'b0), .out(multiplexer_11_out), .sel(\同步清零_气泡_高电平有效 ));
  Multiplexer #(.select(1), .width(32), .disabled("Z"), .enable("false")) multiplexer_12 (
    .in0(Din22_12), .in1({32{1'b0}}), .out(multiplexer_12_out), .sel(\同步清零_气泡_高电平有效 ));
  Multiplexer #(.select(1), .width(32), .disabled("Z"), .enable("false")) multiplexer_13 (
    .in0(Din22_13), .in1({32{1'b0}}), .out(multiplexer_13_out), .sel(\同步清零_气泡_高电平有效 ));
  Multiplexer #(.select(1), .width(32), .disabled("Z"), .enable("false")) multiplexer_14 (
    .in0(Din22_14), .in1({32{1'b0}}), .out(multiplexer_14_out), .sel(\同步清零_气泡_高电平有效 ));
  Multiplexer #(.select(1), .width(32), .disabled("Z"), .enable("false")) multiplexer_15 (
    .in0(Din22_15), .in1({32{1'b0}}), .out(multiplexer_15_out), .sel(\同步清零_气泡_高电平有效 ));
  Multiplexer #(.select(1), .width(5), .disabled("Z"), .enable("false")) multiplexer_16 (
    .in0(Din22_16), .in1({5{1'b0}}), .out(multiplexer_16_out), .sel(\同步清零_气泡_高电平有效 ));
  Multiplexer #(.select(1), .width(1), .disabled("Z"), .enable("false")) multiplexer_17 (
    .in0(\传输状态In_表明当前传输数据有效 ), .in1(1'b0), .out(multiplexer_17_out), .sel(\同步清零_气泡_高电平有效 ));
  Pull_Resistor #(.pull(0)) pull_resistor_1 (.node(\同步清零_气泡_高电平有效 ));
  Pull_Resistor #(.pull(0)) pull_resistor_2 (.node(pull_resistor_2_node));
  not not_1 (pull_resistor_2_node, \使能端_低电平有效_stall_高电平有效 );
  Register #(.width(32), .trigger("rising"), .Select("low")) register_1 (
    .D(multiplexer_1_out), .en(pull_resistor_2_node), .Q(Dout22), .clk(CLK));  // open: clr
  Register #(.width(6), .trigger("rising"), .Select("low")) register_2 (
    .D(multiplexer_2_out), .en(pull_resistor_2_node), .Q(Dout22_2), .clk(CLK));  // open: clr
  Register #(.width(32), .trigger("rising"), .Select("low")) register_3 (
    .D(multiplexer_3_out), .en(pull_resistor_2_node), .Q(Dout22_3), .clk(CLK));  // open: clr
  Register #(.width(1), .trigger("rising"), .Select("low")) register_4 (
    .D(multiplexer_4_out), .en(pull_resistor_2_node), .Q(Dout22_4), .clk(CLK));  // open: clr
  Register #(.width(1), .trigger("rising"), .Select("low")) register_5 (
    .D(multiplexer_5_out), .en(pull_resistor_2_node), .Q(Dout22_5), .clk(CLK));  // open: clr
  Register #(.width(1), .trigger("rising"), .Select("low")) register_6 (
    .D(multiplexer_6_out), .en(pull_resistor_2_node), .Q(Dout22_6), .clk(CLK));  // open: clr
  Register #(.width(1), .trigger("rising"), .Select("low")) register_7 (
    .D(multiplexer_7_out), .en(pull_resistor_2_node), .Q(Dout22_7), .clk(CLK));  // open: clr
  Register #(.width(1), .trigger("rising"), .Select("low")) register_8 (
    .D(multiplexer_8_out), .en(pull_resistor_2_node), .Q(Dout22_8), .clk(CLK));  // open: clr
  Register #(.width(1), .trigger("rising"), .Select("low")) register_9 (
    .D(multiplexer_9_out), .en(pull_resistor_2_node), .Q(Dout22_9), .clk(CLK));  // open: clr
  Register #(.width(1), .trigger("rising"), .Select("low")) register_10 (
    .D(multiplexer_10_out), .en(pull_resistor_2_node), .Q(Dout22_10), .clk(CLK));  // open: clr
  Register #(.width(1), .trigger("rising"), .Select("low")) register_11 (
    .D(multiplexer_11_out), .en(pull_resistor_2_node), .Q(Dout22_11), .clk(CLK));  // open: clr
  Register #(.width(32), .trigger("rising"), .Select("low")) register_12 (
    .D(multiplexer_12_out), .en(pull_resistor_2_node), .Q(Dout22_12), .clk(CLK));  // open: clr
  Register #(.width(32), .trigger("rising"), .Select("low")) register_13 (
    .D(multiplexer_13_out), .en(pull_resistor_2_node), .Q(Dout22_13), .clk(CLK));  // open: clr
  Register #(.width(32), .trigger("rising"), .Select("low")) register_14 (
    .D(multiplexer_14_out), .en(pull_resistor_2_node), .Q(Dout22_14), .clk(CLK));  // open: clr
  Register #(.width(32), .trigger("rising"), .Select("low")) register_15 (
    .D(multiplexer_15_out), .en(pull_resistor_2_node), .Q(Dout22_15), .clk(CLK));  // open: clr
  Register #(.width(5), .trigger("rising"), .Select("low")) register_16 (
    .D(multiplexer_16_out), .en(pull_resistor_2_node), .Q(Dout22_16), .clk(CLK));  // open: clr
  Register #(.width(1), .trigger("rising"), .Select("low")) register_17 (
    .D(multiplexer_17_out), .en(pull_resistor_2_node), .Q(\传输状态Out_表明当前传输数据有效 ), .clk(CLK));  // open: clr

  // Notes on the sheet:
  //   同步清零_气泡_高电平有效: pull=down
  //   使能端_低电平有效_stall_高电平有效: pull=down
endmodule

module \气泡MEM_WB  (
  input  \同步清零_气泡_高电平有效 ,
  input  [31:0] Din22,
  input  [5:0] Din22_2,
  input  [31:0] Din22_3,
  input  Din22_4,
  input  Din22_5,
  input  Din22_6,
  input  Din22_7,
  input  Din22_8,
  input  Din22_9,
  input  Din22_10,
  input  [1:0] Din22_11,
  input  [31:0] Din22_12,
  input  [31:0] Din22_13,
  input  [31:0] Din22_14,
  input  [4:0] Din22_15,
  input  [31:0] Din22_16,
  input  \传输状态In_表明当前传输数据有效 ,
  input  \使能端_低电平有效_stall_高电平有效 ,
  input  CLK,
  output [31:0] Dout22,
  output [5:0] Dout22_2,
  output [31:0] Dout22_3,
  output Dout22_4,
  output Dout22_5,
  output Dout22_6,
  output Dout22_7,
  output Dout22_8,
  output Dout22_9,
  output Dout22_10,
  output [1:0] Dout22_11,
  output [31:0] Dout22_12,
  output [31:0] Dout22_13,
  output [31:0] Dout22_14,
  output [4:0] Dout22_15,
  output [31:0] Dout22_16,
  output \传输状态Out_表明当前传输数据有效 
);

  wire multiplexer_4_out, multiplexer_5_out, multiplexer_6_out, multiplexer_7_out, multiplexer_8_out,
       multiplexer_9_out, multiplexer_10_out, multiplexer_17_out, pull_resistor_2_node;
  wire [1:0] multiplexer_11_out;
  wire [4:0] multiplexer_15_out;
  wire [5:0] multiplexer_2_out;
  wire [31:0] multiplexer_1_out, multiplexer_3_out, multiplexer_12_out, multiplexer_13_out,
       multiplexer_14_out, multiplexer_16_out;

  Multiplexer #(.select(1), .width(32), .disabled("Z"), .enable("false")) multiplexer_1 (
    .in0(Din22), .in1({32{1'b0}}), .out(multiplexer_1_out), .sel(\同步清零_气泡_高电平有效 ));
  Multiplexer #(.select(1), .width(6), .disabled("Z"), .enable("false")) multiplexer_2 (
    .in0(Din22_2), .in1({6{1'b0}}), .out(multiplexer_2_out), .sel(\同步清零_气泡_高电平有效 ));
  Multiplexer #(.select(1), .width(32), .disabled("Z"), .enable("false")) multiplexer_3 (
    .in0(Din22_3), .in1({32{1'b0}}), .out(multiplexer_3_out), .sel(\同步清零_气泡_高电平有效 ));
  Multiplexer #(.select(1), .width(1), .disabled("Z"), .enable("false")) multiplexer_4 (
    .in0(Din22_4), .in1(1'b0), .out(multiplexer_4_out), .sel(\同步清零_气泡_高电平有效 ));
  Multiplexer #(.select(1), .width(1), .disabled("Z"), .enable("false")) multiplexer_5 (
    .in0(Din22_5), .in1(1'b0), .out(multiplexer_5_out), .sel(\同步清零_气泡_高电平有效 ));
  Multiplexer #(.select(1), .width(1), .disabled("Z"), .enable("false")) multiplexer_6 (
    .in0(Din22_6), .in1(1'b0), .out(multiplexer_6_out), .sel(\同步清零_气泡_高电平有效 ));
  Multiplexer #(.select(1), .width(1), .disabled("Z"), .enable("false")) multiplexer_7 (
    .in0(Din22_7), .in1(1'b0), .out(multiplexer_7_out), .sel(\同步清零_气泡_高电平有效 ));
  Multiplexer #(.select(1), .width(1), .disabled("Z"), .enable("false")) multiplexer_8 (
    .in0(Din22_8), .in1(1'b0), .out(multiplexer_8_out), .sel(\同步清零_气泡_高电平有效 ));
  Multiplexer #(.select(1), .width(1), .disabled("Z"), .enable("false")) multiplexer_9 (
    .in0(Din22_9), .in1(1'b0), .out(multiplexer_9_out), .sel(\同步清零_气泡_高电平有效 ));
  Multiplexer #(.select(1), .width(1), .disabled("Z"), .enable("false")) multiplexer_10 (
    .in0(Din22_10), .in1(1'b0), .out(multiplexer_10_out), .sel(\同步清零_气泡_高电平有效 ));
  Multiplexer #(.select(1), .width(2), .disabled("Z"), .enable("false")) multiplexer_11 (
    .in0(Din22_11), .in1(2'b00), .out(multiplexer_11_out), .sel(\同步清零_气泡_高电平有效 ));
  Multiplexer #(.select(1), .width(32), .disabled("Z"), .enable("false")) multiplexer_12 (
    .in0(Din22_12), .in1({32{1'b0}}), .out(multiplexer_12_out), .sel(\同步清零_气泡_高电平有效 ));
  Multiplexer #(.select(1), .width(32), .disabled("Z"), .enable("false")) multiplexer_13 (
    .in0(Din22_13), .in1({32{1'b0}}), .out(multiplexer_13_out), .sel(\同步清零_气泡_高电平有效 ));
  Multiplexer #(.select(1), .width(32), .disabled("Z"), .enable("false")) multiplexer_14 (
    .in0(Din22_14), .in1({32{1'b0}}), .out(multiplexer_14_out), .sel(\同步清零_气泡_高电平有效 ));
  Multiplexer #(.select(1), .width(5), .disabled("Z"), .enable("false")) multiplexer_15 (
    .in0(Din22_15), .in1({5{1'b0}}), .out(multiplexer_15_out), .sel(\同步清零_气泡_高电平有效 ));
  Multiplexer #(.select(1), .width(32), .disabled("Z"), .enable("false")) multiplexer_16 (
    .in0(Din22_16), .in1({32{1'b0}}), .out(multiplexer_16_out), .sel(\同步清零_气泡_高电平有效 ));
  Multiplexer #(.select(1), .width(1), .disabled("Z"), .enable("false")) multiplexer_17 (
    .in0(\传输状态In_表明当前传输数据有效 ), .in1(1'b0), .out(multiplexer_17_out), .sel(\同步清零_气泡_高电平有效 ));
  Pull_Resistor #(.pull(0)) pull_resistor_1 (.node(\同步清零_气泡_高电平有效 ));
  Pull_Resistor #(.pull(0)) pull_resistor_2 (.node(pull_resistor_2_node));
  not not_1 (pull_resistor_2_node, \使能端_低电平有效_stall_高电平有效 );
  Register #(.width(32), .trigger("rising"), .Select("low")) register_1 (
    .D(multiplexer_1_out), .en(pull_resistor_2_node), .Q(Dout22), .clk(CLK));  // open: clr
  Register #(.width(6), .trigger("rising"), .Select("low")) register_2 (
    .D(multiplexer_2_out), .en(pull_resistor_2_node), .Q(Dout22_2), .clk(CLK));  // open: clr
  Register #(.width(32), .trigger("rising"), .Select("low")) register_3 (
    .D(multiplexer_3_out), .en(pull_resistor_2_node), .Q(Dout22_3), .clk(CLK));  // open: clr
  Register #(.width(1), .trigger("rising"), .Select("low")) register_4 (
    .D(multiplexer_4_out), .en(pull_resistor_2_node), .Q(Dout22_4), .clk(CLK));  // open: clr
  Register #(.width(1), .trigger("rising"), .Select("low")) register_5 (
    .D(multiplexer_5_out), .en(pull_resistor_2_node), .Q(Dout22_5), .clk(CLK));  // open: clr
  Register #(.width(1), .trigger("rising"), .Select("low")) register_6 (
    .D(multiplexer_6_out), .en(pull_resistor_2_node), .Q(Dout22_6), .clk(CLK));  // open: clr
  Register #(.width(1), .trigger("rising"), .Select("low")) register_7 (
    .D(multiplexer_7_out), .en(pull_resistor_2_node), .Q(Dout22_7), .clk(CLK));  // open: clr
  Register #(.width(1), .trigger("rising"), .Select("low")) register_8 (
    .D(multiplexer_8_out), .en(pull_resistor_2_node), .Q(Dout22_8), .clk(CLK));  // open: clr
  Register #(.width(1), .trigger("rising"), .Select("low")) register_9 (
    .D(multiplexer_9_out), .en(pull_resistor_2_node), .Q(Dout22_9), .clk(CLK));  // open: clr
  Register #(.width(1), .trigger("rising"), .Select("low")) register_10 (
    .D(multiplexer_10_out), .en(pull_resistor_2_node), .Q(Dout22_10), .clk(CLK));  // open: clr
  Register #(.width(2), .trigger("rising"), .Select("low")) register_11 (
    .D(multiplexer_11_out), .en(pull_resistor_2_node), .Q(Dout22_11), .clk(CLK));  // open: clr
  Register #(.width(32), .trigger("rising"), .Select("low")) register_12 (
    .D(multiplexer_12_out), .en(pull_resistor_2_node), .Q(Dout22_12), .clk(pull_resistor_2_node));  // open: clr
  Register #(.width(32), .trigger("rising"), .Select("low")) register_13 (
    .D(multiplexer_13_out), .en(pull_resistor_2_node), .Q(Dout22_13), .clk(CLK));  // open: clr
  Register #(.width(32), .trigger("rising"), .Select("low")) register_14 (
    .D(multiplexer_14_out), .en(pull_resistor_2_node), .Q(Dout22_14), .clk(CLK));  // open: clr
  Register #(.width(5), .trigger("rising"), .Select("low")) register_15 (
    .D(multiplexer_15_out), .en(pull_resistor_2_node), .Q(Dout22_15), .clk(CLK));  // open: clr
  Register #(.width(32), .trigger("rising"), .Select("low")) register_16 (
    .D(multiplexer_16_out), .en(pull_resistor_2_node), .Q(Dout22_16), .clk(CLK));  // open: clr
  Register #(.width(1), .trigger("rising"), .Select("low")) register_17 (
    .D(multiplexer_17_out), .en(pull_resistor_2_node), .Q(\传输状态Out_表明当前传输数据有效 ), .clk(CLK));  // open: clr

  // Notes on the sheet:
  //   同步清零_气泡_高电平有效: pull=down
  //   使能端_低电平有效_stall_高电平有效: pull=down
endmodule

module \重定向流水线  (
  output RegWrite,
  output MemWrite,
  output [31:0] IF_PC,
  output [31:0] ID_PC,
  output [31:0] EX_PC,
  output [31:0] M_PC,
  output [31:0] WB_PC,
  output [31:0] RDin,
  output [31:0] MDin,
  output [31:0] LedData
);

  wire and_1_out, and_2_out, and_3_out, and_4_out, and_5_out, and_6_out, and_7_out, and_8_out, and_9_out,
       and_10_out, and_11_out, and_12_out, and_15_out, and_20_out, and_21_out, and_22_out, and_23_out,
       and_24_out, and_25_out, and_28_out, and_29_out, and_30_out, and_31_out, and_32_out, and_34_out,
       and_35_out, B, Choose_WB, CLK, comparator_1_eq, comparator_2_eq, comparator_3_eq, comparator_4_eq,
       comparator_5_eq, comparator_6_eq, comparator_7_eq, comparator_8_eq, comparator_9_eq, comparator_10_eq,
       comparator_11_eq, comparator_12_gt, comparator_13_eq, comparator_14_eq, comparator_15_eq, DataIMM,
       Ex_Conflict, Ex_RegWrite, Go, Halt, IR1, IR2, IR3, JAL, JAL_WB, JMP, JR, loaduse, Mem_Conflict,
       Mem_RegWrite, mips_alu_3_equal, not_1_out, not_2_out, not_3_out, not_4_out, not_5_out, not_6_out,
       not_7_out, not_8_out, not_9_out, not_10_out, not_11_out, not_12_out, not_13_out, or_3_out, or_4_out,
       or_6_out, or_7_out, or_8_out, or_9_out, or_11_out, or_12_out, R1_Ex, R1_Mem, R1_Unused, R2_Ex, R2_Mem,
       R2_Unused, RST, SignedExt, Syscall, undriven, W1, W2, W3, WB_R1, WB_R2, \单周期硬布线控制器_1_alu_src ,
       \单周期硬布线控制器_1_beq , \单周期硬布线控制器_1_bne , \单周期硬布线控制器_1_jal , \单周期硬布线控制器_1_jmp , \单周期硬布线控制器_1_jr ,
       \单周期硬布线控制器_1_memtoreg , \单周期硬布线控制器_1_memwrite , \单周期硬布线控制器_1_regdst , \单周期硬布线控制器_1_regwrite ,
       \单周期硬布线控制器_1_syscall , \数据相关 , \无条件 , \气泡 , \气泡ex_mem_1_dout22_8 , \气泡ex_mem_1_dout22_9 ,
       \气泡ex_mem_1_dout22_10 , \气泡ex_mem_1_传输状态out_表明当前传输数据有效 , \气泡id_ex_1_dout22_6 , \气泡id_ex_1_dout22_7 ,
       \气泡id_ex_1_dout22_8 , \气泡id_ex_1_dout22_9 , \气泡id_ex_1_dout22_10 , \气泡id_ex_1_dout22_20 ,
       \气泡id_ex_1_传输状态out_表明当前传输数据有效 , \气泡if_id_1_传输状态out_表明当前传输数据有效 ;
  wire [1:0] f1_2_q, f2_q, forward1, forward2, \气泡mem_wb_1_dout22_11 ;
  wire [3:0] \单周期硬布线控制器_1_alu_op , \气泡id_ex_1_dout22_14 ;
  wire [4:0] bit_extender_4_out, Ex_WriteReg_num, LB, Mem_WriteReg_num, multiplexer_4_out, multiplexer_5_out,
       multiplexer_6_out, multiplexer_8_out, multiplexer_9_out, multiplexer_13_out, R1_num, R2_num, W_num,
       \气泡id_ex_1_dout22_21 ;
  wire [5:0] OP, OP_Ex, OP_Mem, \气泡id_ex_1_dout22_22 ;
  wire [15:0] \LoadUse次数 , \总周期数 , \插入气泡数 , \无条件分支数 , \条件分支成功数 ;
  wire [31:0] ALU_Result1, ALU_Result2, bit_extender_1_out, bit_extender_2_out, bit_extender_3_out,
       Composition, IR, Mem_FinalData, Mem_ReadData, mips_alu_1_result, mips_alu_3_result,
       mips_regifile_1_r1, mips_regifile_1_r2, multiplexer_1_out, multiplexer_2_out, multiplexer_3_out,
       multiplexer_11_out, multiplexer_12_out, multiplexer_15_out, multiplexer_16_out, multiplexer_18_out,
       New_ad, PC_4, ram_1_data, RD1, RD2, rd2_t, rs, rsf, rt, shifter_1_out, shifter_2_out,
       \气泡ex_mem_1_dout22_3 , \气泡ex_mem_1_dout22_15 , \气泡id_ex_1_dout22_2 , \气泡id_ex_1_dout22_3 ,
       \气泡id_ex_1_dout22_18 , \气泡id_ex_1_dout22_19 , \气泡if_id_1_dout22_2 , \气泡if_id_1_dout22_3 ;

  Button \u_总复位  (.out(RST));
  Button _1 (.out(IR1));
  Button _2 (.out(IR2));
  Button _3 (.out(IR3));
  Counter #(.width(16), .max('hffff), .ongoal("wrap"), .trigger("rising"), .behavior("old")) counter_1 (
    .Q(\总周期数 ), .clk(and_1_out));  // open: load, D, count, carry, clr, preset
  and and_1 (and_1_out, CLK, not_1_out);
  not not_1 (not_1_out, Halt);
  Button \u_继续运行  (.out(Go));
  LED #(.active("true")) led_1 (.in(W1));
  LED #(.active("true")) led_2 (.in(W2));
  LED #(.active("true")) led_3 (.in(W3));
  not not_2 (not_2_out, JR);
  // Probe on New_ad
  Hex_Digit_Display hex_digit_display_1 (.value(LedData[31:28]));  // open: dp
  Counter #(.width(16), .max('hffff), .ongoal("wrap"), .trigger("falling"), .behavior("old")) counter_2 (
    .count(\无条件 ), .Q(\无条件分支数 ), .clk(and_2_out));  // open: load, D, carry, clr, preset
  and and_2 (and_2_out, CLK, not_3_out);
  not not_3 (not_3_out, Halt);
  and and_3 (and_3_out, JMP, not_2_out);
  Multiplexer #(.select(1), .width(32), .disabled("Z"), .enable("false")) multiplexer_1 (
    .in0(multiplexer_2_out), .in1(Composition), .out(multiplexer_1_out), .sel(and_3_out));
  Multiplexer #(.select(1), .width(32), .disabled("Z"), .enable("false")) multiplexer_2 (
    .in0(multiplexer_3_out), .in1(rs), .out(multiplexer_2_out), .sel(JR));
  Multiplexer #(.select(1), .width(32), .disabled("Z"), .enable("false")) multiplexer_3 (
    .in0(mips_alu_1_result), .in1(New_ad), .out(multiplexer_3_out), .sel(B));
  and and_4 (and_4_out, ~Halt, ~and_5_out);  // AND_Gate
  Multiplexer #(.select(1), .width(5), .disabled("Z"), .enable("false")) multiplexer_4 (
    .in0(R1_num), .in1({5{1'b0}}), .out(multiplexer_4_out), .sel(R1_Unused));
  Multiplexer #(.select(1), .width(5), .disabled("Z"), .enable("false")) multiplexer_5 (
    .in0(R2_num), .in1({5{1'b0}}), .out(multiplexer_5_out), .sel(R2_Unused));
  Hex_Digit_Display hex_digit_display_2 (.value(LedData[23:20]));  // open: dp
  Hex_Digit_Display hex_digit_display_3 (.value(LedData[27:24]));  // open: dp
  Register #(.width(32), .trigger("rising"), .Select("low")) PC (
    .D(multiplexer_1_out), .en(and_4_out), .Q(IF_PC), .clk(CLK), .clr(RST));
  // Probe on IF_PC
  and and_5 (and_5_out, ~\气泡 , loaduse);  // AND_Gate
  Hex_Digit_Display hex_digit_display_4 (.value(LedData[19:16]));  // open: dp
  Hex_Digit_Display hex_digit_display_5 (.value(LedData[15:12]));  // open: dp
  Counter #(.width(16), .max('hffff), .ongoal("wrap"), .trigger("rising"), .behavior("old")) counter_3 (
    .count(B), .Q(\条件分支成功数 ), .clk(and_6_out));  // open: load, D, carry, clr, preset
  and and_6 (and_6_out, CLK, not_4_out);
  not not_4 (not_4_out, Halt);
  Hex_Digit_Display hex_digit_display_6 (.value(LedData[11:8]));  // open: dp
  Hex_Digit_Display hex_digit_display_7 (.value(LedData[7:4]));  // open: dp
  Clock #(.highDuration(1), .lowDuration(1)) clock_1 (.out(CLK));
  Hex_Digit_Display hex_digit_display_8 (.value(LedData[3:0]));  // open: dp
  MIPS_ALU mips_alu_1 (
    .X(IF_PC), .Y(32'h4), .AluOP(4'b0101), .Result(mips_alu_1_result));  // open: Equal, Result_2, shamt
  ROM #(.addrWidth(10), .dataWidth(32), .Select("high")) rom_1 (.addr(IF_PC[11:2]), .data(IR));
  and and_7 (and_7_out, CLK, not_5_out);
  not not_5 (not_5_out, Halt);
  Comparator #(.width(5), .mode("twosComplement")) comparator_1 (
    .a(multiplexer_4_out), .b(Ex_WriteReg_num), .eq(comparator_1_eq));  // open: gt, lt
  Comparator #(.width(5), .mode("twosComplement")) comparator_2 (
    .a(Ex_WriteReg_num), .b(multiplexer_5_out), .eq(comparator_2_eq));  // open: gt, lt
  Comparator #(.width(5), .mode("twosComplement")) comparator_3 (
    .a(multiplexer_4_out), .b({5{1'b0}}), .eq(comparator_3_eq));  // open: gt, lt
  Comparator #(.width(5), .mode("twosComplement")) comparator_4 (
    .a(multiplexer_5_out), .b({5{1'b0}}), .eq(comparator_4_eq));  // open: gt, lt
  Comparator #(.width(5), .mode("twosComplement")) comparator_5 (
    .a(multiplexer_4_out), .b(Mem_WriteReg_num), .eq(comparator_5_eq));  // open: gt, lt
  Comparator #(.width(5), .mode("twosComplement")) comparator_6 (
    .a(Mem_WriteReg_num), .b(multiplexer_5_out), .eq(comparator_6_eq));  // open: gt, lt
  or or_1 (\气泡 , B, \无条件 );
  \气泡IF_ID  \u_气泡if_id_1  (
    .Din22_2(mips_alu_1_result), .Din22_3(IR), .\传输状态In_表明当前传输数据有效 (1'b1), .Dout22_2(\气泡if_id_1_dout22_2 ),
    .Dout22_3(\气泡if_id_1_dout22_3 ), .\传输状态Out_表明当前传输数据有效 (\气泡if_id_1_传输状态out_表明当前传输数据有效 ),
    .\同步清零_气泡_高电平有效 (\气泡 ), .CLK(and_7_out), .\使能端_低电平有效_stall_高电平有效 (and_8_out), .Din22(IF_PC),
    .Dout22(ID_PC));
  and and_8 (and_8_out, ~\气泡 , loaduse);  // AND_Gate
  and and_9 (and_9_out, comparator_1_eq, ~comparator_3_eq);  // AND_Gate
  and and_10 (and_10_out, comparator_2_eq, ~comparator_4_eq);  // AND_Gate
  and and_11 (and_11_out, comparator_5_eq, ~comparator_3_eq);  // AND_Gate
  and and_12 (and_12_out, comparator_6_eq, ~comparator_4_eq);  // AND_Gate
  // Probe on \总周期数 
  // Probe on \无条件分支数 
  // Probe on \条件分支成功数 
  // Probe on \插入气泡数 
  // Probe on \LoadUse次数 
  and and_13 (R2_Ex, and_10_out, Ex_RegWrite);
  // Probe on IF_PC[11:0]
  or or_2 (\无条件 , JMP, JAL, JR);
  and and_14 (R1_Ex, Ex_RegWrite, and_9_out);
  or or_3 (or_3_out, and_9_out, and_10_out);
  and and_15 (and_15_out, and_11_out, Mem_RegWrite);
  or or_4 (or_4_out, and_11_out, and_12_out);
  and and_16 (R2_Mem, Mem_RegWrite, ~R2_Ex, and_12_out);  // AND_Gate
  // Probe on ID_PC[11:0]
  // Probe on EX_PC[11:0]
  R_Not_Used r_not_used_1 (
    .OpCode(\气泡if_id_1_dout22_3 [31:26]), .Funct(\气泡if_id_1_dout22_3 [5:0]), .R2_Unused(R2_Unused),
    .R1_Unused(R1_Unused));
  Multiplexer #(.select(1), .width(5), .disabled("Z"), .enable("false")) multiplexer_6 (
    .in0(\气泡if_id_1_dout22_3 [25:21]), .in1(5'b00010), .out(multiplexer_6_out), .sel(\单周期硬布线控制器_1_syscall ));
  Multiplexer #(.select(1), .width(5), .disabled("Z"), .enable("false")) multiplexer_7 (
    .in0(multiplexer_6_out), .in1({5{1'b1}}), .out(R1_num), .sel(\单周期硬布线控制器_1_jr ));
  Multiplexer #(.select(1), .width(5), .disabled("Z"), .enable("false")) multiplexer_8 (
    .in0(\气泡if_id_1_dout22_3 [20:16]), .in1(\气泡if_id_1_dout22_3 [15:11]), .out(multiplexer_8_out),
    .sel(\单周期硬布线控制器_1_regdst ));
  Multiplexer #(.select(1), .width(5), .disabled("Z"), .enable("false")) multiplexer_9 (
    .in0(multiplexer_8_out), .in1({5{1'b1}}), .out(multiplexer_9_out), .sel(\单周期硬布线控制器_1_jal ));
  and and_17 (Ex_Conflict, or_3_out, Ex_RegWrite);
  and and_18 (Mem_Conflict, or_4_out, Mem_RegWrite);
  // Probe on M_PC[11:0]
  Comparator #(.width(32), .mode("twosComplement")) comparator_7 (
    .a(rsf), .b(32'h22), .eq(comparator_7_eq));  // open: gt, lt
  \单周期硬布线控制器  \u_单周期硬布线控制器_1  (
    .Func(\气泡if_id_1_dout22_3 [5:0]), .OP(\气泡if_id_1_dout22_3 [31:26]), .ALU_OP(\单周期硬布线控制器_1_alu_op ),
    .MemToReg(\单周期硬布线控制器_1_memtoreg ), .MemWrite(\单周期硬布线控制器_1_memwrite ), .ALU_SRC(\单周期硬布线控制器_1_alu_src ),
    .RegWrite(\单周期硬布线控制器_1_regwrite ), .SysCALL(\单周期硬布线控制器_1_syscall ), .SignedExt(SignedExt),
    .RegDst(\单周期硬布线控制器_1_regdst ), .JR(\单周期硬布线控制器_1_jr ), .JMP(\单周期硬布线控制器_1_jmp ), .Beq(\单周期硬布线控制器_1_beq ),
    .JAL(\单周期硬布线控制器_1_jal ), .Bne(\单周期硬布线控制器_1_bne ));
  Multiplexer #(.select(1), .width(5), .disabled("Z"), .enable("false")) multiplexer_10 (
    .in0(\气泡if_id_1_dout22_3 [20:16]), .in1(5'b00100), .out(R2_num), .sel(\单周期硬布线控制器_1_syscall ));
  // Probe on RDin
  assign bit_extender_1_out = {{16{1'b0}}, \气泡if_id_1_dout22_3 [15:0]};  // Bit_Extender bit_extender_1
  assign bit_extender_2_out = {{16{\气泡if_id_1_dout22_3 [15]}}, \气泡if_id_1_dout22_3 [15:0]};  // Bit_Extender bit_extender_2
  or or_5 (\数据相关 , Ex_Conflict, Mem_Conflict);
  and and_19 (R1_Mem, ~R1_Ex, and_15_out);  // AND_Gate
  // Probe on WB_PC[11:0]
  and and_20 (and_20_out, Syscall, not_6_out);
  not not_6 (not_6_out, comparator_7_eq);
  and and_21 (and_21_out, comparator_7_eq, Syscall);
  Multiplexer #(.select(1), .width(32), .disabled("Z"), .enable("false")) multiplexer_11 (
    .in0(bit_extender_1_out), .in1(bit_extender_2_out), .out(multiplexer_11_out), .sel(SignedExt));
  Counter #(.width(1), .max('h1), .ongoal("wrap"), .trigger("rising"), .behavior("old")) counter_4 (
    .load(and_20_out), .D(and_20_out), .count(1'b0), .Q(Halt), .clk(CLK), .clr(Go), .preset(undriven));  // open: carry
  Counter #(.width(32), .max('hffffffff), .ongoal("wrap"), .trigger("rising"), .behavior("old")) counter_5 (
    .load(and_21_out), .D(rt), .count(1'b0), .Q(LedData), .clk(and_22_out));  // open: carry, clr, preset
  and and_22 (and_22_out, CLK, not_7_out);
  not not_7 (not_7_out, Halt);
  MIPS_Regifile mips_regifile_1 (
    .Din(RDin), .Clk(CLK), .R1(mips_regifile_1_r1), .R2(mips_regifile_1_r2), .WE(RegWrite), .W_num(W_num),
    .R1_num(R1_num), .R2_num(R2_num));
  // Probe on mips_regifile_1_r2
  Multiplexer #(.select(1), .width(32), .disabled("Z"), .enable("false")) multiplexer_12 (
    .in0(mips_regifile_1_r2), .in1(multiplexer_11_out), .out(multiplexer_12_out), .sel(\单周期硬布线控制器_1_alu_src ));
  Shifter #(.width(32), .shift("ll")) shifter_1 (.in(multiplexer_11_out), .\dist (5'b00010), .out(shifter_1_out));
  assign forward1 = not_8_out ? 2'b00 : 2'bz;  // Controlled_Buffer controlled_buffer_1
  not not_8 (not_8_out, or_6_out);
  or or_6 (or_6_out, R1_Ex, R1_Mem, WB_R1);
  assign forward1 = and_23_out ? 2'b01 : 2'bz;  // Controlled_Buffer controlled_buffer_2
  and and_23 (and_23_out, R1_Ex, ~WB_R1);  // AND_Gate
  assign forward1 = and_24_out ? 2'b10 : 2'bz;  // Controlled_Buffer controlled_buffer_3
  and and_24 (and_24_out, R1_Mem, ~WB_R1);  // AND_Gate
  assign forward1 = WB_R1 ? 2'b11 : 2'bz;  // Controlled_Buffer controlled_buffer_4
  Comparator #(.width(6), .mode("twosComplement")) comparator_8 (
    .a(OP_Mem), .b(6'b100011), .eq(comparator_8_eq));  // open: gt, lt
  Comparator #(.width(6), .mode("twosComplement")) comparator_9 (
    .a(OP_Mem), .b(6'b100000), .eq(comparator_9_eq));  // open: gt, lt
  or or_7 (or_7_out, \气泡 , loaduse);
  \气泡ID_EX  \u_气泡id_ex_1  (
    .Din22_2(\气泡if_id_1_dout22_2 ), .Din22_3(shifter_1_out),
    .\传输状态In_表明当前传输数据有效 (\气泡if_id_1_传输状态out_表明当前传输数据有效 ), .Dout22_2(\气泡id_ex_1_dout22_2 ),
    .Dout22_3(\气泡id_ex_1_dout22_3 ), .\传输状态Out_表明当前传输数据有效 (\气泡id_ex_1_传输状态out_表明当前传输数据有效 ),
    .\同步清零_气泡_高电平有效 (or_7_out), .CLK(and_7_out), .Din22_4(\气泡if_id_1_dout22_3 [31:26]), .Dout22_4(OP_Ex),
    .Din22_6(\单周期硬布线控制器_1_beq ), .Dout22_6(\气泡id_ex_1_dout22_6 ), .Din22_7(\单周期硬布线控制器_1_bne ),
    .Dout22_7(\气泡id_ex_1_dout22_7 ), .Din22_8(\单周期硬布线控制器_1_syscall ), .Dout22_8(\气泡id_ex_1_dout22_8 ),
    .Din22_9(\单周期硬布线控制器_1_memtoreg ), .Dout22_9(\气泡id_ex_1_dout22_9 ), .Din22_10(\单周期硬布线控制器_1_memwrite ),
    .Dout22_10(\气泡id_ex_1_dout22_10 ), .Din22_11(\单周期硬布线控制器_1_jmp ), .Dout22_11(JMP),
    .Din22_12(\单周期硬布线控制器_1_jr ), .Dout22_12(JR), .Din22_13(\单周期硬布线控制器_1_jal ), .Dout22_13(JAL),
    .Din22_16(mips_regifile_1_r1), .Dout22_16(RD1), .Din22_17(multiplexer_12_out), .Dout22_17(RD2),
    .Din22_14(\单周期硬布线控制器_1_alu_op ), .Dout22_14(\气泡id_ex_1_dout22_14 ), .Din22_18(mips_regifile_1_r2),
    .Dout22_18(\气泡id_ex_1_dout22_18 ), .Din22_21(\气泡if_id_1_dout22_3 [10:6]),
    .Dout22_21(\气泡id_ex_1_dout22_21 ), .Din22_22(\气泡if_id_1_dout22_3 [5:0]),
    .Dout22_22(\气泡id_ex_1_dout22_22 ), .Din22_23(multiplexer_9_out), .Dout22_23(Ex_WriteReg_num),
    .Din22_5(\单周期硬布线控制器_1_regwrite ), .Dout22_5(Ex_RegWrite),
    .Din22_15({\气泡if_id_1_dout22_2 [31:28], \气泡if_id_1_dout22_3 [25:0], 2'b00}), .Dout22_15(Composition),
    .Din22(ID_PC), .Dout22(EX_PC), .Din22_20(\单周期硬布线控制器_1_alu_src ), .Dout22_20(\气泡id_ex_1_dout22_20 ),
    .Din22_19(multiplexer_11_out), .Dout22_19(\气泡id_ex_1_dout22_19 ));  // open: 使能端_低电平有效_stall_高电平有效
  // Probe on forward1
  or or_8 (or_8_out, comparator_8_eq, comparator_9_eq);
  Counter #(.width(16), .max('hffff), .ongoal("wrap"), .trigger("rising"), .behavior("old")) counter_6 (
    .count(loaduse), .Q(\LoadUse次数 ), .clk(and_25_out));  // open: load, D, carry, clr, preset
  and and_25 (and_25_out, CLK, not_9_out);
  not not_9 (not_9_out, Halt);
  // Probe on RD1
  and and_26 (WB_R2, R2_Mem, or_8_out);
  and and_27 (WB_R1, R1_Mem, or_8_out);
  Multiplexer #(.select(1), .width(5), .disabled("Z"), .enable("false")) multiplexer_13 (
    .in0(\气泡id_ex_1_dout22_21 ), .in1(rs[4:0]), .out(multiplexer_13_out), .sel(comparator_10_eq));
  Comparator #(.width(6), .mode("twosComplement")) comparator_10 (
    .a(\气泡id_ex_1_dout22_22 ), .b(6'b000111), .eq(comparator_10_eq));  // open: gt, lt
  Multiplexer #(.select(1), .width(32), .disabled("Z"), .enable("false")) multiplexer_14 (
    .in0(Mem_FinalData), .in1(PC_4), .out(RDin), .sel(JAL_WB));
  Comparator #(.width(6), .mode("twosComplement")) comparator_11 (
    .a(OP_Ex), .b(6'b000111), .eq(comparator_11_eq));  // open: gt, lt
  and and_28 (and_28_out, comparator_11_eq, comparator_12_gt);
  Comparator #(.width(32), .mode("twosComplement")) comparator_12 (
    .a(rs), .b({32{1'b0}}), .gt(comparator_12_gt));  // open: eq, lt
  and and_29 (and_29_out, \气泡id_ex_1_dout22_6 , mips_alu_3_equal);
  and and_30 (and_30_out, \气泡id_ex_1_dout22_7 , not_10_out);
  not not_10 (not_10_out, mips_alu_3_equal);
  // Probe on rs
  Multiplexer #(.select(1), .width(32), .disabled("Z"), .enable("false")) multiplexer_15 (
    .in0(rd2_t), .in1(\气泡id_ex_1_dout22_19 ), .out(multiplexer_15_out), .sel(\气泡id_ex_1_dout22_20 ));
  Multiplexer #(.select(1), .width(32), .disabled("Z"), .enable("false")) multiplexer_16 (
    .in0(\气泡id_ex_1_dout22_18 ), .in1(rd2_t), .out(multiplexer_16_out), .sel(DataIMM));
  assign forward2 = not_11_out ? 2'b00 : 2'bz;  // Controlled_Buffer controlled_buffer_5
  not not_11 (not_11_out, or_9_out);
  or or_9 (or_9_out, R2_Ex, R2_Mem, WB_R2);
  assign forward2 = and_31_out ? 2'b01 : 2'bz;  // Controlled_Buffer controlled_buffer_6
  and and_31 (and_31_out, R2_Ex, ~WB_R2);  // AND_Gate
  assign forward2 = and_32_out ? 2'b10 : 2'bz;  // Controlled_Buffer controlled_buffer_7
  and and_32 (and_32_out, R2_Mem, ~WB_R2);  // AND_Gate
  assign forward2 = WB_R2 ? 2'b11 : 2'bz;  // Controlled_Buffer controlled_buffer_8
  // Probe on Mem_FinalData
  MIPS_ALU mips_alu_2 (
    .X(\气泡id_ex_1_dout22_2 ), .Y(\气泡id_ex_1_dout22_3 ), .AluOP(4'b0101), .Result(New_ad));  // open: Equal, Result_2, shamt
  or or_10 (B, and_28_out, and_29_out, and_30_out);
  // Probe on multiplexer_15_out
  // Probe on forward2
  Multiplexer #(.select(1), .width(32), .disabled("Z"), .enable("false")) multiplexer_17 (
    .in0(multiplexer_18_out), .in1(bit_extender_3_out), .out(Mem_FinalData), .sel(comparator_13_eq));
  Comparator #(.width(6), .mode("twosComplement")) comparator_13 (
    .a(OP), .b(6'b100000), .eq(comparator_13_eq));  // open: gt, lt
  // Probe on mips_alu_3_result
  MIPS_ALU mips_alu_3 (
    .X(rs), .Y(multiplexer_15_out), .AluOP(\气泡id_ex_1_dout22_14 ), .Equal(mips_alu_3_equal),
    .Result(mips_alu_3_result), .shamt(multiplexer_13_out));  // open: Result_2
  Register #(.width(1), .trigger("rising"), .Select("low")) f1 (
    .D(or_9_out), .Q(DataIMM), .clk(CLK), .clr(1'b0));  // open: en
  Comparator #(.width(6), .mode("twosComplement")) comparator_14 (
    .a(OP_Ex), .b(6'b100011), .eq(comparator_14_eq));  // open: gt, lt
  Comparator #(.width(6), .mode("twosComplement")) comparator_15 (
    .a(OP_Ex), .b(6'b100000), .eq(comparator_15_eq));  // open: gt, lt
  Multiplexer #(.select(1), .width(32), .disabled("Z"), .enable("false")) multiplexer_18 (
    .in0(ALU_Result2), .in1(Mem_ReadData), .out(multiplexer_18_out), .sel(Choose_WB));
  \气泡EX_MEM  \u_气泡ex_mem_1  (
    .Din22_8(JAL), .Din22_9(\气泡id_ex_1_dout22_8 ), .Din22_10(\气泡id_ex_1_dout22_9 ),
    .Din22_11(\气泡id_ex_1_dout22_10 ), .Din22_13(mips_alu_3_result), .Din22_14(multiplexer_16_out),
    .\传输状态In_表明当前传输数据有效 (\气泡id_ex_1_传输状态out_表明当前传输数据有效 ), .Dout22_8(\气泡ex_mem_1_dout22_8 ),
    .Dout22_9(\气泡ex_mem_1_dout22_9 ), .Dout22_10(\气泡ex_mem_1_dout22_10 ), .Dout22_11(MemWrite),
    .Dout22_13(ALU_Result1), .Dout22_14(MDin), .\传输状态Out_表明当前传输数据有效 (\气泡ex_mem_1_传输状态out_表明当前传输数据有效 ),
    .CLK(and_7_out), .Din22_2(OP_Ex), .Dout22_2(OP_Mem), .Din22_3(\气泡id_ex_1_dout22_2 ),
    .Dout22_3(\气泡ex_mem_1_dout22_3 ), .Din22_15(rs), .Dout22_15(\气泡ex_mem_1_dout22_15 ),
    .Din22_16(Ex_WriteReg_num), .Dout22_16(Mem_WriteReg_num), .Din22_4(Ex_RegWrite), .Dout22_4(Mem_RegWrite),
    .Din22(EX_PC), .Dout22(M_PC));  // open: Din22_5, Din22_6, Din22_7, Dout22_5, Dout22_6, Dout22_7, 同步清零_气泡_高电平有效, 使能端_低电平有效_stall_高电平有效, Din22_12, Dout22_12
  or or_11 (or_11_out, comparator_14_eq, comparator_15_eq);
  and and_33 (loaduse, or_11_out, or_12_out);
  or or_12 (or_12_out, R1_Ex, R2_Ex);
  Shifter #(.width(32), .shift("lr")) shifter_2 (.in(multiplexer_18_out), .\dist (LB), .out(shifter_2_out));
  // Probe on ALU_Result1
  // Probe on MDin
  Multiplexer #(.select(2), .width(32), .disabled("Z"), .enable("false")) multiplexer_19 (
    .in0(RD1), .in1(ALU_Result1), .in2(ALU_Result2), .in3(Mem_FinalData), .out(rs), .sel(f1_2_q));
  Register #(.width(2), .trigger("rising"), .Select("low")) f1_2 (
    .D(forward1), .Q(f1_2_q), .clk(CLK), .clr(Go));  // open: en
  assign bit_extender_3_out = {{24{shifter_2_out[7]}}, shifter_2_out[7:0]};  // Bit_Extender bit_extender_3
  // Probe on rs
  // Probe on Mem_FinalData
  not not_12 (not_12_out, Halt);
  and and_34 (and_34_out, \气泡 , ~loaduse);  // AND_Gate
  RAM #(.addrWidth(10), .dataWidth(32), .bus("separate"), .Select("high")) ram_1 (
    .addr(ALU_Result1[11:2]), .din(MDin), .data(ram_1_data), .str(MemWrite), .sel(not_12_out), .clk(CLK),
    .clr(RST));  // open: ld
  Multiplexer #(.select(2), .width(32), .disabled("Z"), .enable("false")) multiplexer_20 (
    .in0(RD2), .in1(ALU_Result1), .in2(ALU_Result2), .in3(Mem_FinalData), .out(rd2_t), .sel(f2_q));
  Register #(.width(2), .trigger("rising"), .Select("low")) f2 (
    .D(forward2), .Q(f2_q), .clk(CLK), .clr(Go));  // open: en
  Counter #(.width(16), .max('hffff), .ongoal("wrap"), .trigger("rising"), .behavior("old")) counter_7 (
    .count(and_34_out), .Q(\插入气泡数 ), .clk(and_35_out));  // open: load, D, carry, clr, preset
  and and_35 (and_35_out, CLK, not_13_out);
  not not_13 (not_13_out, Halt);
  \气泡MEM_WB  \u_气泡mem_wb_1  (
    .Din22_6(\气泡ex_mem_1_dout22_9 ), .Din22_7(\气泡ex_mem_1_dout22_10 ), .Din22_10(\气泡ex_mem_1_dout22_8 ),
    .Din22_11(ALU_Result1[1:0]), .Din22_12(ALU_Result1), .Din22_13(ram_1_data),
    .\传输状态In_表明当前传输数据有效 (\气泡ex_mem_1_传输状态out_表明当前传输数据有效 ), .Dout22_6(Syscall), .Dout22_7(Choose_WB),
    .Dout22_10(JAL_WB), .Dout22_11(\气泡mem_wb_1_dout22_11 ), .Dout22_12(ALU_Result2),
    .Dout22_13(Mem_ReadData), .CLK(and_7_out), .Din22_2(OP_Mem), .Dout22_2(OP),
    .Din22_3(\气泡ex_mem_1_dout22_3 ), .Dout22_3(PC_4), .Din22_14(\气泡ex_mem_1_dout22_15 ), .Dout22_14(rsf),
    .Din22_15(Mem_WriteReg_num), .Dout22_15(W_num), .Din22_4(Mem_RegWrite), .Dout22_4(RegWrite),
    .Din22_16(MDin), .Dout22_16(rt), .Din22(M_PC), .Dout22(WB_PC));  // open: Din22_5, Din22_8, Din22_9, Dout22_5, Dout22_8, Dout22_9, 传输状态Out_表明当前传输数据有效, 同步清零_气泡_高电平有效, 使能端_低电平有效_stall_高电平有效
  // Probe on rd2_t
  // Probe on Mem_FinalData
  assign bit_extender_4_out = {{3{1'b0}}, \气泡mem_wb_1_dout22_11 };  // Bit_Extender bit_extender_4
  Multiplier #(.width(5)) multiplier_1 (.a(bit_extender_4_out), .b(5'b01000), .out(LB));  // open: cin, cout

  // Other names for the same wires on the sheet: MEM_PC[31:0] = M_PC

  // Notes on the sheet:
  //   中断源
  //   中断等待指示
  //   总复位信号应将除ROM以外所有存储组件全部清零
  //   数码管输出
  //   数码管输出应该用寄存器锁存，否则显示数据只能一闪而过
  //   指令存储器
  //   指令字
  //   contents of rom_1 (hex, n*v repeats v):
  //   20110001 8000c05 20110001 20120002 20130003 8000c09 20110001 20120002 20130003 8000c0d 20110001
  //   20120002 20130003 8000c11 20110001 20120002 20130003 c000d12 20100001 20110001 118fc0 112020
  //   20020022 c 118882 12200001 8000c15 112020 20020022 c 20110001 118880 112020 20020022 c 12200001
  //   8000c1f 20110001 118fc0 112020 20020022 c 1188c3 112020 20020022 c 118903 112020 20020022 c 118903
  //   112020 20020022 c 118903 112020 20020022 c 118903 112020 20020022 c 118903 112020 20020022 c 118903
  //   112020 20020022 c 118903 112020 20020022 c 20100001 109fc0 139fc3 8021 2012000c 24160003 26100001
  //   3210000f 20080008 20090001 139900 2709825 132020 20020022 c 1094022 1500fff9 22100001 2018000f
  //   2188024 108700 20080008 20090001 139902 2709825 132021 20020022 c 1094022 1500fff9 108702 2c9b022
  //   12c00001 8000c50 4020 1084027 84400 3508ffff 82021 20020022 c 2010ffff 20110000 ae300000 22100001
  //   22310004 ae300000 22100001 22310004 ae300000 22100001 22310004 ae300000 22100001 22310004 ae300000
  //   22100001 22310004 ae300000 22100001 22310004 ae300000 22100001 22310004 ae300000 22100001 22310004
  //   ae300000 22100001 22310004 ae300000 22100001 22310004 ae300000 22100001 22310004 ae300000 22100001
  //   22310004 ae300000 22100001 22310004 ae300000 22100001 22310004 ae300000 22100001 22310004 ae300000
  //   22100001 22310004 22100001 8020 2011003c 8e130000 8e340000 274402a 11000002 ae330000 ae140000
  //   2231fffc 1611fff8 102020 20020022 c 22100004 2011003c 1611fff2 20020032 c 5*0 20080001 20090003
  //   20110876 118d00 112020 20020022 c 200b0008 1118807 1318807 112020 20020022 c 216bffff 1560fff9
  //   2002000a c 5*0 2008ffff 20117777 112020 20020022 c 200b0010 2288826 112020 20020022 c 216bffff
  //   1560fffa 2002000a c 5*0 20090000 200b0010 34118483 20120404 118c00 129400 36318281 22520404 ad310000
  //   2328820 21290004 216bffff 1560fffb 200b0020 20090000 81310000 112020 20020022 c 21290001 216bffff
  //   1560fff9 2002000a c 5*0 2011000f 112020 20020022 c 2231ffff 1e20fffb 2002000a c 20020032 c 5*0
  //   20100000 22100001 102020 20020022 c 22100002 102020 20020022 c 22100003 102020 20020022 c 22100004
  //   102020 20020022 c 22100005 102020 20020022 c 22100006 102020 20020022 c 22100007 102020 20020022 c
  //   22100008 102020 20020022 20020022 c 3e00008
  //   OP
  //   Func
  //   rs
  //   rt
  //   rd
  //   JMP
  //   JR
  //   OP
  //   Func
  //   流水调试日志用
  //   Beq
  //   Bne
  //   MemToReg
  //   MemWrite
  //   AluOP
  //   AluSrcB
  //   RegWrite
  //   JAL
  //   RegDst
  //   Syscall
  //   SRAV指令偏移地址
  //   BGTZ
  //   为方便自动评测，需要输出流水线各段保存的PC值，注意是PC不是PC+4，另外ID段寄存器写入信息，Mem段内存写入信息也要输出
endmodule

module \中断按键参考电路  (
  input  in_1,
  input  in_2,
  input  \同步清零信号 ,
  output \与中断屏蔽位与 ,
  output out_5
);

  wire and_1_out, d_ff_1_q, or_2_out;

  or or_1 (out_5, \与中断屏蔽位与 , d_ff_1_q);
  D_Flip_Flop #(.trigger("rising"), .Pre_Clr_Positions("LEGACY"), .NegatePresetClear("false"), .enable("true"), .NewFFLayout("false")) d_ff_1 (
    .clk(in_2), .D(1'b1), .Q(d_ff_1_q), .reset(\与中断屏蔽位与 ));  // open: Qn, preset, en
  or or_2 (or_2_out, d_ff_1_q, \与中断屏蔽位与 );
  and and_1 (and_1_out, or_2_out, ~\同步清零信号 );  // AND_Gate
  D_Flip_Flop #(.trigger("rising"), .Pre_Clr_Positions("LEGACY"), .NegatePresetClear("false"), .enable("true"), .NewFFLayout("false")) IR1 (
    .clk(in_1), .D(and_1_out), .Q(\与中断屏蔽位与 ));  // open: Qn, preset, en, reset

  // Notes on the sheet:
  //   中断信号采样参考电路
  //   Reset 
endmodule
